// Logisim project cpu24.circ as structural Verilog: 23 circuits, main circuit ◇单周期MIPS
module \单周期MIPS  (
);

  wire and_1_out, and_2_out, and_3_out, and_4_out, and_5_out, CLK, comparator_1_eq, comparator_2_eq, Go,
       mips_alu_2_equal, not_1_out, not_2_out, or_1_out, or_2_out, or_3_out, or_4_out, or_5_out, RST,
       SignedExt, \硬布线控制器_1_alu_src , \硬布线控制器_1_beq , \硬布线控制器_1_bltz , \硬布线控制器_1_bne , \硬布线控制器_1_jal ,
       \硬布线控制器_1_jmp , \硬布线控制器_1_jr , \硬布线控制器_1_lb , \硬布线控制器_1_memtoreg , \硬布线控制器_1_memwrite ,
       \硬布线控制器_1_regdst , \硬布线控制器_1_regwrite , \硬布线控制器_1_sllv , \硬布线控制器_1_syscall , \硬布线控制器_2_alu_src ,
       \硬布线控制器_2_beq , \硬布线控制器_2_bne , \硬布线控制器_2_jal , \硬布线控制器_2_jmp , \硬布线控制器_2_jr , \硬布线控制器_2_memtoreg ,
       \硬布线控制器_2_memwrite , \硬布线控制器_2_regdst , \硬布线控制器_2_regwrite , \硬布线控制器_2_syscall ;
  wire [3:0] \硬布线控制器_1_alu_op , \硬布线控制器_2_alu_op ;
  wire [4:0] mips_regifile_2_r1, multiplexer_4_out, multiplexer_6_out, multiplexer_8_out, multiplexer_9_out,
       multiplexer_13_out;
  wire [5:0] undriven, undriven_2;
  wire [7:0] multiplexer_15_out;
  wire [15:0] \总周期数 , \无条件分支数 , \条件分支成功数 ;
  wire [27:0] PC_2_q;
  wire [31:0] adder_1_out, adder_2_out, bit_extender_1_out, bit_extender_2_out, bit_extender_3_out, LedData,
       mips_alu_2_result, mips_regifile_2_r2, multiplexer_1_out, multiplexer_2_out, multiplexer_3_out,
       multiplexer_5_out, multiplexer_7_out, multiplexer_10_out, multiplexer_11_out, multiplexer_12_out,
       multiplexer_14_out, ram_2_data, shifter_1_out;
  wire [31:2] PC_2_q_2;
  wire [31:5] mips_regifile_2_r1_2;
  wire [31:26] rom_2_data;

  Button \u_总复位  (.out(RST));
  Button u_Go (.out(Go));
  Clock clock_1 (.out(CLK));
  Register #(.width(32)) PC ();  // open: D, en, Q, clk, clr
  Multiplexer #(.width(32), .enable("false")) multiplexer_1 (
    .in0(adder_1_out), .in1(adder_2_out), .out(multiplexer_1_out), .sel(or_5_out));
  Multiplexer #(.width(32), .enable("false")) multiplexer_2 (
    .in0(multiplexer_1_out), .in1({mips_regifile_2_r1_2, mips_regifile_2_r1}), .out(multiplexer_2_out),
    .sel(\硬布线控制器_1_jr ));
  Hex_Digit_Display hex_digit_display_1 (.value(LedData[27:24]));  // open: dp
  Hex_Digit_Display hex_digit_display_2 (.value(LedData[31:28]));  // open: dp
  or or_1 (or_1_out, or_3_out, not_1_out);
  or or_2 (or_2_out, \硬布线控制器_1_jmp , \硬布线控制器_1_jal );
  Multiplexer #(.width(32), .enable("false")) multiplexer_3 (
    .in0(multiplexer_2_out), .in1({PC_2_q_2, 2'b00}), .out(multiplexer_3_out), .sel(or_2_out));
  Hex_Digit_Display hex_digit_display_3 (.value(LedData[19:16]));  // open: dp
  Hex_Digit_Display hex_digit_display_4 (.value(LedData[23:20]));  // open: dp
  ROM #(.addrWidth(10), .dataWidth(32)) rom_1 ();  // open: addr, data, sel
  not not_1 (not_1_out, \硬布线控制器_1_syscall );
  or or_3 (or_3_out, and_1_out, Go);
  Counter #(.width(16), .max('hffff)) counter_1 (
    .count(or_1_out), .Q(\总周期数 ), .clk(CLK), .clr(RST));  // open: load, D, carry
  Register #(.width(32)) PC_2 (
    .D(multiplexer_3_out), .en(or_1_out), .Q({PC_2_q_2[31:28], PC_2_q}), .clk(CLK), .clr(RST));
  Hex_Digit_Display hex_digit_display_5 (.value(LedData[15:12]));  // open: dp
  Hex_Digit_Display hex_digit_display_6 (.value(LedData[11:8]));  // open: dp
  and and_1 (and_1_out, \硬布线控制器_1_syscall , comparator_1_eq);
  Comparator #(.width(32)) comparator_1 (
    .a(32'h22), .b({mips_regifile_2_r1_2, mips_regifile_2_r1}), .eq(comparator_1_eq));  // open: gt, lt
  Adder #(.width(32)) adder_1 (.a({PC_2_q_2[31:28], PC_2_q}), .b(32'h4), .out(adder_1_out));  // open: cin, cout
  Hex_Digit_Display hex_digit_display_7 (.value(LedData[3:0]));  // open: dp
  Hex_Digit_Display hex_digit_display_8 (.value(LedData[7:4]));  // open: dp
  MIPS_Regifile mips_regifile_1 ();  // open: Din, Clk, R1, R2, WE, W_num, R1_num, R2_num
  ROM #(.addrWidth(10), .dataWidth(32)) rom_2 (.addr(PC_2_q[11:2]), .data({rom_2_data, PC_2_q_2[27:2]}));  // open: sel
  Multiplexer #(.width(5), .enable("false")) multiplexer_4 (
    .in0(PC_2_q_2[22:18]), .in1(PC_2_q_2[17:13]), .out(multiplexer_4_out), .sel(\硬布线控制器_1_regdst ));
  Multiplexer #(.width(32), .enable("false")) multiplexer_5 (
    .in0(multiplexer_14_out), .in1(adder_1_out), .out(multiplexer_5_out), .sel(\硬布线控制器_1_jal ));
  MIPS_ALU mips_alu_1 ();  // open: X, Y, AluOP, Equal, Result, Result_2, shamt
  \硬布线控制器  \u_硬布线控制器_1  (
    .OP(rom_2_data), .Func(PC_2_q_2[7:2]), .ALU_OP(\硬布线控制器_1_alu_op ), .MemToReg(\硬布线控制器_1_memtoreg ),
    .MemWrite(\硬布线控制器_1_memwrite ), .ALU_SRC(\硬布线控制器_1_alu_src ), .RegWrite(\硬布线控制器_1_regwrite ),
    .SysCALL(\硬布线控制器_1_syscall ), .SignedExt(SignedExt), .RegDst(\硬布线控制器_1_regdst ), .Beq(\硬布线控制器_1_beq ),
    .Bne(\硬布线控制器_1_bne ), .JR(\硬布线控制器_1_jr ), .JMP(\硬布线控制器_1_jmp ), .JAL(\硬布线控制器_1_jal ),
    .SLLV(\硬布线控制器_1_sllv ), .LB(\硬布线控制器_1_lb ), .BLTZ(\硬布线控制器_1_bltz ));  // open: MFC0, MTC0, ERET, RS
  Multiplexer #(.width(5), .enable("false")) multiplexer_6 (
    .in0(multiplexer_4_out), .in1({5{1'b1}}), .out(multiplexer_6_out), .sel(\硬布线控制器_1_jal ));
  Multiplexer #(.width(32), .enable("false")) multiplexer_7 (
    .in0(multiplexer_5_out), .in1(bit_extender_3_out), .out(multiplexer_7_out), .sel(\硬布线控制器_1_lb ));
  assign bit_extender_1_out = {{16{1'b0}}, PC_2_q_2[17:2]};  // Bit_Extender bit_extender_1
  assign bit_extender_2_out = {{16{PC_2_q_2[17]}}, PC_2_q_2[17:2]};  // Bit_Extender bit_extender_2
  // Probe on \总周期数 
  // Probe on \无条件分支数 
  // Probe on \条件分支成功数 
  Counter #(.width(16), .max('hffff)) counter_2 (
    .count(or_4_out), .Q(\无条件分支数 ), .clk(CLK), .clr(RST));  // open: load, D, carry
  or or_4 (or_4_out, \硬布线控制器_1_jmp , \硬布线控制器_1_jr , \硬布线控制器_1_jal );
  Multiplexer #(.width(5), .enable("false")) multiplexer_8 (
    .in0(PC_2_q_2[27:23]), .in1(5'b00010), .out(multiplexer_8_out), .sel(\硬布线控制器_1_syscall ));
  and and_2 (and_2_out, \硬布线控制器_1_syscall , comparator_1_eq);
  Multiplexer #(.width(5), .enable("false")) multiplexer_9 (
    .in0(PC_2_q_2[22:18]), .in1(5'b00100), .out(multiplexer_9_out), .sel(and_2_out));
  Multiplexer #(.width(32), .enable("false")) multiplexer_10 (
    .in0(bit_extender_1_out), .in1(bit_extender_2_out), .out(multiplexer_10_out), .sel(SignedExt));
  RAM #(.addrWidth(10), .dataWidth(32), .bus("separate")) ram_1 ();  // open: addr, din, data, str, sel, clk, ld, clr
  MIPS_Regifile mips_regifile_2 (
    .Din(multiplexer_7_out), .Clk(CLK), .R1({mips_regifile_2_r1_2, mips_regifile_2_r1}),
    .R2(mips_regifile_2_r2), .WE(\硬布线控制器_1_regwrite ), .W_num(multiplexer_6_out), .R1_num(multiplexer_8_out),
    .R2_num(multiplexer_9_out));
  \硬布线控制器  \u_硬布线控制器_2  (
    .OP(undriven), .Func(undriven_2), .ALU_OP(\硬布线控制器_2_alu_op ), .MemToReg(\硬布线控制器_2_memtoreg ),
    .MemWrite(\硬布线控制器_2_memwrite ), .ALU_SRC(\硬布线控制器_2_alu_src ), .RegWrite(\硬布线控制器_2_regwrite ),
    .SysCALL(\硬布线控制器_2_syscall ), .RegDst(\硬布线控制器_2_regdst ), .Beq(\硬布线控制器_2_beq ), .Bne(\硬布线控制器_2_bne ),
    .JR(\硬布线控制器_2_jr ), .JMP(\硬布线控制器_2_jmp ), .JAL(\硬布线控制器_2_jal ));  // open: SignedExt, SLLV, LB, BLTZ, MFC0, MTC0, ERET, RS
  Multiplexer #(.width(32), .enable("false")) multiplexer_11 (
    .in0(mips_regifile_2_r2), .in1(multiplexer_10_out), .out(multiplexer_11_out), .sel(\硬布线控制器_1_alu_src ));
  Shifter #(.width(32)) shifter_1 (.in(bit_extender_2_out), .\dist (5'b00010), .out(shifter_1_out));
  Multiplexer #(.width(32), .enable("false")) multiplexer_12 (
    .in0(multiplexer_11_out), .in1({32{1'b0}}), .out(multiplexer_12_out), .sel(\硬布线控制器_1_bltz ));
  Multiplexer #(.width(5), .enable("false")) multiplexer_13 (
    .in0(PC_2_q_2[12:8]), .in1(mips_regifile_2_r1), .out(multiplexer_13_out), .sel(\硬布线控制器_1_sllv ));
  Adder #(.width(32)) adder_2 (.a(shifter_1_out), .b(adder_1_out), .out(adder_2_out));  // open: cin, cout
  MIPS_ALU mips_alu_2 (
    .X({mips_regifile_2_r1_2, mips_regifile_2_r1}), .Y(multiplexer_12_out), .AluOP(\硬布线控制器_1_alu_op ),
    .Equal(mips_alu_2_equal), .Result(mips_alu_2_result), .shamt(multiplexer_13_out));  // open: Result_2
  // Probe on mips_regifile_2_r2
  and and_3 (and_3_out, \硬布线控制器_1_beq , mips_alu_2_equal);
  and and_4 (and_4_out, \硬布线控制器_1_bne , not_2_out);
  not not_2 (not_2_out, mips_alu_2_equal);
  Comparator #(.width(32)) comparator_2 (.a(mips_alu_2_result), .b(32'h1), .eq(comparator_2_eq));  // open: gt, lt
  or or_5 (or_5_out, and_3_out, and_5_out, and_4_out);
  and and_5 (and_5_out, comparator_2_eq, \硬布线控制器_1_bltz );
  RAM #(.addrWidth(10), .dataWidth(32), .bus("separate")) ram_2 (
    .addr(mips_alu_2_result[11:2]), .din(mips_regifile_2_r2), .data(ram_2_data), .str(\硬布线控制器_1_memwrite ),
    .clk(CLK), .clr(RST));  // open: sel, ld
  Counter #(.width(16), .max('hffff)) counter_3 (
    .count(or_5_out), .Q(\条件分支成功数 ), .clk(CLK), .clr(RST));  // open: load, D, carry
  Multiplexer #(.width(32)) multiplexer_14 (
    .in0(mips_alu_2_result), .in1(ram_2_data), .out(multiplexer_14_out), .sel(\硬布线控制器_1_memtoreg ));  // open: en
  Register #(.width(32), .trigger("high")) register_1 (
    .D(mips_regifile_2_r2), .en(and_2_out), .Q(LedData), .clk(CLK), .clr(RST));
  // Probe on mips_regifile_2_r2
  Multiplexer #(.select(2), .width(8), .enable("false")) multiplexer_15 (
    .in0(multiplexer_14_out[7:0]), .in1(multiplexer_14_out[15:8]), .in2(multiplexer_14_out[23:16]),
    .in3(multiplexer_14_out[31:24]), .out(multiplexer_15_out), .sel(mips_alu_2_result[1:0]));
  assign bit_extender_3_out = {{24{multiplexer_15_out[7]}}, multiplexer_15_out};  // Bit_Extender bit_extender_3

  // Notes on the sheet:
  //   数码管输出应该用寄存器锁存，否则显示数据只能一闪而过
  //   指令存储器
  //   可以通过项目增加Logisim库的方式将前几次实验完成的电路作为子电路引入到本电路中使用
  //   OP
  //   Func
  //   rs
  //   指令字
  //   rt
  //   rd
  //   contents of rom_1 (hex, n*v repeats v):
  //   20110001 8000c05 20110001 20120002 20130003 8000c09 20110001 20120002 20130003 8000c0d 20110001
  //   20120002 20130003 8000c11 20110001 20120002 20130003 c000cf8 20100001 20110001 118fc0 112020
  //   20020022 c 118882 12200001 8000c15 112020 20020022 c 20110001 118880 112020 20020022 c 12200001
  //   8000c1f 20110001 118fc0 112020 20020022 c 1188c3 112020 20020022 c 118903 112020 20020022 c 118903
  //   112020 20020022 c 118903 112020 20020022 c 118903 112020 20020022 c 118903 112020 20020022 c 118903
  //   112020 20020022 c 118903 112020 20020022 c 20100001 109fc0 139fc3 8021 2012000c 24160003 26100001
  //   3210000f 20080008 20090001 139900 2709825 132020 20020022 c 1094022 1500fff9 22100001 2018000f
  //   2188024 108700 20080008 20090001 139902 2709825 132021 20020022 c 1094022 1500fff9 108702 2c9b022
  //   12c00001 8000c50 4020 1084027 84400 3508ffff 82021 20020022 c 2010ffff 20110000 ae300000 22100001
  //   22310004 ae300000 22100001 22310004 ae300000 22100001 22310004 ae300000 22100001 22310004 ae300000
  //   22100001 22310004 ae300000 22100001 22310004 ae300000 22100001 22310004 ae300000 22100001 22310004
  //   ae300000 22100001 22310004 ae300000 22100001 22310004 ae300000 22100001 22310004 ae300000 22100001
  //   22310004 ae300000 22100001 22310004 ae300000 22100001 22310004 ae300000 22100001 22310004 ae300000
  //   22100001 22310004 22100001 8020 2011003c 8e130000 8e340000 274402a 11000002 ae330000 ae140000
  //   2231fffc 1611fff8 102020 20020022 c 22100004 2011003c 1611fff2 20020032 c 20080001 20090003 20110876
  //   112020 20020022 c 200b0008 1118804 1318804 112020 20020022 c 216bffff 1560fff9 2002000a c 20080001
  //   20110010 112020 20020022 c 200b0020 2288823 112020 20020022 c 216bffff 1560fffa 2002000a c 20090000
  //   200b0010 34118483 20120404 118c00 129400 36318281 22520404 ad310000 2328820 21290004 216bffff
  //   1560fffb 200b0020 20090000 81310000 112020 20020022 c 21290001 216bffff 1560fff9 2002000a c 2011fff1
  //   112020 20020022 c 22310001 620fffb 2002000a c 2002000a c 20100000 22100001 102020 20020022 c
  //   22100002 102020 20020022 c 22100003 102020 20020022 c 22100004 102020 20020022 c 22100005 102020
  //   20020022 c 22100006 102020 20020022 c 22100007 102020 20020022 c 22100008 102020 20020022 20020022 c
  //   3e00008
  //   指令存储器
  //   数码管输出
  //   contents of rom_2 (hex, n*v repeats v):
  //   20110001 8000c05 20110001 20120002 20130003 8000c09 20110001 20120002 20130003 8000c0d 20110001
  //   20120002 20130003 8000c11 20110001 20120002 20130003 c000cb8 20100001 20110001 118fc0 112020
  //   20020022 c 118882 12200001 8000c15 112020 20020022 c 20110001 118880 112020 20020022 c 12200001
  //   8000c1f 20110001 118fc0 112020 20020022 c 1188c3 112020 20020022 c 118903 112020 20020022 c 118903
  //   112020 20020022 c 118903 112020 20020022 c 118903 112020 20020022 c 118903 112020 20020022 c 118903
  //   112020 20020022 c 118903 112020 20020022 c 20100001 109fc0 139fc3 8021 2012000c 24160003 26100001
  //   3210000f 20080008 20090001 139900 2709825 132020 20020022 c 1094022 1500fff9 22100001 2018000f
  //   2188024 108700 20080008 20090001 139902 2709825 132021 20020022 c 1094022 1500fff9 108702 2c9b022
  //   12c00001 8000c50 4020 1084027 84400 3508ffff 82021 20020022 c 2010ffff 20110000 ae300000 22100001
  //   22310004 ae300000 22100001 22310004 ae300000 22100001 22310004 ae300000 22100001 22310004 ae300000
  //   22100001 22310004 ae300000 22100001 22310004 ae300000 22100001 22310004 ae300000 22100001 22310004
  //   ae300000 22100001 22310004 ae300000 22100001 22310004 ae300000 22100001 22310004 ae300000 22100001
  //   22310004 ae300000 22100001 22310004 ae300000 22100001 22310004 ae300000 22100001 22310004 ae300000
  //   22100001 22310004 22100001 8020 2011003c 8e130000 8e340000 274402a 11000002 ae330000 ae140000
  //   2231fffc 1611fff8 102020 20020022 c 22100004 2011003c 1611fff2 2002000a c 20100000 22100001 102020
  //   20020022 c 22100002 102020 20020022 c 22100003 102020 20020022 c 22100004 102020 20020022 c 22100005
  //   102020 20020022 c 22100006 102020 20020022 c 22100007 102020 20020022 c 22100008 102020 20020022
  //   20020022 c 3e00008
  //   Op
  //   Func
  //   Beq
  //   Bne
  //   MemToReg
  //   MemWrite
  //   AluOP
  //   AluSrcB
  //   RegWrite
  //   RegDst
  //   总复位信号应将除ROM以外所有存储组件全部清零
  //   JMP
  //   JR
  //   OP
  //   Func
  //   Syscall
  //   Beq
  //   Bne
  //   MemToReg
  //   MemWrite
  //   AluOP
  //   AluSrcB
  //   RegWrite
  //   JAL
  //   RegDst
endmodule

// 单周期硬布线控制器
module \硬布线控制器  (
  input  [5:0] OP,
  input  [5:0] Func,
  input  [4:0] RS,
  output [3:0] ALU_OP,
  output MemToReg,
  output MemWrite,
  output ALU_SRC,
  output RegWrite,
  output SysCALL,
  output SignedExt,
  output RegDst,
  output Beq,
  output Bne,
  output JR,
  output JMP,
  output JAL,
  output SLLV,
  output LB,
  output BLTZ,
  output MFC0,
  output ERET,
  output MTC0
);

  wire not_1_out, not_2_out, not_3_out, not_4_out, not_5_out, not_6_out, not_7_out, not_8_out, not_9_out,
       not_10_out, not_11_out, not_12_out, not_13_out, not_14_out, not_15_out, not_16_out, not_17_out,
       not_18_out, not_19_out, not_20_out, not_21_out, not_22_out, not_23_out, not_24_out, not_25_out,
       not_26_out, not_27_out, not_28_out;

  \运算控制器  \u_运算控制器_1  (
    .OP0(OP[0]), .OP1(OP[1]), .OP2(OP[2]), .OP3(OP[3]), .OP4(OP[4]), .OP5(OP[5]), .F0(Func[0]), .F1(Func[1]),
    .F2(Func[2]), .F3(Func[3]), .F4(Func[4]), .F5(Func[5]), .S0(ALU_OP[0]), .S1(ALU_OP[1]), .S2(ALU_OP[2]),
    .S3(ALU_OP[3]));
  \控制信号生成  \u_控制信号生成_1  (
    .OP0(OP[0]), .OP1(OP[1]), .OP2(OP[2]), .OP3(OP[3]), .OP4(OP[4]), .OP5(OP[5]), .F0(Func[0]), .F1(Func[1]),
    .F2(Func[2]), .F3(Func[3]), .F4(Func[4]), .F5(Func[5]), .MemToReg(MemToReg), .MemWrite(MemWrite),
    .ALU_SRC(ALU_SRC), .RegWrite(RegWrite), .SysCALL(SysCALL), .SignedExt(SignedExt), .RegDst(RegDst),
    .BEQ(Beq), .BNE(Bne), .JR(JR), .JMP(JMP), .JAL(JAL), .SLLV(SLLV), .LB(LB), .BLTZ(BLTZ));
  not not_1 (not_1_out, OP[5]);
  not not_2 (not_2_out, OP[3]);
  not not_3 (not_3_out, OP[2]);
  not not_4 (not_4_out, OP[1]);
  not not_5 (not_5_out, OP[0]);
  not not_6 (not_6_out, RS[4]);
  not not_7 (not_7_out, RS[3]);
  not not_8 (not_8_out, RS[2]);
  not not_9 (not_9_out, RS[1]);
  not not_10 (not_10_out, RS[0]);
  not not_11 (not_11_out, OP[5]);
  not not_12 (not_12_out, OP[3]);
  not not_13 (not_13_out, OP[2]);
  not not_14 (not_14_out, OP[1]);
  not not_15 (not_15_out, OP[0]);
  not not_16 (not_16_out, RS[4]);
  not not_17 (not_17_out, RS[3]);
  not not_18 (not_18_out, RS[1]);
  not not_19 (not_19_out, RS[0]);
  and and_1 (MFC0, not_1_out, OP[4], not_2_out, not_3_out, not_4_out, not_5_out, not_6_out, not_7_out, not_8_out, not_9_out, not_10_out);
  and and_2 (MTC0, not_11_out, OP[4], not_12_out, not_13_out, not_14_out, not_15_out, not_16_out, not_17_out, RS[2], not_18_out, not_19_out);
  not not_20 (not_20_out, OP[5]);
  not not_21 (not_21_out, OP[3]);
  not not_22 (not_22_out, OP[2]);
  not not_23 (not_23_out, OP[1]);
  not not_24 (not_24_out, OP[1]);
  not not_25 (not_25_out, Func[5]);
  not not_26 (not_26_out, Func[2]);
  not not_27 (not_27_out, Func[1]);
  not not_28 (not_28_out, Func[0]);
  and and_3 (ERET, not_20_out, OP[4], not_21_out, not_22_out, not_23_out, not_24_out, not_25_out, Func[4], Func[3], not_26_out, not_27_out, not_28_out);

  // Other names for the same wires on the sheet: OP_CODE[5:0] = OP

  // Notes on the sheet:
  //   运算器控制器，根据指令生成运算器功能选择信号
  //   控制信号生成，产生数据通路需要的其他控制信号
endmodule

// 运算器控制器
module \运算控制器  (
  input  OP0,
  input  OP1,
  input  OP2,
  input  OP3,
  input  OP4,
  input  OP5,
  input  F0,
  input  F1,
  input  F2,
  input  F3,
  input  F4,
  input  F5,
  output S0,
  output S1,
  output S2,
  output S3
);

  wire and_1_out, and_2_out, and_3_out, and_4_out, and_5_out, and_6_out, and_7_out, and_8_out, and_9_out,
       and_10_out, and_11_out, and_12_out, and_13_out, and_14_out, and_15_out, and_16_out, and_17_out,
       and_18_out, and_19_out, and_20_out, and_21_out, and_22_out, and_23_out, and_24_out, and_25_out,
       and_26_out, and_27_out, and_28_out, and_29_out, and_30_out, and_31_out, and_32_out, and_33_out,
       and_34_out, and_35_out, and_36_out, and_37_out, and_38_out, and_39_out, and_40_out, and_41_out,
       not_1_out, not_2_out, not_3_out, not_4_out, not_5_out, not_6_out, not_7_out, not_8_out, not_9_out,
       not_10_out, not_11_out, not_12_out, not_13_out, not_14_out, not_15_out, not_16_out, not_17_out,
       not_18_out, not_19_out, not_20_out, not_21_out, not_22_out, not_23_out, not_24_out, not_25_out,
       not_26_out, not_27_out, not_28_out, not_29_out, not_30_out, not_31_out, not_32_out, not_33_out,
       not_34_out, not_35_out, not_36_out, not_37_out, not_38_out, not_39_out, not_40_out, not_41_out,
       not_42_out, not_43_out, not_44_out, not_45_out, not_46_out, not_47_out, not_48_out, not_49_out,
       not_50_out, not_51_out, not_52_out, not_53_out, not_54_out, not_55_out, not_56_out, not_57_out,
       not_58_out, not_59_out, not_60_out, not_61_out, not_62_out, not_63_out, not_64_out, not_65_out,
       not_66_out, not_67_out, not_68_out, not_69_out, not_70_out, not_71_out, not_72_out, not_73_out,
       not_74_out, not_75_out, not_76_out, not_77_out, not_78_out, not_79_out, not_80_out, not_81_out,
       not_82_out, not_83_out, not_84_out, not_85_out, not_86_out, not_87_out, not_88_out, not_89_out,
       not_90_out, not_91_out, not_92_out, not_93_out, not_94_out, not_95_out, not_96_out, not_97_out,
       not_98_out, not_99_out, not_100_out, not_101_out, not_102_out, not_103_out, not_104_out, not_105_out,
       not_106_out, not_107_out, not_108_out, not_109_out, not_110_out, not_111_out, not_112_out,
       not_113_out, not_114_out, not_115_out, not_116_out, not_117_out, not_118_out, not_119_out,
       not_120_out, not_121_out, not_122_out, not_123_out, not_124_out, not_125_out, not_126_out,
       not_127_out, not_128_out, not_129_out, not_130_out, not_131_out, not_132_out, not_133_out,
       not_134_out, not_135_out, not_136_out, not_137_out, not_138_out, not_139_out, not_140_out,
       not_141_out, not_142_out, not_143_out, not_144_out, not_145_out, not_146_out, not_147_out,
       not_148_out, not_149_out, not_150_out, not_151_out, not_152_out, not_153_out, not_154_out,
       not_155_out, not_156_out, not_157_out, not_158_out, not_159_out, not_160_out, not_161_out,
       not_162_out, not_163_out, not_164_out, not_165_out, not_166_out, not_167_out, not_168_out,
       not_169_out, not_170_out, not_171_out, not_172_out, not_173_out, not_174_out, not_175_out,
       not_176_out, not_177_out, not_178_out, not_179_out, not_180_out, not_181_out, not_182_out,
       not_183_out, not_184_out, not_185_out, not_186_out, not_187_out, not_188_out, not_189_out,
       not_190_out, not_191_out, not_192_out, not_193_out, not_194_out, not_195_out, not_196_out,
       not_197_out, not_198_out, not_199_out, not_200_out, not_201_out, not_202_out, not_203_out,
       not_204_out, not_205_out, not_206_out, not_207_out, not_208_out, not_209_out, not_210_out,
       not_211_out, not_212_out, not_213_out, not_214_out, not_215_out, not_216_out, not_217_out,
       not_218_out, not_219_out, not_220_out, not_221_out, not_222_out, not_223_out, not_224_out,
       not_225_out, not_226_out, not_227_out, not_228_out, not_229_out, not_230_out, not_231_out,
       not_232_out, not_233_out, not_234_out, not_235_out, not_236_out, not_237_out, not_238_out,
       not_239_out, not_240_out, not_241_out, not_242_out, not_243_out, not_244_out, not_245_out,
       not_246_out, not_247_out, not_248_out, not_249_out, not_250_out, not_251_out, not_252_out,
       not_253_out, not_254_out, not_255_out, not_256_out, not_257_out, not_258_out, not_259_out,
       not_260_out, not_261_out, not_262_out, not_263_out, not_264_out, not_265_out, not_266_out,
       not_267_out, not_268_out, not_269_out, not_270_out, not_271_out, not_272_out, not_273_out,
       not_274_out, not_275_out, not_276_out, not_277_out, not_278_out, not_279_out;

  not not_1 (not_1_out, OP5);
  not not_2 (not_2_out, OP4);
  not not_3 (not_3_out, OP3);
  not not_4 (not_4_out, OP2);
  not not_5 (not_5_out, OP1);
  not not_6 (not_6_out, OP0);
  not not_7 (not_7_out, F5);
  not not_8 (not_8_out, F4);
  not not_9 (not_9_out, F3);
  not not_10 (not_10_out, F2);
  not not_11 (not_11_out, OP5);
  not not_12 (not_12_out, OP4);
  not not_13 (not_13_out, OP3);
  not not_14 (not_14_out, OP2);
  not not_15 (not_15_out, OP1);
  not not_16 (not_16_out, OP0);
  not not_17 (not_17_out, F4);
  not not_18 (not_18_out, F3);
  not not_19 (not_19_out, F2);
  not not_20 (not_20_out, F1);
  not not_21 (not_21_out, F0);
  not not_22 (not_22_out, OP5);
  not not_23 (not_23_out, OP4);
  not not_24 (not_24_out, OP3);
  not not_25 (not_25_out, OP2);
  not not_26 (not_26_out, OP1);
  not not_27 (not_27_out, OP0);
  not not_28 (not_28_out, F4);
  not not_29 (not_29_out, F3);
  not not_30 (not_30_out, F2);
  not not_31 (not_31_out, F1);
  not not_32 (not_32_out, OP5);
  not not_33 (not_33_out, OP4);
  not not_34 (not_34_out, OP3);
  not not_35 (not_35_out, OP2);
  not not_36 (not_36_out, OP1);
  not not_37 (not_37_out, OP0);
  not not_38 (not_38_out, F4);
  not not_39 (not_39_out, F3);
  not not_40 (not_40_out, F1);
  not not_41 (not_41_out, F0);
  not not_42 (not_42_out, OP5);
  not not_43 (not_43_out, OP4);
  not not_44 (not_44_out, OP3);
  not not_45 (not_45_out, OP2);
  not not_46 (not_46_out, OP1);
  not not_47 (not_47_out, OP0);
  not not_48 (not_48_out, F4);
  not not_49 (not_49_out, F2);
  not not_50 (not_50_out, F0);
  not not_51 (not_51_out, OP5);
  not not_52 (not_52_out, OP4);
  not not_53 (not_53_out, OP2);
  not not_54 (not_54_out, OP1);
  not not_55 (not_55_out, OP0);
  not not_56 (not_56_out, OP5);
  not not_57 (not_57_out, OP4);
  not not_58 (not_58_out, OP1);
  not not_59 (not_59_out, OP0);
  not not_60 (not_60_out, OP5);
  not not_61 (not_61_out, OP4);
  not not_62 (not_62_out, OP2);
  not not_63 (not_63_out, OP1);
  not not_64 (not_64_out, OP5);
  not not_65 (not_65_out, OP4);
  not not_66 (not_66_out, OP2);
  not not_67 (not_67_out, OP0);
  not not_68 (not_68_out, OP4);
  not not_69 (not_69_out, OP3);
  not not_70 (not_70_out, OP2);
  not not_71 (not_71_out, OP4);
  not not_72 (not_72_out, OP2);
  not not_73 (not_73_out, OP4);
  not not_74 (not_74_out, OP3);
  not not_75 (not_75_out, OP2);
  not not_76 (not_76_out, OP1);
  not not_77 (not_77_out, OP0);
  not not_78 (not_78_out, OP5);
  not not_79 (not_79_out, OP4);
  not not_80 (not_80_out, OP3);
  not not_81 (not_81_out, OP2);
  not not_82 (not_82_out, OP1);
  not not_83 (not_83_out, OP5);
  not not_84 (not_84_out, OP4);
  not not_85 (not_85_out, OP3);
  not not_86 (not_86_out, OP2);
  not not_87 (not_87_out, OP1);
  not not_88 (not_88_out, OP0);
  not not_89 (not_89_out, F5);
  not not_90 (not_90_out, F4);
  not not_91 (not_91_out, F3);
  not not_92 (not_92_out, F2);
  not not_93 (not_93_out, F0);
  not not_94 (not_94_out, OP5);
  not not_95 (not_95_out, OP4);
  not not_96 (not_96_out, OP3);
  not not_97 (not_97_out, OP2);
  not not_98 (not_98_out, OP1);
  not not_99 (not_99_out, OP0);
  not not_100 (not_100_out, F4);
  not not_101 (not_101_out, F3);
  not not_102 (not_102_out, F2);
  not not_103 (not_103_out, F0);
  not not_104 (not_104_out, OP5);
  not not_105 (not_105_out, OP4);
  not not_106 (not_106_out, OP3);
  not not_107 (not_107_out, OP2);
  not not_108 (not_108_out, OP1);
  not not_109 (not_109_out, OP0);
  not not_110 (not_110_out, F4);
  not not_111 (not_111_out, F3);
  not not_112 (not_112_out, F1);
  not not_113 (not_113_out, F0);
  not not_114 (not_114_out, OP5);
  not not_115 (not_115_out, OP4);
  not not_116 (not_116_out, OP3);
  not not_117 (not_117_out, OP2);
  not not_118 (not_118_out, OP1);
  not not_119 (not_119_out, OP0);
  not not_120 (not_120_out, F4);
  not not_121 (not_121_out, F3);
  not not_122 (not_122_out, OP5);
  not not_123 (not_123_out, OP4);
  not not_124 (not_124_out, OP3);
  not not_125 (not_125_out, OP2);
  not not_126 (not_126_out, OP1);
  not not_127 (not_127_out, OP0);
  not not_128 (not_128_out, F4);
  not not_129 (not_129_out, F2);
  not not_130 (not_130_out, F0);
  not not_131 (not_131_out, OP5);
  not not_132 (not_132_out, OP4);
  not not_133 (not_133_out, OP1);
  not not_134 (not_134_out, OP0);
  not not_135 (not_135_out, OP5);
  not not_136 (not_136_out, OP4);
  not not_137 (not_137_out, OP2);
  not not_138 (not_138_out, OP0);
  not not_139 (not_139_out, OP5);
  not not_140 (not_140_out, OP4);
  not not_141 (not_141_out, OP3);
  not not_142 (not_142_out, OP2);
  not not_143 (not_143_out, OP1);
  not not_144 (not_144_out, OP0);
  not not_145 (not_145_out, F4);
  not not_146 (not_146_out, F3);
  not not_147 (not_147_out, F2);
  not not_148 (not_148_out, OP5);
  not not_149 (not_149_out, OP4);
  not not_150 (not_150_out, OP3);
  not not_151 (not_151_out, OP2);
  not not_152 (not_152_out, OP1);
  not not_153 (not_153_out, OP5);
  not not_154 (not_154_out, OP4);
  not not_155 (not_155_out, OP3);
  not not_156 (not_156_out, OP2);
  not not_157 (not_157_out, OP1);
  not not_158 (not_158_out, OP0);
  not not_159 (not_159_out, F4);
  not not_160 (not_160_out, F3);
  not not_161 (not_161_out, F2);
  not not_162 (not_162_out, F1);
  not not_163 (not_163_out, F0);
  not not_164 (not_164_out, OP5);
  not not_165 (not_165_out, OP4);
  not not_166 (not_166_out, OP3);
  not not_167 (not_167_out, OP2);
  not not_168 (not_168_out, OP1);
  not not_169 (not_169_out, OP0);
  not not_170 (not_170_out, F4);
  not not_171 (not_171_out, F3);
  not not_172 (not_172_out, F2);
  not not_173 (not_173_out, F1);
  not not_174 (not_174_out, OP5);
  not not_175 (not_175_out, OP4);
  not not_176 (not_176_out, OP3);
  not not_177 (not_177_out, OP2);
  not not_178 (not_178_out, OP1);
  not not_179 (not_179_out, OP0);
  not not_180 (not_180_out, F4);
  not not_181 (not_181_out, F3);
  not not_182 (not_182_out, F2);
  not not_183 (not_183_out, F0);
  not not_184 (not_184_out, OP5);
  not not_185 (not_185_out, OP4);
  not not_186 (not_186_out, OP3);
  not not_187 (not_187_out, OP2);
  not not_188 (not_188_out, OP1);
  not not_189 (not_189_out, OP0);
  not not_190 (not_190_out, F4);
  not not_191 (not_191_out, F3);
  not not_192 (not_192_out, F1);
  not not_193 (not_193_out, F0);
  not not_194 (not_194_out, OP5);
  not not_195 (not_195_out, OP4);
  not not_196 (not_196_out, OP3);
  not not_197 (not_197_out, OP2);
  not not_198 (not_198_out, OP1);
  not not_199 (not_199_out, OP0);
  not not_200 (not_200_out, F4);
  not not_201 (not_201_out, F2);
  not not_202 (not_202_out, OP5);
  not not_203 (not_203_out, OP4);
  not not_204 (not_204_out, OP2);
  not not_205 (not_205_out, OP1);
  not not_206 (not_206_out, OP0);
  not not_207 (not_207_out, OP5);
  not not_208 (not_208_out, OP4);
  not not_209 (not_209_out, OP1);
  not not_210 (not_210_out, OP0);
  not not_211 (not_211_out, OP5);
  not not_212 (not_212_out, OP4);
  not not_213 (not_213_out, OP2);
  not not_214 (not_214_out, OP1);
  not not_215 (not_215_out, OP4);
  not not_216 (not_216_out, OP3);
  not not_217 (not_217_out, OP2);
  not not_218 (not_218_out, OP4);
  not not_219 (not_219_out, OP2);
  not not_220 (not_220_out, OP5);
  not not_221 (not_221_out, OP4);
  not not_222 (not_222_out, OP3);
  not not_223 (not_223_out, OP2);
  not not_224 (not_224_out, OP1);
  not not_225 (not_225_out, OP0);
  not not_226 (not_226_out, F4);
  not not_227 (not_227_out, F3);
  not not_228 (not_228_out, F2);
  not not_229 (not_229_out, OP4);
  not not_230 (not_230_out, OP3);
  not not_231 (not_231_out, OP2);
  not not_232 (not_232_out, OP1);
  not not_233 (not_233_out, OP0);
  not not_234 (not_234_out, OP5);
  not not_235 (not_235_out, OP4);
  not not_236 (not_236_out, OP3);
  not not_237 (not_237_out, OP2);
  not not_238 (not_238_out, OP1);
  not not_239 (not_239_out, OP0);
  not not_240 (not_240_out, F4);
  not not_241 (not_241_out, F3);
  not not_242 (not_242_out, F1);
  not not_243 (not_243_out, OP5);
  not not_244 (not_244_out, OP4);
  not not_245 (not_245_out, OP3);
  not not_246 (not_246_out, OP2);
  not not_247 (not_247_out, OP1);
  not not_248 (not_248_out, OP0);
  not not_249 (not_249_out, F4);
  not not_250 (not_250_out, F3);
  not not_251 (not_251_out, OP5);
  not not_252 (not_252_out, OP4);
  not not_253 (not_253_out, OP3);
  not not_254 (not_254_out, OP2);
  not not_255 (not_255_out, OP1);
  not not_256 (not_256_out, OP0);
  not not_257 (not_257_out, F4);
  not not_258 (not_258_out, F2);
  not not_259 (not_259_out, F0);
  not not_260 (not_260_out, OP5);
  not not_261 (not_261_out, OP4);
  not not_262 (not_262_out, OP3);
  not not_263 (not_263_out, OP2);
  not not_264 (not_264_out, OP1);
  not not_265 (not_265_out, OP0);
  not not_266 (not_266_out, F4);
  not not_267 (not_267_out, F2);
  not not_268 (not_268_out, OP5);
  not not_269 (not_269_out, OP4);
  not not_270 (not_270_out, OP2);
  not not_271 (not_271_out, OP0);
  not not_272 (not_272_out, OP5);
  not not_273 (not_273_out, OP4);
  not not_274 (not_274_out, OP1);
  not not_275 (not_275_out, OP5);
  not not_276 (not_276_out, OP4);
  not not_277 (not_277_out, OP3);
  not not_278 (not_278_out, OP2);
  not not_279 (not_279_out, OP1);
  and and_1 (and_1_out, not_1_out, not_2_out, not_3_out, not_4_out, not_5_out, not_6_out, not_7_out, not_8_out, not_9_out, not_10_out, F1, F0);
  and and_2 (and_2_out, not_11_out, not_12_out, not_13_out, not_14_out, not_15_out, not_16_out, F5, not_17_out, not_18_out, not_19_out, not_20_out, not_21_out);
  and and_3 (and_3_out, not_22_out, not_23_out, not_24_out, not_25_out, not_26_out, not_27_out, F5, not_28_out, not_29_out, not_30_out, not_31_out, F0);
  and and_4 (and_4_out, not_32_out, not_33_out, not_34_out, not_35_out, not_36_out, not_37_out, F5, not_38_out, not_39_out, F2, not_40_out, not_41_out);
  and and_5 (and_5_out, not_42_out, not_43_out, not_44_out, not_45_out, not_46_out, not_47_out, F5, not_48_out, F3, not_49_out, F1, not_50_out);
  and and_6 (and_6_out, not_51_out, not_52_out, OP3, not_53_out, not_54_out, not_55_out);
  and and_7 (and_7_out, not_56_out, not_57_out, OP3, OP2, not_58_out, not_59_out);
  and and_8 (and_8_out, not_60_out, not_61_out, OP3, not_62_out, not_63_out, OP0);
  and and_9 (and_9_out, not_64_out, not_65_out, OP3, not_66_out, OP1, not_67_out);
  and and_10 (and_10_out, OP5, not_68_out, not_69_out, not_70_out, OP1, OP0);
  and and_11 (and_11_out, OP5, not_71_out, OP3, not_72_out, OP1, OP0);
  and and_12 (and_12_out, OP5, not_73_out, not_74_out, not_75_out, not_76_out, not_77_out);
  and and_13 (and_13_out, not_78_out, not_79_out, not_80_out, not_81_out, not_82_out, OP0);
  and and_14 (and_14_out, not_83_out, not_84_out, not_85_out, not_86_out, not_87_out, not_88_out, not_89_out, not_90_out, not_91_out, not_92_out, F1, not_93_out);
  and and_15 (and_15_out, not_94_out, not_95_out, not_96_out, not_97_out, not_98_out, not_99_out, F5, not_100_out, not_101_out, not_102_out, F1, not_103_out);
  and and_16 (and_16_out, not_104_out, not_105_out, not_106_out, not_107_out, not_108_out, not_109_out, F5, not_110_out, not_111_out, F2, not_112_out, not_113_out);
  and and_17 (and_17_out, not_114_out, not_115_out, not_116_out, not_117_out, not_118_out, not_119_out, F5, not_120_out, not_121_out, F2, F1, F0);
  and and_18 (and_18_out, not_122_out, not_123_out, not_124_out, not_125_out, not_126_out, not_127_out, F5, not_128_out, F3, not_129_out, F1, not_130_out);
  and and_19 (and_19_out, not_131_out, not_132_out, OP3, OP2, not_133_out, not_134_out);
  and and_20 (and_20_out, not_135_out, not_136_out, OP3, not_137_out, OP1, not_138_out);
  and and_21 (and_21_out, not_139_out, not_140_out, not_141_out, not_142_out, not_143_out, not_144_out, F5, not_145_out, not_146_out, not_147_out, F1, F0);
  and and_22 (and_22_out, not_148_out, not_149_out, not_150_out, not_151_out, not_152_out, OP0);
  and and_23 (and_23_out, not_153_out, not_154_out, not_155_out, not_156_out, not_157_out, not_158_out, F5, not_159_out, not_160_out, not_161_out, not_162_out, not_163_out);
  and and_24 (and_24_out, not_164_out, not_165_out, not_166_out, not_167_out, not_168_out, not_169_out, F5, not_170_out, not_171_out, not_172_out, not_173_out, F0);
  and and_25 (and_25_out, not_174_out, not_175_out, not_176_out, not_177_out, not_178_out, not_179_out, F5, not_180_out, not_181_out, not_182_out, F1, not_183_out);
  and and_26 (and_26_out, not_184_out, not_185_out, not_186_out, not_187_out, not_188_out, not_189_out, F5, not_190_out, not_191_out, F2, not_192_out, not_193_out);
  and and_27 (and_27_out, not_194_out, not_195_out, not_196_out, not_197_out, not_198_out, not_199_out, F5, not_200_out, F3, not_201_out, F1, F0);
  and and_28 (and_28_out, not_202_out, not_203_out, OP3, not_204_out, not_205_out, not_206_out);
  and and_29 (and_29_out, not_207_out, not_208_out, OP3, OP2, not_209_out, not_210_out);
  and and_30 (and_30_out, not_211_out, not_212_out, OP3, not_213_out, not_214_out, OP0);
  and and_31 (and_31_out, OP5, not_215_out, not_216_out, not_217_out, OP1, OP0);
  and and_32 (and_32_out, OP5, not_218_out, OP3, not_219_out, OP1, OP0);
  and and_33 (and_33_out, not_220_out, not_221_out, not_222_out, not_223_out, not_224_out, not_225_out, F5, not_226_out, not_227_out, not_228_out, F1, F0);
  and and_34 (and_34_out, OP5, not_229_out, not_230_out, not_231_out, not_232_out, not_233_out);
  and and_35 (and_35_out, not_234_out, not_235_out, not_236_out, not_237_out, not_238_out, not_239_out, F5, not_240_out, not_241_out, F2, not_242_out, F0);
  and and_36 (and_36_out, not_243_out, not_244_out, not_245_out, not_246_out, not_247_out, not_248_out, F5, not_249_out, not_250_out, F2, F1, F0);
  and and_37 (and_37_out, not_251_out, not_252_out, not_253_out, not_254_out, not_255_out, not_256_out, F5, not_257_out, F3, not_258_out, F1, not_259_out);
  and and_38 (and_38_out, not_260_out, not_261_out, not_262_out, not_263_out, not_264_out, not_265_out, F5, not_266_out, F3, not_267_out, F1, F0);
  and and_39 (and_39_out, not_268_out, not_269_out, OP3, not_270_out, OP1, not_271_out);
  and and_40 (and_40_out, not_272_out, not_273_out, OP3, OP2, not_274_out, OP0);
  and and_41 (and_41_out, not_275_out, not_276_out, not_277_out, not_278_out, not_279_out, OP0);
  or or_1 (S1, and_14_out, and_15_out, and_16_out, and_17_out, and_18_out, and_19_out, and_20_out, and_21_out, and_22_out);
  or or_2 (S3, and_35_out, and_36_out, and_37_out, and_38_out, and_39_out, and_40_out, and_41_out);
  or or_3 (S0, and_1_out, and_2_out, and_3_out, and_4_out, and_5_out, and_6_out, and_7_out, and_8_out, and_9_out, and_10_out, and_11_out, and_12_out, and_13_out);
  or or_4 (S2, and_23_out, and_24_out, and_25_out, and_26_out, and_27_out, and_28_out, and_29_out, and_30_out, and_31_out, and_32_out, and_33_out, and_34_out);
endmodule

// 控制信号生成
module \控制信号生成  (
  input  OP0,
  input  OP1,
  input  OP2,
  input  OP3,
  input  OP4,
  input  OP5,
  input  F0,
  input  F1,
  input  F2,
  input  F3,
  input  F4,
  input  F5,
  output MemToReg,
  output MemWrite,
  output ALU_SRC,
  output RegWrite,
  output SysCALL,
  output SignedExt,
  output RegDst,
  output BEQ,
  output BNE,
  output JR,
  output JMP,
  output JAL,
  output SLLV,
  output LB,
  output BLTZ
);

  wire and_1_out, and_2_out, and_4_out, and_5_out, and_6_out, and_7_out, and_8_out, and_9_out, and_10_out,
       and_11_out, and_12_out, and_13_out, and_14_out, and_15_out, and_16_out, and_17_out, and_18_out,
       and_19_out, and_20_out, and_21_out, and_22_out, and_23_out, and_24_out, and_25_out, and_26_out,
       and_27_out, and_28_out, and_29_out, and_30_out, and_31_out, and_32_out, and_33_out, and_35_out,
       and_36_out, and_37_out, and_38_out, and_39_out, and_40_out, and_41_out, and_42_out, and_43_out,
       and_44_out, and_45_out, and_46_out, and_47_out, and_48_out, and_57_out, not_1_out, not_2_out,
       not_3_out, not_4_out, not_5_out, not_6_out, not_7_out, not_8_out, not_9_out, not_10_out, not_11_out,
       not_12_out, not_13_out, not_14_out, not_15_out, not_16_out, not_17_out, not_18_out, not_19_out,
       not_20_out, not_21_out, not_22_out, not_23_out, not_24_out, not_25_out, not_26_out, not_27_out,
       not_28_out, not_29_out, not_30_out, not_31_out, not_32_out, not_33_out, not_34_out, not_35_out,
       not_36_out, not_37_out, not_38_out, not_39_out, not_40_out, not_41_out, not_42_out, not_43_out,
       not_44_out, not_45_out, not_46_out, not_47_out, not_48_out, not_49_out, not_50_out, not_51_out,
       not_52_out, not_53_out, not_54_out, not_55_out, not_56_out, not_57_out, not_58_out, not_59_out,
       not_60_out, not_61_out, not_62_out, not_63_out, not_64_out, not_65_out, not_66_out, not_67_out,
       not_68_out, not_69_out, not_70_out, not_71_out, not_72_out, not_73_out, not_74_out, not_75_out,
       not_76_out, not_77_out, not_78_out, not_79_out, not_80_out, not_81_out, not_82_out, not_83_out,
       not_84_out, not_85_out, not_86_out, not_87_out, not_88_out, not_89_out, not_90_out, not_91_out,
       not_92_out, not_93_out, not_94_out, not_95_out, not_96_out, not_97_out, not_98_out, not_99_out,
       not_100_out, not_101_out, not_102_out, not_103_out, not_104_out, not_105_out, not_106_out,
       not_107_out, not_108_out, not_109_out, not_110_out, not_111_out, not_112_out, not_113_out,
       not_114_out, not_115_out, not_116_out, not_117_out, not_118_out, not_119_out, not_120_out,
       not_121_out, not_122_out, not_123_out, not_124_out, not_125_out, not_126_out, not_127_out,
       not_128_out, not_129_out, not_130_out, not_131_out, not_132_out, not_133_out, not_134_out,
       not_135_out, not_136_out, not_137_out, not_138_out, not_139_out, not_140_out, not_141_out,
       not_142_out, not_143_out, not_144_out, not_145_out, not_146_out, not_147_out, not_148_out,
       not_149_out, not_150_out, not_151_out, not_152_out, not_153_out, not_154_out, not_155_out,
       not_156_out, not_157_out, not_158_out, not_159_out, not_160_out, not_161_out, not_162_out,
       not_163_out, not_164_out, not_165_out, not_166_out, not_167_out, not_168_out, not_169_out,
       not_170_out, not_171_out, not_172_out, not_173_out, not_174_out, not_175_out, not_176_out,
       not_177_out, not_178_out, not_179_out, not_180_out, not_181_out, not_182_out, not_183_out,
       not_184_out, not_185_out, not_186_out, not_187_out, not_188_out, not_189_out, not_190_out,
       not_191_out, not_192_out, not_193_out, not_194_out, not_195_out, not_196_out, not_197_out,
       not_198_out, not_199_out, not_200_out, not_201_out, not_202_out, not_203_out, not_204_out,
       not_205_out, not_206_out, not_207_out, not_208_out, not_209_out, not_210_out, not_211_out,
       not_212_out, not_213_out, not_214_out, not_215_out, not_216_out, not_217_out, not_218_out,
       not_219_out, not_220_out, not_221_out, not_222_out, not_223_out, not_224_out, not_225_out,
       not_226_out, not_227_out, not_228_out, not_229_out, not_230_out, not_231_out, not_232_out,
       not_233_out, not_234_out, not_235_out, not_236_out, not_237_out, not_238_out, not_239_out,
       not_240_out, not_241_out, not_242_out, not_243_out, not_244_out, not_245_out, not_246_out,
       not_247_out, not_248_out, not_249_out, not_250_out, not_251_out, not_252_out, not_253_out,
       not_254_out, not_255_out, not_256_out, not_257_out, not_258_out, not_259_out, not_260_out,
       not_261_out, not_262_out, not_263_out, not_264_out, not_265_out, not_266_out, not_267_out,
       not_268_out, not_269_out, not_270_out, not_271_out, not_272_out, not_273_out, not_274_out,
       not_275_out, not_276_out, not_277_out, not_278_out, not_279_out, not_280_out, not_281_out,
       not_282_out, not_283_out, not_284_out, not_285_out, not_286_out, not_287_out, not_288_out,
       not_289_out, not_290_out, not_291_out, not_292_out, not_293_out, not_294_out, not_295_out,
       not_296_out, not_297_out, not_298_out, not_299_out, not_300_out, not_301_out, not_302_out,
       not_303_out, not_304_out, not_305_out, not_306_out, not_307_out, not_308_out, not_309_out,
       not_310_out, not_311_out, not_312_out, not_313_out, not_314_out, not_315_out, not_316_out,
       not_317_out, not_318_out, not_319_out, not_320_out, not_321_out, not_322_out, not_323_out,
       not_324_out, not_325_out, not_326_out, not_327_out, not_328_out, not_329_out, not_330_out,
       not_331_out, not_332_out, not_333_out, not_334_out, not_335_out, not_336_out, not_337_out,
       not_338_out, not_339_out, not_340_out, not_341_out, not_342_out, not_343_out, not_344_out,
       not_345_out, not_346_out, not_347_out, not_348_out, not_349_out, not_350_out, not_351_out,
       not_352_out, not_353_out, not_354_out, not_355_out, not_356_out, not_357_out, not_358_out,
       not_359_out, not_360_out, not_361_out, not_362_out, not_363_out, not_364_out, not_365_out,
       not_366_out, not_367_out, not_368_out, not_369_out, not_370_out, not_371_out, not_372_out,
       not_373_out, not_374_out, not_375_out, not_376_out, not_377_out, not_378_out, not_379_out,
       not_380_out, not_381_out, not_382_out, not_383_out, not_384_out, not_385_out, not_386_out,
       not_387_out, not_388_out, not_389_out, not_390_out, not_391_out, not_392_out, not_393_out,
       not_394_out, not_395_out, not_396_out, not_397_out, not_398_out, not_399_out, not_400_out,
       not_401_out, not_402_out, not_403_out, not_404_out, not_405_out, not_406_out, not_407_out,
       not_408_out, not_409_out, not_410_out, not_411_out;

  not not_1 (not_1_out, OP4);
  not not_2 (not_2_out, OP3);
  not not_3 (not_3_out, OP2);
  not not_4 (not_4_out, OP4);
  not not_5 (not_5_out, OP3);
  not not_6 (not_6_out, OP2);
  not not_7 (not_7_out, OP1);
  not not_8 (not_8_out, OP0);
  not not_9 (not_9_out, OP4);
  not not_10 (not_10_out, OP2);
  not not_11 (not_11_out, OP5);
  not not_12 (not_12_out, OP4);
  not not_13 (not_13_out, OP2);
  not not_14 (not_14_out, OP1);
  not not_15 (not_15_out, OP0);
  not not_16 (not_16_out, OP5);
  not not_17 (not_17_out, OP4);
  not not_18 (not_18_out, OP1);
  not not_19 (not_19_out, OP0);
  not not_20 (not_20_out, OP5);
  not not_21 (not_21_out, OP4);
  not not_22 (not_22_out, OP2);
  not not_23 (not_23_out, OP1);
  not not_24 (not_24_out, OP5);
  not not_25 (not_25_out, OP4);
  not not_26 (not_26_out, OP2);
  not not_27 (not_27_out, OP0);
  not not_28 (not_28_out, OP5);
  not not_29 (not_29_out, OP4);
  not not_30 (not_30_out, OP1);
  not not_31 (not_31_out, OP4);
  not not_32 (not_32_out, OP3);
  not not_33 (not_33_out, OP2);
  not not_34 (not_34_out, OP4);
  not not_35 (not_35_out, OP2);
  not not_36 (not_36_out, OP4);
  not not_37 (not_37_out, OP3);
  not not_38 (not_38_out, OP2);
  not not_39 (not_39_out, OP1);
  not not_40 (not_40_out, OP0);
  not not_41 (not_41_out, OP5);
  not not_42 (not_42_out, OP4);
  not not_43 (not_43_out, OP3);
  not not_44 (not_44_out, OP2);
  not not_45 (not_45_out, OP1);
  not not_46 (not_46_out, OP0);
  not not_47 (not_47_out, F5);
  not not_48 (not_48_out, F4);
  not not_49 (not_49_out, F3);
  not not_50 (not_50_out, F2);
  not not_51 (not_51_out, F1);
  not not_52 (not_52_out, F0);
  not not_53 (not_53_out, OP5);
  not not_54 (not_54_out, OP4);
  not not_55 (not_55_out, OP3);
  not not_56 (not_56_out, OP2);
  not not_57 (not_57_out, OP1);
  not not_58 (not_58_out, OP0);
  not not_59 (not_59_out, F5);
  not not_60 (not_60_out, F4);
  not not_61 (not_61_out, F3);
  not not_62 (not_62_out, F2);
  not not_63 (not_63_out, OP5);
  not not_64 (not_64_out, OP4);
  not not_65 (not_65_out, OP3);
  not not_66 (not_66_out, OP2);
  not not_67 (not_67_out, OP1);
  not not_68 (not_68_out, OP0);
  not not_69 (not_69_out, F5);
  not not_70 (not_70_out, F4);
  not not_71 (not_71_out, F3);
  not not_72 (not_72_out, F2);
  not not_73 (not_73_out, F0);
  not not_74 (not_74_out, OP5);
  not not_75 (not_75_out, OP4);
  not not_76 (not_76_out, OP3);
  not not_77 (not_77_out, OP2);
  not not_78 (not_78_out, OP1);
  not not_79 (not_79_out, OP0);
  not not_80 (not_80_out, F4);
  not not_81 (not_81_out, F3);
  not not_82 (not_82_out, F2);
  not not_83 (not_83_out, F1);
  not not_84 (not_84_out, F0);
  not not_85 (not_85_out, OP5);
  not not_86 (not_86_out, OP4);
  not not_87 (not_87_out, OP3);
  not not_88 (not_88_out, OP2);
  not not_89 (not_89_out, OP1);
  not not_90 (not_90_out, OP0);
  not not_91 (not_91_out, F4);
  not not_92 (not_92_out, F3);
  not not_93 (not_93_out, F2);
  not not_94 (not_94_out, F1);
  not not_95 (not_95_out, OP5);
  not not_96 (not_96_out, OP4);
  not not_97 (not_97_out, OP3);
  not not_98 (not_98_out, OP2);
  not not_99 (not_99_out, OP1);
  not not_100 (not_100_out, OP0);
  not not_101 (not_101_out, F4);
  not not_102 (not_102_out, F3);
  not not_103 (not_103_out, F2);
  not not_104 (not_104_out, F0);
  not not_105 (not_105_out, OP5);
  not not_106 (not_106_out, OP4);
  not not_107 (not_107_out, OP3);
  not not_108 (not_108_out, OP2);
  not not_109 (not_109_out, OP1);
  not not_110 (not_110_out, OP0);
  not not_111 (not_111_out, F4);
  not not_112 (not_112_out, F3);
  not not_113 (not_113_out, F1);
  not not_114 (not_114_out, F0);
  not not_115 (not_115_out, OP5);
  not not_116 (not_116_out, OP4);
  not not_117 (not_117_out, OP3);
  not not_118 (not_118_out, OP2);
  not not_119 (not_119_out, OP1);
  not not_120 (not_120_out, OP0);
  not not_121 (not_121_out, F4);
  not not_122 (not_122_out, F3);
  not not_123 (not_123_out, F1);
  not not_124 (not_124_out, OP5);
  not not_125 (not_125_out, OP4);
  not not_126 (not_126_out, OP3);
  not not_127 (not_127_out, OP2);
  not not_128 (not_128_out, OP1);
  not not_129 (not_129_out, OP0);
  not not_130 (not_130_out, F4);
  not not_131 (not_131_out, F3);
  not not_132 (not_132_out, OP5);
  not not_133 (not_133_out, OP4);
  not not_134 (not_134_out, OP3);
  not not_135 (not_135_out, OP2);
  not not_136 (not_136_out, OP1);
  not not_137 (not_137_out, OP0);
  not not_138 (not_138_out, F4);
  not not_139 (not_139_out, F2);
  not not_140 (not_140_out, F0);
  not not_141 (not_141_out, OP5);
  not not_142 (not_142_out, OP4);
  not not_143 (not_143_out, OP3);
  not not_144 (not_144_out, OP2);
  not not_145 (not_145_out, OP1);
  not not_146 (not_146_out, OP0);
  not not_147 (not_147_out, F4);
  not not_148 (not_148_out, F2);
  not not_149 (not_149_out, OP5);
  not not_150 (not_150_out, OP4);
  not not_151 (not_151_out, OP3);
  not not_152 (not_152_out, OP2);
  not not_153 (not_153_out, OP1);
  not not_154 (not_154_out, OP0);
  not not_155 (not_155_out, F5);
  not not_156 (not_156_out, F4);
  not not_157 (not_157_out, F2);
  not not_158 (not_158_out, F1);
  not not_159 (not_159_out, F0);
  not not_160 (not_160_out, OP5);
  not not_161 (not_161_out, OP4);
  not not_162 (not_162_out, OP3);
  not not_163 (not_163_out, OP2);
  not not_164 (not_164_out, OP5);
  not not_165 (not_165_out, OP4);
  not not_166 (not_166_out, OP2);
  not not_167 (not_167_out, OP1);
  not not_168 (not_168_out, OP0);
  not not_169 (not_169_out, OP5);
  not not_170 (not_170_out, OP4);
  not not_171 (not_171_out, OP1);
  not not_172 (not_172_out, OP0);
  not not_173 (not_173_out, OP5);
  not not_174 (not_174_out, OP4);
  not not_175 (not_175_out, OP2);
  not not_176 (not_176_out, OP1);
  not not_177 (not_177_out, OP5);
  not not_178 (not_178_out, OP4);
  not not_179 (not_179_out, OP2);
  not not_180 (not_180_out, OP0);
  not not_181 (not_181_out, OP5);
  not not_182 (not_182_out, OP4);
  not not_183 (not_183_out, OP1);
  not not_184 (not_184_out, OP4);
  not not_185 (not_185_out, OP3);
  not not_186 (not_186_out, OP2);
  not not_187 (not_187_out, OP5);
  not not_188 (not_188_out, OP4);
  not not_189 (not_189_out, OP3);
  not not_190 (not_190_out, OP2);
  not not_191 (not_191_out, OP1);
  not not_192 (not_192_out, OP0);
  not not_193 (not_193_out, F5);
  not not_194 (not_194_out, F4);
  not not_195 (not_195_out, F3);
  not not_196 (not_196_out, F1);
  not not_197 (not_197_out, F0);
  not not_198 (not_198_out, OP5);
  not not_199 (not_199_out, OP4);
  not not_200 (not_200_out, OP3);
  not not_201 (not_201_out, OP2);
  not not_202 (not_202_out, OP1);
  not not_203 (not_203_out, OP0);
  not not_204 (not_204_out, F4);
  not not_205 (not_205_out, F3);
  not not_206 (not_206_out, F2);
  not not_207 (not_207_out, OP4);
  not not_208 (not_208_out, OP3);
  not not_209 (not_209_out, OP2);
  not not_210 (not_210_out, OP1);
  not not_211 (not_211_out, OP0);
  not not_212 (not_212_out, OP5);
  not not_213 (not_213_out, OP4);
  not not_214 (not_214_out, OP3);
  not not_215 (not_215_out, OP2);
  not not_216 (not_216_out, OP1);
  not not_217 (not_217_out, OP0);
  not not_218 (not_218_out, F5);
  not not_219 (not_219_out, F4);
  not not_220 (not_220_out, F1);
  not not_221 (not_221_out, F0);
  not not_222 (not_222_out, OP5);
  not not_223 (not_223_out, OP4);
  not not_224 (not_224_out, OP3);
  not not_225 (not_225_out, OP2);
  not not_226 (not_226_out, OP1);
  not not_227 (not_227_out, OP0);
  not not_228 (not_228_out, F5);
  not not_229 (not_229_out, F4);
  not not_230 (not_230_out, F3);
  not not_231 (not_231_out, F2);
  not not_232 (not_232_out, F1);
  not not_233 (not_233_out, F0);
  not not_234 (not_234_out, OP5);
  not not_235 (not_235_out, OP4);
  not not_236 (not_236_out, OP3);
  not not_237 (not_237_out, OP2);
  not not_238 (not_238_out, OP1);
  not not_239 (not_239_out, OP0);
  not not_240 (not_240_out, F5);
  not not_241 (not_241_out, F4);
  not not_242 (not_242_out, F3);
  not not_243 (not_243_out, F2);
  not not_244 (not_244_out, OP5);
  not not_245 (not_245_out, OP4);
  not not_246 (not_246_out, OP3);
  not not_247 (not_247_out, OP2);
  not not_248 (not_248_out, OP1);
  not not_249 (not_249_out, OP0);
  not not_250 (not_250_out, F5);
  not not_251 (not_251_out, F4);
  not not_252 (not_252_out, F3);
  not not_253 (not_253_out, F2);
  not not_254 (not_254_out, F0);
  not not_255 (not_255_out, OP5);
  not not_256 (not_256_out, OP4);
  not not_257 (not_257_out, OP3);
  not not_258 (not_258_out, OP2);
  not not_259 (not_259_out, OP1);
  not not_260 (not_260_out, OP0);
  not not_261 (not_261_out, F4);
  not not_262 (not_262_out, F3);
  not not_263 (not_263_out, F2);
  not not_264 (not_264_out, F1);
  not not_265 (not_265_out, F0);
  not not_266 (not_266_out, OP5);
  not not_267 (not_267_out, OP4);
  not not_268 (not_268_out, OP3);
  not not_269 (not_269_out, OP2);
  not not_270 (not_270_out, OP1);
  not not_271 (not_271_out, OP0);
  not not_272 (not_272_out, F4);
  not not_273 (not_273_out, F3);
  not not_274 (not_274_out, F2);
  not not_275 (not_275_out, F1);
  not not_276 (not_276_out, OP5);
  not not_277 (not_277_out, OP4);
  not not_278 (not_278_out, OP3);
  not not_279 (not_279_out, OP2);
  not not_280 (not_280_out, OP1);
  not not_281 (not_281_out, OP0);
  not not_282 (not_282_out, F4);
  not not_283 (not_283_out, F3);
  not not_284 (not_284_out, F2);
  not not_285 (not_285_out, F0);
  not not_286 (not_286_out, OP5);
  not not_287 (not_287_out, OP4);
  not not_288 (not_288_out, OP3);
  not not_289 (not_289_out, OP2);
  not not_290 (not_290_out, OP1);
  not not_291 (not_291_out, OP0);
  not not_292 (not_292_out, F4);
  not not_293 (not_293_out, F3);
  not not_294 (not_294_out, F1);
  not not_295 (not_295_out, F0);
  not not_296 (not_296_out, OP5);
  not not_297 (not_297_out, OP4);
  not not_298 (not_298_out, OP3);
  not not_299 (not_299_out, OP2);
  not not_300 (not_300_out, OP1);
  not not_301 (not_301_out, OP0);
  not not_302 (not_302_out, F4);
  not not_303 (not_303_out, F3);
  not not_304 (not_304_out, F1);
  not not_305 (not_305_out, OP5);
  not not_306 (not_306_out, OP4);
  not not_307 (not_307_out, OP3);
  not not_308 (not_308_out, OP2);
  not not_309 (not_309_out, OP1);
  not not_310 (not_310_out, OP0);
  not not_311 (not_311_out, F4);
  not not_312 (not_312_out, F3);
  not not_313 (not_313_out, OP5);
  not not_314 (not_314_out, OP4);
  not not_315 (not_315_out, OP3);
  not not_316 (not_316_out, OP2);
  not not_317 (not_317_out, OP1);
  not not_318 (not_318_out, OP0);
  not not_319 (not_319_out, F4);
  not not_320 (not_320_out, F2);
  not not_321 (not_321_out, F0);
  not not_322 (not_322_out, OP5);
  not not_323 (not_323_out, OP4);
  not not_324 (not_324_out, OP3);
  not not_325 (not_325_out, OP2);
  not not_326 (not_326_out, OP1);
  not not_327 (not_327_out, OP0);
  not not_328 (not_328_out, F4);
  not not_329 (not_329_out, F2);
  not not_330 (not_330_out, OP5);
  not not_331 (not_331_out, OP4);
  not not_332 (not_332_out, OP3);
  not not_333 (not_333_out, OP2);
  not not_334 (not_334_out, OP1);
  not not_335 (not_335_out, OP0);
  not not_336 (not_336_out, F5);
  not not_337 (not_337_out, F4);
  not not_338 (not_338_out, F2);
  not not_339 (not_339_out, F1);
  not not_340 (not_340_out, F0);
  not not_341 (not_341_out, OP5);
  not not_342 (not_342_out, OP4);
  not not_343 (not_343_out, OP3);
  not not_344 (not_344_out, OP2);
  not not_345 (not_345_out, OP1);
  not not_346 (not_346_out, OP0);
  not not_347 (not_347_out, F5);
  not not_348 (not_348_out, F4);
  not not_349 (not_349_out, F3);
  not not_350 (not_350_out, F1);
  not not_351 (not_351_out, F0);
  not not_352 (not_352_out, OP5);
  not not_353 (not_353_out, OP4);
  not not_354 (not_354_out, OP3);
  not not_355 (not_355_out, OP2);
  not not_356 (not_356_out, OP1);
  not not_357 (not_357_out, OP0);
  not not_358 (not_358_out, F4);
  not not_359 (not_359_out, F3);
  not not_360 (not_360_out, F2);
  not not_361 (not_361_out, OP5);
  not not_362 (not_362_out, OP4);
  not not_363 (not_363_out, OP3);
  not not_364 (not_364_out, OP1);
  not not_365 (not_365_out, OP0);
  not not_366 (not_366_out, OP5);
  not not_367 (not_367_out, OP4);
  not not_368 (not_368_out, OP3);
  not not_369 (not_369_out, OP1);
  not not_370 (not_370_out, OP5);
  not not_371 (not_371_out, OP4);
  not not_372 (not_372_out, OP3);
  not not_373 (not_373_out, OP2);
  not not_374 (not_374_out, OP1);
  not not_375 (not_375_out, OP0);
  not not_376 (not_376_out, F5);
  not not_377 (not_377_out, F4);
  not not_378 (not_378_out, F2);
  not not_379 (not_379_out, F1);
  not not_380 (not_380_out, F0);
  not not_381 (not_381_out, OP5);
  not not_382 (not_382_out, OP4);
  not not_383 (not_383_out, OP3);
  not not_384 (not_384_out, OP2);
  not not_385 (not_385_out, OP0);
  not not_386 (not_386_out, OP5);
  not not_387 (not_387_out, OP4);
  not not_388 (not_388_out, OP3);
  not not_389 (not_389_out, OP2);
  not not_390 (not_390_out, OP0);
  not not_391 (not_391_out, OP1);
  not not_392 (not_392_out, OP2);
  not not_393 (not_393_out, OP3);
  not not_394 (not_394_out, OP4);
  not not_395 (not_395_out, OP5);
  not not_396 (not_396_out, F0);
  not not_397 (not_397_out, F1);
  not not_398 (not_398_out, F3);
  not not_399 (not_399_out, F4);
  not not_400 (not_400_out, F5);
  not not_401 (not_401_out, OP4);
  not not_402 (not_402_out, OP3);
  not not_403 (not_403_out, OP2);
  not not_404 (not_404_out, OP1);
  not not_405 (not_405_out, OP0);
  not not_406 (not_406_out, OP5);
  not not_407 (not_407_out, OP4);
  not not_408 (not_408_out, OP3);
  not not_409 (not_409_out, OP2);
  not not_410 (not_410_out, OP1);
  and and_1 (and_1_out, OP5, not_1_out, not_2_out, not_3_out, OP1, OP0);
  and and_2 (and_2_out, OP5, not_4_out, not_5_out, not_6_out, not_7_out, not_8_out);
  and and_3 (MemWrite, OP5, not_9_out, OP3, not_10_out, OP1, OP0);
  and and_4 (and_4_out, not_11_out, not_12_out, OP3, not_13_out, not_14_out, not_15_out);
  and and_5 (and_5_out, not_16_out, not_17_out, OP3, OP2, not_18_out, not_19_out);
  and and_6 (and_6_out, not_20_out, not_21_out, OP3, not_22_out, not_23_out, OP0);
  and and_7 (and_7_out, not_24_out, not_25_out, OP3, not_26_out, OP1, not_27_out);
  and and_8 (and_8_out, not_28_out, not_29_out, OP3, OP2, not_30_out, OP0);
  and and_9 (and_9_out, OP5, not_31_out, not_32_out, not_33_out, OP1, OP0);
  and and_10 (and_10_out, OP5, not_34_out, OP3, not_35_out, OP1, OP0);
  and and_11 (and_11_out, OP5, not_36_out, not_37_out, not_38_out, not_39_out, not_40_out);
  and and_12 (and_12_out, not_41_out, not_42_out, not_43_out, not_44_out, not_45_out, not_46_out, not_47_out, not_48_out, not_49_out, not_50_out, not_51_out, not_52_out);
  and and_13 (and_13_out, not_53_out, not_54_out, not_55_out, not_56_out, not_57_out, not_58_out, not_59_out, not_60_out, not_61_out, not_62_out, F1, F0);
  and and_14 (and_14_out, not_63_out, not_64_out, not_65_out, not_66_out, not_67_out, not_68_out, not_69_out, not_70_out, not_71_out, not_72_out, F1, not_73_out);
  and and_15 (and_15_out, not_74_out, not_75_out, not_76_out, not_77_out, not_78_out, not_79_out, F5, not_80_out, not_81_out, not_82_out, not_83_out, not_84_out);
  and and_16 (and_16_out, not_85_out, not_86_out, not_87_out, not_88_out, not_89_out, not_90_out, F5, not_91_out, not_92_out, not_93_out, not_94_out, F0);
  and and_17 (and_17_out, not_95_out, not_96_out, not_97_out, not_98_out, not_99_out, not_100_out, F5, not_101_out, not_102_out, not_103_out, F1, not_104_out);
  and and_18 (and_18_out, not_105_out, not_106_out, not_107_out, not_108_out, not_109_out, not_110_out, F5, not_111_out, not_112_out, F2, not_113_out, not_114_out);
  and and_19 (and_19_out, not_115_out, not_116_out, not_117_out, not_118_out, not_119_out, not_120_out, F5, not_121_out, not_122_out, F2, not_123_out, F0);
  and and_20 (and_20_out, not_124_out, not_125_out, not_126_out, not_127_out, not_128_out, not_129_out, F5, not_130_out, not_131_out, F2, F1, F0);
  and and_21 (and_21_out, not_132_out, not_133_out, not_134_out, not_135_out, not_136_out, not_137_out, F5, not_138_out, F3, not_139_out, F1, not_140_out);
  and and_22 (and_22_out, not_141_out, not_142_out, not_143_out, not_144_out, not_145_out, not_146_out, F5, not_147_out, F3, not_148_out, F1, F0);
  and and_23 (and_23_out, not_149_out, not_150_out, not_151_out, not_152_out, not_153_out, not_154_out, not_155_out, not_156_out, F3, not_157_out, not_158_out, not_159_out);
  and and_24 (and_24_out, not_160_out, not_161_out, not_162_out, not_163_out, OP1, OP0);
  and and_25 (and_25_out, not_164_out, not_165_out, OP3, not_166_out, not_167_out, not_168_out);
  and and_26 (and_26_out, not_169_out, not_170_out, OP3, OP2, not_171_out, not_172_out);
  and and_27 (and_27_out, not_173_out, not_174_out, OP3, not_175_out, not_176_out, OP0);
  and and_28 (and_28_out, not_177_out, not_178_out, OP3, not_179_out, OP1, not_180_out);
  and and_29 (and_29_out, not_181_out, not_182_out, OP3, OP2, not_183_out, OP0);
  and and_30 (and_30_out, OP5, not_184_out, not_185_out, not_186_out, OP1, OP0);
  and and_31 (and_31_out, not_187_out, not_188_out, not_189_out, not_190_out, not_191_out, not_192_out, not_193_out, not_194_out, not_195_out, F2, not_196_out, not_197_out);
  and and_32 (and_32_out, not_198_out, not_199_out, not_200_out, not_201_out, not_202_out, not_203_out, F5, not_204_out, not_205_out, not_206_out, F1, F0);
  and and_33 (and_33_out, OP5, not_207_out, not_208_out, not_209_out, not_210_out, not_211_out);
  and and_34 (SysCALL, not_212_out, not_213_out, not_214_out, not_215_out, not_216_out, not_217_out, not_218_out, not_219_out, F3, F2, not_220_out, not_221_out);
  and and_35 (and_35_out, not_222_out, not_223_out, not_224_out, not_225_out, not_226_out, not_227_out, not_228_out, not_229_out, not_230_out, not_231_out, not_232_out, not_233_out);
  and and_36 (and_36_out, not_234_out, not_235_out, not_236_out, not_237_out, not_238_out, not_239_out, not_240_out, not_241_out, not_242_out, not_243_out, F1, F0);
  and and_37 (and_37_out, not_244_out, not_245_out, not_246_out, not_247_out, not_248_out, not_249_out, not_250_out, not_251_out, not_252_out, not_253_out, F1, not_254_out);
  and and_38 (and_38_out, not_255_out, not_256_out, not_257_out, not_258_out, not_259_out, not_260_out, F5, not_261_out, not_262_out, not_263_out, not_264_out, not_265_out);
  and and_39 (and_39_out, not_266_out, not_267_out, not_268_out, not_269_out, not_270_out, not_271_out, F5, not_272_out, not_273_out, not_274_out, not_275_out, F0);
  and and_40 (and_40_out, not_276_out, not_277_out, not_278_out, not_279_out, not_280_out, not_281_out, F5, not_282_out, not_283_out, not_284_out, F1, not_285_out);
  and and_41 (and_41_out, not_286_out, not_287_out, not_288_out, not_289_out, not_290_out, not_291_out, F5, not_292_out, not_293_out, F2, not_294_out, not_295_out);
  and and_42 (and_42_out, not_296_out, not_297_out, not_298_out, not_299_out, not_300_out, not_301_out, F5, not_302_out, not_303_out, F2, not_304_out, F0);
  and and_43 (and_43_out, not_305_out, not_306_out, not_307_out, not_308_out, not_309_out, not_310_out, F5, not_311_out, not_312_out, F2, F1, F0);
  and and_44 (and_44_out, not_313_out, not_314_out, not_315_out, not_316_out, not_317_out, not_318_out, F5, not_319_out, F3, not_320_out, F1, not_321_out);
  and and_45 (and_45_out, not_322_out, not_323_out, not_324_out, not_325_out, not_326_out, not_327_out, F5, not_328_out, F3, not_329_out, F1, F0);
  and and_46 (and_46_out, not_330_out, not_331_out, not_332_out, not_333_out, not_334_out, not_335_out, not_336_out, not_337_out, F3, not_338_out, not_339_out, not_340_out);
  and and_47 (and_47_out, not_341_out, not_342_out, not_343_out, not_344_out, not_345_out, not_346_out, not_347_out, not_348_out, not_349_out, F2, not_350_out, not_351_out);
  and and_48 (and_48_out, not_352_out, not_353_out, not_354_out, not_355_out, not_356_out, not_357_out, F5, not_358_out, not_359_out, not_360_out, F1, F0);
  and and_49 (BEQ, not_361_out, not_362_out, not_363_out, OP2, not_364_out, not_365_out);
  and and_50 (BNE, not_366_out, not_367_out, not_368_out, OP2, not_369_out, OP0);
  and and_51 (JR, not_370_out, not_371_out, not_372_out, not_373_out, not_374_out, not_375_out, not_376_out, not_377_out, F3, not_378_out, not_379_out, not_380_out);
  and and_52 (JMP, not_381_out, not_382_out, not_383_out, not_384_out, OP1, not_385_out);
  and and_53 (JAL, not_386_out, not_387_out, not_388_out, not_389_out, OP1, OP0);
  and and_54 (SLLV, not_390_out, not_391_out, not_392_out, not_393_out, not_394_out, not_395_out, not_396_out, not_397_out, F2, not_398_out, not_399_out, not_400_out);
  and and_55 (LB, OP5, not_401_out, not_402_out, not_403_out, not_404_out, not_405_out);
  and and_56 (BLTZ, not_406_out, not_407_out, not_408_out, not_409_out, not_410_out, OP0);
  or or_1 (MemToReg, and_1_out, and_2_out);
  or or_2 (ALU_SRC, and_4_out, and_5_out, and_6_out, and_7_out, and_8_out, and_9_out, and_10_out, and_11_out);
  not not_411 (not_411_out, OP1);
  or or_3 (RegWrite, and_12_out, and_13_out, and_14_out, and_15_out, and_16_out, and_17_out, and_18_out, and_19_out, and_20_out, and_21_out, and_22_out, and_23_out, and_24_out, and_25_out, and_26_out, and_27_out, and_28_out, and_29_out, and_30_out, and_31_out, and_32_out, and_33_out);
  or or_4 (RegDst, and_35_out, and_36_out, and_37_out, and_38_out, and_39_out, and_40_out, and_41_out, and_42_out, and_43_out, and_44_out, and_45_out, and_46_out, and_47_out, and_48_out);
  not not_412 (SignedExt, and_57_out);
  and and_57 (and_57_out, not_222_out, not_223_out, OP3, OP2, not_411_out, OP0);
endmodule

// ALU
module MIPS_ALU (
  input  [4:0] shamt,
  input  [31:0] X,
  input  [31:0] Y,
  input  [3:0] AluOP,
  output Equal,
  output [31:0] Result,
  output [31:0] Result_2
);

  wire [0:0] comparator_1_lt, comparator_2_lt;
  wire [31:0] adder_1_out, AND_out, divider_1_out, divider_1_rem, multiplier_1_cout, multiplier_1_out,
       NOR_out, OR_out, shifter_1_out, shifter_2_out, shifter_3_out, subtractor_1_out, XOR_out;

  assign AND_out = X & Y;  // AND_Gate AND, 32 bits wide
  assign OR_out = X | Y;  // OR_Gate OR, 32 bits wide
  Shifter #(.width(32)) shifter_1 (.in(Y), .\dist (shamt), .out(shifter_1_out));
  Shifter #(.width(32), .shift("ar")) shifter_2 (.in(Y), .\dist (shamt), .out(shifter_2_out));
  Shifter #(.width(32), .shift("lr")) shifter_3 (.in(Y), .\dist (shamt), .out(shifter_3_out));
  Multiplier #(.width(32)) multiplier_1 (.a(X), .b(Y), .out(multiplier_1_out), .cout(multiplier_1_cout));  // open: cin
  Divider #(.width(32)) divider_1 (.a(X), .b(Y), .out(divider_1_out), .rem(divider_1_rem));  // open: upper
  Adder #(.width(32)) adder_1 (.a(X), .b(Y), .out(adder_1_out));  // open: cin, cout
  Subtractor #(.width(32)) subtractor_1 (.a(X), .b(Y), .out(subtractor_1_out));  // open: bin, bout
  assign XOR_out = X ^ Y;  // XOR_Gate XOR, 32 bits wide
  assign NOR_out = ~(X | Y);  // NOR_Gate NOR, 32 bits wide
  Comparator #(.width(32)) comparator_1 (.a(X), .b(Y), .eq(Equal), .lt(comparator_1_lt[0]));  // open: gt
  Comparator #(.width(32), .mode("unsigned")) comparator_2 (.a(X), .b(Y), .lt(comparator_2_lt[0]));  // open: gt, eq
  Multiplexer #(.select(4), .width(32), .enable("false")) multiplexer_1 (
    .in0(shifter_1_out), .in1(shifter_2_out), .in2(shifter_3_out), .in3(multiplier_1_out),
    .in4(divider_1_out), .in5(adder_1_out), .in6(subtractor_1_out), .in7(AND_out), .in8(OR_out),
    .in9(XOR_out), .in10(NOR_out), .in11({{31{1'b0}}, comparator_1_lt[0]}),
    .in12({{31{1'b0}}, comparator_2_lt[0]}), .in13({32{1'b0}}), .in14({32{1'b0}}), .in15({32{1'b0}}),
    .out(Result), .sel(AluOP));
  Multiplexer #(.select(4), .width(32), .enable("false")) multiplexer_2 (
    .in0({32{1'b0}}), .in1({32{1'b0}}), .in2({32{1'b0}}), .in3(multiplier_1_cout), .in4(divider_1_rem),
    .in5({32{1'b0}}), .in6({32{1'b0}}), .in7({32{1'b0}}), .in8({32{1'b0}}), .in9({32{1'b0}}),
    .in10({32{1'b0}}), .in11({32{1'b0}}), .in12({32{1'b0}}), .in13({32{1'b0}}), .in14({32{1'b0}}),
    .in15({32{1'b0}}), .out(Result_2), .sel(AluOP));

  // Other names for the same wires on the sheet: Result2[31:0] = Result_2; S[3:0] = AluOP

  // Notes on the sheet:
  //   不要改变此引脚区域内容，也不要改变ALU封装形式
  //   输入引脚
  //   输出引脚
endmodule

module MIPS_Regifile (
  input  [31:0] Din,
  input  Clk,
  input  WE,
  input  [4:0] R1_num,
  input  [4:0] W_num,
  input  [4:0] R2_num,
  output [31:0] R1,
  output [31:0] R2
);

  // RegisterFile registerfile_1: pin names not known; wires that end beside it: Din, Clk, WE, W_num, R1_num, R2_num, R1, R2
endmodule

module \理想流水线  (
);

  wire and_1_out, and_2_out, and_3_out, and_4_out, and_5_out, and_6_out, CLK, comparator_1_eq,
       comparator_2_eq, comparator_3_eq, ex_mem_1_aluequal_out, ex_mem_1_beq_out, ex_mem_1_bltzandar1_out,
       ex_mem_1_bne_out, ex_mem_1_jal_out, ex_mem_1_jmp_out, ex_mem_1_jr_out, ex_mem_1_lb_out,
       ex_mem_1_m2r_out, ex_mem_1_memw_out, ex_mem_1_r1equal22_out, ex_mem_1_regdst_out, ex_mem_1_regw_out,
       ex_mem_1_syscall_out, Go, id_ex_1_alusrc_out, id_ex_1_beq_out, id_ex_1_bltz_out, id_ex_1_bne_out,
       id_ex_1_jal_out, id_ex_1_jmp_out, id_ex_1_jr_out, id_ex_1_lb_out, id_ex_1_m2r_out, id_ex_1_memw_out,
       id_ex_1_r1equal22_out, id_ex_1_regdst_out, id_ex_1_regw_out, id_ex_1_sllv_out, id_ex_1_syscall_out,
       IR1, IR2, IR3, mem_wb_1_aluequal_out, mem_wb_1_beq_out, mem_wb_1_bltzandar1_out, mem_wb_1_bne_out,
       mem_wb_1_jal_out, mem_wb_1_jmp_out, mem_wb_1_jr_out, mem_wb_1_lb_out, mem_wb_1_m2r_out,
       mem_wb_1_r1equal22_out, mem_wb_1_regw_out, mem_wb_1_syscall_out, mips_alu_1_equal, not_1_out,
       not_2_out, or_2_out, or_3_out, or_4_out, or_5_out, or_6_out, RST, SignedExt, W1, W2, W3,
       \硬布线控制器_1_alu_src , \硬布线控制器_1_beq , \硬布线控制器_1_bltz , \硬布线控制器_1_bne , \硬布线控制器_1_jal , \硬布线控制器_1_jmp ,
       \硬布线控制器_1_jr , \硬布线控制器_1_lb , \硬布线控制器_1_memtoreg , \硬布线控制器_1_memwrite , \硬布线控制器_1_regdst ,
       \硬布线控制器_1_regwrite , \硬布线控制器_1_sllv , \硬布线控制器_1_syscall ;
  wire [3:0] id_ex_1_aluop_out, \硬布线控制器_1_alu_op ;
  wire [4:0] ex_mem_1_w__out, id_ex_1_w__out, mem_wb_1_w__out, multiplexer_4_out, multiplexer_5_out,
       multiplexer_6_out, multiplexer_7_out, multiplexer_11_out;
  wire [7:0] multiplexer_13_out;
  wire [11:0] EX_PC, ID_PC, IF_PC, MEM_PC, WB_PC;
  wire [15:0] \LoadUse次数 , mem_wb_1_instrcode_out, \总周期数 , \插入气泡数 , \无条件分支数 , \条件分支成功数 ;
  wire [27:0] PC_q;
  wire [31:0] adder_1_out, adder_2_out, adder_3_out, bit_extender_1_out, bit_extender_2_out,
       bit_extender_3_out, bit_extender_4_out, ex_mem_1_a_out, ex_mem_1_aluresult_out, ex_mem_1_b_out,
       ex_mem_1_instrcode_out, ex_mem_1_pc_out, id_ex_1_a_out, id_ex_1_b_out, id_ex_1_imm_out,
       id_ex_1_instrcode_out, id_ex_1_pc_out, if_id_1_instrcode_out, if_id_1_pc_out, LedData, mem_wb_1_a_out,
       mem_wb_1_aluresult_out, mem_wb_1_b_out, mem_wb_1_md_out, mem_wb_1_pc_out, mips_alu_1_result,
       mips_regifile_1_r1, mips_regifile_1_r2, multiplexer_1_out, multiplexer_2_out, multiplexer_3_out,
       multiplexer_8_out, multiplexer_9_out, multiplexer_10_out, multiplexer_12_out, multiplexer_14_out,
       multiplexer_15_out, ram_1_data, rom_1_data, shifter_1_out;
  wire [31:18] PC_q_2;
  wire [31:26] mem_wb_1_instrcode_out_2;

  Button \u_总复位  (.out(RST));
  Button _1 (.out(IR1));
  Button _2 (.out(IR2));
  Button _3 (.out(IR3));
  Button \u_继续运行  (.out(Go));
  LED led_1 (.in(W1));
  LED led_2 (.in(W2));
  LED led_3 (.in(W3));
  Multiplexer #(.width(32), .enable("false")) multiplexer_1 (
    .in0(adder_3_out), .in1(adder_2_out), .out(multiplexer_1_out), .sel(or_6_out));
  Multiplexer #(.width(32), .enable("false")) multiplexer_2 (
    .in0(multiplexer_1_out), .in1(mem_wb_1_a_out), .out(multiplexer_2_out), .sel(mem_wb_1_jr_out));
  Hex_Digit_Display hex_digit_display_1 (.value(LedData[31:28]));  // open: dp
  // OR_Gate or_1 has open pins: in0=or_3_out, out=open
  or or_2 (or_2_out, mem_wb_1_jmp_out, mem_wb_1_jal_out);
  Multiplexer #(.width(32), .enable("false")) multiplexer_3 (
    .in0(multiplexer_2_out), .in1({PC_q_2, mem_wb_1_instrcode_out, 2'b00}), .out(multiplexer_3_out),
    .sel(or_2_out));
  Hex_Digit_Display hex_digit_display_2 (.value(LedData[27:24]));  // open: dp
  Hex_Digit_Display hex_digit_display_3 (.value(LedData[23:20]));  // open: dp
  not not_1 (not_1_out, or_4_out);
  or or_3 (or_3_out, and_1_out, Go);
  Counter #(.width(16), .max('hffff)) counter_1 (
    .count(not_1_out), .Q(\总周期数 ), .clk(CLK), .clr(RST));  // open: load, D, carry
  Register #(.width(32)) PC (.D(adder_1_out), .en(not_1_out), .Q({PC_q_2[31:28], PC_q}), .clk(CLK), .clr(RST));
  Hex_Digit_Display hex_digit_display_4 (.value(LedData[15:12]));  // open: dp
  Hex_Digit_Display hex_digit_display_5 (.value(LedData[19:16]));  // open: dp
  and and_1 (and_1_out, or_4_out, mem_wb_1_r1equal22_out);
  Adder #(.width(32)) adder_1 (.a({PC_q_2[31:28], PC_q}), .b(32'h4), .out(adder_1_out));  // open: cin, cout
  Hex_Digit_Display hex_digit_display_6 (.value(LedData[11:8]));  // open: dp
  Hex_Digit_Display hex_digit_display_7 (.value(LedData[7:4]));  // open: dp
  Clock clock_1 (.out(CLK));
  ROM #(.addrWidth(10), .dataWidth(32)) rom_1 (.addr(PC_q[11:2]), .data(rom_1_data));  // open: sel
  Hex_Digit_Display hex_digit_display_8 (.value(LedData[3:0]));  // open: dp
  Comparator #(.width(32)) comparator_1 (
    .a({32{1'b0}}), .b({mem_wb_1_instrcode_out_2, PC_q_2[27:18], mem_wb_1_instrcode_out}),
    .eq(comparator_1_eq));  // open: gt, lt
  or or_4 (or_4_out, comparator_1_eq, mem_wb_1_syscall_out);
  IF_ID if_id_1 (
    .rst(RST), .clk(CLK), .InstrCode_IN(rom_1_data), .PC_IN({PC_q_2[31:28], PC_q}),
    .InstrCode_OUT(if_id_1_instrcode_out), .PC_OUT(if_id_1_pc_out));  // open: En
  // Probe on \总周期数 
  // Probe on \无条件分支数 
  // Probe on \条件分支成功数 
  // Probe on \插入气泡数 
  // Probe on \LoadUse次数 
  Adder #(.width(32)) adder_2 (.a(adder_3_out), .b(shifter_1_out), .out(adder_2_out));  // open: cin, cout
  // Probe on IF_PC
  // Probe on ID_PC
  \硬布线控制器  \u_硬布线控制器_1  (
    .OP(if_id_1_instrcode_out[31:26]), .Func(if_id_1_instrcode_out[5:0]), .ALU_OP(\硬布线控制器_1_alu_op ),
    .MemToReg(\硬布线控制器_1_memtoreg ), .MemWrite(\硬布线控制器_1_memwrite ), .ALU_SRC(\硬布线控制器_1_alu_src ),
    .RegWrite(\硬布线控制器_1_regwrite ), .SysCALL(\硬布线控制器_1_syscall ), .SignedExt(SignedExt),
    .RegDst(\硬布线控制器_1_regdst ), .Beq(\硬布线控制器_1_beq ), .Bne(\硬布线控制器_1_bne ), .JR(\硬布线控制器_1_jr ),
    .JMP(\硬布线控制器_1_jmp ), .JAL(\硬布线控制器_1_jal ), .SLLV(\硬布线控制器_1_sllv ), .LB(\硬布线控制器_1_lb ),
    .BLTZ(\硬布线控制器_1_bltz ));  // open: MFC0, MTC0, ERET, RS
  Multiplexer #(.width(5), .enable("false")) multiplexer_4 (
    .in0(if_id_1_instrcode_out[20:16]), .in1(if_id_1_instrcode_out[15:11]), .out(multiplexer_4_out),
    .sel(\硬布线控制器_1_regdst ));
  Multiplexer #(.width(5), .enable("false")) multiplexer_5 (
    .in0(multiplexer_4_out), .in1({5{1'b1}}), .out(multiplexer_5_out), .sel(\硬布线控制器_1_jal ));
  assign bit_extender_1_out = {{16{1'b0}}, if_id_1_instrcode_out[15:0]};  // Bit_Extender bit_extender_1
  assign bit_extender_2_out = {{16{if_id_1_instrcode_out[15]}}, if_id_1_instrcode_out[15:0]};  // Bit_Extender bit_extender_2
  // Probe on EX_PC
  // Probe on MEM_PC
  Multiplexer #(.width(5), .enable("false")) multiplexer_6 (
    .in0(if_id_1_instrcode_out[25:21]), .in1(5'b00010), .out(multiplexer_6_out), .sel(\硬布线控制器_1_syscall ));
  and and_2 (and_2_out, \硬布线控制器_1_syscall , comparator_2_eq);
  Multiplexer #(.width(5), .enable("false")) multiplexer_7 (
    .in0(if_id_1_instrcode_out[20:16]), .in1(5'b00100), .out(multiplexer_7_out), .sel(and_2_out));
  // Probe on WB_PC
  Multiplexer #(.width(32), .enable("false")) multiplexer_8 (
    .in0(bit_extender_1_out), .in1(bit_extender_2_out), .out(multiplexer_8_out), .sel(SignedExt));
  Shifter #(.width(32)) shifter_1 (.in(bit_extender_3_out), .\dist (5'b00010), .out(shifter_1_out));
  MIPS_Regifile mips_regifile_1 (
    .Din(multiplexer_15_out), .Clk(CLK), .R1(mips_regifile_1_r1), .R2(mips_regifile_1_r2),
    .WE(mem_wb_1_regw_out), .W_num(mem_wb_1_w__out), .R1_num(multiplexer_6_out), .R2_num(multiplexer_7_out));
  Comparator #(.width(32)) comparator_2 (.a(32'h22), .b(mips_regifile_1_r1), .eq(comparator_2_eq));  // open: gt, lt
  ID_EX id_ex_1 (
    .rst(RST), .clk(CLK), .JAL_IN(\硬布线控制器_1_jal ), .InstrCode_IN(if_id_1_instrcode_out),
    .A_IN(mips_regifile_1_r1), .LB_IN(\硬布线控制器_1_lb ), .RegW_IN(\硬布线控制器_1_regwrite ), .PC_IN(if_id_1_pc_out),
    .B_IN(mips_regifile_1_r2), .RegDst_IN(\硬布线控制器_1_regdst ), .syscall_IN(\硬布线控制器_1_syscall ),
    .Imm_IN(multiplexer_8_out), .R1Equal22_IN(comparator_2_eq), .JMP_IN(\硬布线控制器_1_jmp ),
    .JR_IN(\硬布线控制器_1_jr ), .Beq_IN(\硬布线控制器_1_beq ), .Bne_IN(\硬布线控制器_1_bne ), .MemW_IN(\硬布线控制器_1_memwrite ),
    .AluOP_IN(\硬布线控制器_1_alu_op ), .AluSrc_IN(\硬布线控制器_1_alu_src ), .BLTZ_IN(\硬布线控制器_1_bltz ),
    .SLLV_IN(\硬布线控制器_1_sllv ), .JAL_OUT(id_ex_1_jal_out), .InstrCode_OUT(id_ex_1_instrcode_out),
    .A_OUT(id_ex_1_a_out), .LB_OUT(id_ex_1_lb_out), .RegW_OUT(id_ex_1_regw_out), .PC_OUT(id_ex_1_pc_out),
    .B_OUT(id_ex_1_b_out), .RegDst_OUT(id_ex_1_regdst_out), .syscall_OUT(id_ex_1_syscall_out),
    .Imm_OUT(id_ex_1_imm_out), .R1Equal22_OUT(id_ex_1_r1equal22_out), .JMP_OUT(id_ex_1_jmp_out),
    .JR_OUT(id_ex_1_jr_out), .Beq_OUT(id_ex_1_beq_out), .Bne_OUT(id_ex_1_bne_out),
    .MemW_OUT(id_ex_1_memw_out), .AluOP_OUT(id_ex_1_aluop_out), .AluSrc_OUT(id_ex_1_alusrc_out),
    .BLTZ_OUT(id_ex_1_bltz_out), .SLLV_OUT(id_ex_1_sllv_out), .M2R_IN(\硬布线控制器_1_memtoreg ),
    .M2R_OUT(id_ex_1_m2r_out), .W__IN(multiplexer_5_out), .W__OUT(id_ex_1_w__out));  // open: AluEqual_IN, BLTZandAR1_IN, SignedExt_IN, AluEqual_OUT, BLTZandAR1_OUT, SignedExt_OUT, En, R2F2_IN, R2F2_OUT
  assign bit_extender_3_out = {{16{mem_wb_1_instrcode_out[15]}}, mem_wb_1_instrcode_out};  // Bit_Extender bit_extender_3
  Multiplexer #(.width(32), .enable("false")) multiplexer_9 (
    .in0(id_ex_1_b_out), .in1(id_ex_1_imm_out), .out(multiplexer_9_out), .sel(id_ex_1_alusrc_out));
  Multiplexer #(.width(32), .enable("false")) multiplexer_10 (
    .in0(multiplexer_9_out), .in1({32{1'b0}}), .out(multiplexer_10_out), .sel(id_ex_1_bltz_out));
  MIPS_ALU mips_alu_1 (
    .X(id_ex_1_a_out), .Y(multiplexer_10_out), .AluOP(id_ex_1_aluop_out), .Equal(mips_alu_1_equal),
    .Result(mips_alu_1_result), .shamt(multiplexer_11_out));  // open: Result_2
  Multiplexer #(.width(5), .enable("false")) multiplexer_11 (
    .in0(id_ex_1_instrcode_out[10:6]), .in1(id_ex_1_a_out[4:0]), .out(multiplexer_11_out),
    .sel(id_ex_1_sllv_out));
  Comparator #(.width(32)) comparator_3 (.a(mips_alu_1_result), .b(32'h1), .eq(comparator_3_eq));  // open: gt, lt
  and and_3 (and_3_out, comparator_3_eq, id_ex_1_bltz_out);
  EX_MEM ex_mem_1 (
    .rst(RST), .clk(CLK), .JAL_IN(id_ex_1_jal_out), .InstrCode_IN(id_ex_1_instrcode_out),
    .LB_IN(id_ex_1_lb_out), .RegW_IN(id_ex_1_regw_out), .PC_IN(id_ex_1_pc_out), .B_IN(id_ex_1_b_out),
    .RegDst_IN(id_ex_1_regdst_out), .syscall_IN(id_ex_1_syscall_out), .AluResult_IN(mips_alu_1_result),
    .R1Equal22_IN(id_ex_1_r1equal22_out), .JMP_IN(id_ex_1_jmp_out), .JR_IN(id_ex_1_jr_out),
    .Beq_IN(id_ex_1_beq_out), .Bne_IN(id_ex_1_bne_out), .AluEqual_IN(mips_alu_1_equal),
    .BLTZandAR1_IN(and_3_out), .MemW_IN(id_ex_1_memw_out), .JAL_OUT(ex_mem_1_jal_out),
    .InstrCode_OUT(ex_mem_1_instrcode_out), .LB_OUT(ex_mem_1_lb_out), .RegW_OUT(ex_mem_1_regw_out),
    .PC_OUT(ex_mem_1_pc_out), .B_OUT(ex_mem_1_b_out), .RegDst_OUT(ex_mem_1_regdst_out),
    .syscall_OUT(ex_mem_1_syscall_out), .AluResult_OUT(ex_mem_1_aluresult_out),
    .R1Equal22_OUT(ex_mem_1_r1equal22_out), .JMP_OUT(ex_mem_1_jmp_out), .JR_OUT(ex_mem_1_jr_out),
    .Beq_OUT(ex_mem_1_beq_out), .Bne_OUT(ex_mem_1_bne_out), .AluEqual_OUT(ex_mem_1_aluequal_out),
    .BLTZandAR1_OUT(ex_mem_1_bltzandar1_out), .MemW_OUT(ex_mem_1_memw_out), .A_IN(id_ex_1_a_out),
    .A_OUT(ex_mem_1_a_out), .M2R_IN(id_ex_1_m2r_out), .M2R_OUT(ex_mem_1_m2r_out), .W__IN(id_ex_1_w__out),
    .W__OUT(ex_mem_1_w__out));  // open: En
  // Probe on ex_mem_1_b_out
  RAM #(.addrWidth(10), .dataWidth(32), .bus("separate")) ram_1 (
    .addr(ex_mem_1_aluresult_out[11:2]), .din(ex_mem_1_b_out), .data(ram_1_data), .str(ex_mem_1_memw_out),
    .clk(CLK), .clr(RST));  // open: sel, ld
  MEM_WB mem_wb_1 (
    .rst(RST), .clk(CLK), .JAL_IN(ex_mem_1_jal_out), .InstrCode_IN(ex_mem_1_instrcode_out),
    .LB_IN(ex_mem_1_lb_out), .RegW_IN(ex_mem_1_regw_out), .PC_IN(ex_mem_1_pc_out), .MD_IN(ram_1_data),
    .RegDst_IN(ex_mem_1_regdst_out), .syscall_IN(ex_mem_1_syscall_out),
    .AluResult_IN(ex_mem_1_aluresult_out), .R1Equal22_IN(ex_mem_1_r1equal22_out), .JMP_IN(ex_mem_1_jmp_out),
    .JR_IN(ex_mem_1_jr_out), .Beq_IN(ex_mem_1_beq_out), .Bne_IN(ex_mem_1_bne_out),
    .AluEqual_IN(ex_mem_1_aluequal_out), .BLTZandAR1_IN(ex_mem_1_bltzandar1_out), .JAL_OUT(mem_wb_1_jal_out),
    .InstrCode_OUT({mem_wb_1_instrcode_out_2, PC_q_2[27:18], mem_wb_1_instrcode_out}),
    .LB_OUT(mem_wb_1_lb_out), .RegW_OUT(mem_wb_1_regw_out), .PC_OUT(mem_wb_1_pc_out),
    .MD_OUT(mem_wb_1_md_out), .syscall_OUT(mem_wb_1_syscall_out), .AluResult_OUT(mem_wb_1_aluresult_out),
    .R1Equal22_OUT(mem_wb_1_r1equal22_out), .JMP_OUT(mem_wb_1_jmp_out), .JR_OUT(mem_wb_1_jr_out),
    .Beq_OUT(mem_wb_1_beq_out), .Bne_OUT(mem_wb_1_bne_out), .AluEqual_OUT(mem_wb_1_aluequal_out),
    .BLTZandAR1_OUT(mem_wb_1_bltzandar1_out), .A_IN(ex_mem_1_a_out), .A_OUT(mem_wb_1_a_out),
    .B_IN(ex_mem_1_b_out), .B_OUT(mem_wb_1_b_out), .M2R_IN(ex_mem_1_m2r_out), .M2R_OUT(mem_wb_1_m2r_out),
    .W__IN(ex_mem_1_w__out), .W__OUT(mem_wb_1_w__out));  // open: RegDst_OUT, En
  Multiplexer #(.width(32), .enable("false")) multiplexer_12 (
    .in0(mem_wb_1_aluresult_out), .in1(mem_wb_1_md_out), .out(multiplexer_12_out), .sel(mem_wb_1_m2r_out));
  not not_2 (not_2_out, mem_wb_1_aluequal_out);
  or or_5 (or_5_out, mem_wb_1_jal_out, mem_wb_1_jmp_out, mem_wb_1_jr_out);
  and and_4 (and_4_out, mem_wb_1_beq_out, mem_wb_1_aluequal_out);
  and and_5 (and_5_out, mem_wb_1_bne_out, not_2_out);
  and and_6 (and_6_out, mem_wb_1_r1equal22_out, mem_wb_1_syscall_out);
  // Probe on mem_wb_1_b_out
  Multiplexer #(.select(2), .width(8), .enable("false")) multiplexer_13 (
    .in0(multiplexer_12_out[7:0]), .in1(multiplexer_12_out[15:8]), .in2(multiplexer_12_out[23:16]),
    .in3(multiplexer_12_out[31:24]), .out(multiplexer_13_out), .sel(mem_wb_1_aluresult_out[1:0]));
  Counter #(.width(16), .max('hffff)) counter_2 (
    .count(or_5_out), .Q(\无条件分支数 ), .clk(CLK), .clr(RST));  // open: load, D, carry
  or or_6 (or_6_out, and_4_out, mem_wb_1_bltzandar1_out, and_5_out);
  Register #(.width(32), .trigger("high")) register_1 (
    .D(mem_wb_1_b_out), .en(and_6_out), .Q(LedData), .clk(CLK), .clr(RST));
  Adder #(.width(32)) adder_3 (.a(mem_wb_1_pc_out), .b(32'h4), .out(adder_3_out));  // open: cin, cout
  Multiplexer #(.width(32), .enable("false")) multiplexer_14 (
    .in0(multiplexer_12_out), .in1(adder_3_out), .out(multiplexer_14_out), .sel(mem_wb_1_jal_out));
  assign bit_extender_4_out = {{24{multiplexer_13_out[7]}}, multiplexer_13_out};  // Bit_Extender bit_extender_4
  Counter #(.width(16), .max('hffff)) counter_3 (
    .count(or_6_out), .Q(\条件分支成功数 ), .clk(CLK), .clr(RST));  // open: load, D, carry
  Multiplexer #(.width(32), .enable("false")) multiplexer_15 (
    .in0(multiplexer_14_out), .in1(bit_extender_4_out), .out(multiplexer_15_out), .sel(mem_wb_1_lb_out));

  // Notes on the sheet:
  //   中断源
  //   中断等待指示
  //   数码管输出
  //   指令存储器
  //   contents of rom_1 (hex, n*v repeats v):
  //   20100000 20110000 20120000 20130000 36100000 36310001 36520002 36730003 ae100000 ae110004 ae120008
  //   ae13000c 2002000a 20110000 20120000 20130000 c
  //   Op
  //   Func
  //   Beq
  //   Bne
  //   MemToReg
  //   MemWrite
  //   AluOP
  //   AluSrcB
  //   RegWrite
  //   RegDst
  //   流水调试日志用
endmodule
// 源寄存器使用情况
module \源寄存器使用情况  (
  input  OP0,
  input  OP1,
  input  OP2,
  input  OP3,
  input  OP4,
  input  OP5,
  input  F0,
  input  F1,
  input  F2,
  input  F3,
  input  F4,
  input  F5,
  output R1_Used,
  output R2_Used
);

  wire and_1_out, and_2_out, and_3_out, and_4_out, and_5_out, and_6_out, and_7_out, and_8_out, and_9_out,
       and_10_out, and_11_out, and_12_out, and_13_out, and_14_out, and_15_out, and_16_out, and_17_out,
       and_18_out, and_19_out, and_20_out, and_21_out, and_22_out, and_23_out, and_24_out, and_25_out,
       and_26_out, and_27_out, and_28_out, and_29_out, and_30_out, and_31_out, and_32_out, and_33_out,
       and_34_out, and_35_out, and_36_out, and_37_out, and_38_out, and_39_out, and_40_out, not_1_out,
       not_2_out, not_3_out, not_4_out, not_5_out, not_6_out, not_7_out, not_8_out, not_9_out, not_10_out,
       not_11_out, not_12_out, not_13_out, not_14_out, not_15_out, not_16_out, not_17_out, not_18_out,
       not_19_out, not_20_out, not_21_out, not_22_out, not_23_out, not_24_out, not_25_out, not_26_out,
       not_27_out, not_28_out, not_29_out, not_30_out, not_31_out, not_32_out, not_33_out, not_34_out,
       not_35_out, not_36_out, not_37_out, not_38_out, not_39_out, not_40_out, not_41_out, not_42_out,
       not_43_out, not_44_out, not_45_out, not_46_out, not_47_out, not_48_out, not_49_out, not_50_out,
       not_51_out, not_52_out, not_53_out, not_54_out, not_55_out, not_56_out, not_57_out, not_58_out,
       not_59_out, not_60_out, not_61_out, not_62_out, not_63_out, not_64_out, not_65_out, not_66_out,
       not_67_out, not_68_out, not_69_out, not_70_out, not_71_out, not_72_out, not_73_out, not_74_out,
       not_75_out, not_76_out, not_77_out, not_78_out, not_79_out, not_80_out, not_81_out, not_82_out,
       not_83_out, not_84_out, not_85_out, not_86_out, not_87_out, not_88_out, not_89_out, not_90_out,
       not_91_out, not_92_out, not_93_out, not_94_out, not_95_out, not_96_out, not_97_out, not_98_out,
       not_99_out, not_100_out, not_101_out, not_102_out, not_103_out, not_104_out, not_105_out, not_106_out,
       not_107_out, not_108_out, not_109_out, not_110_out, not_111_out, not_112_out, not_113_out,
       not_114_out, not_115_out, not_116_out, not_117_out, not_118_out, not_119_out, not_120_out,
       not_121_out, not_122_out, not_123_out, not_124_out, not_125_out, not_126_out, not_127_out,
       not_128_out, not_129_out, not_130_out, not_131_out, not_132_out, not_133_out, not_134_out,
       not_135_out, not_136_out, not_137_out, not_138_out, not_139_out, not_140_out, not_141_out,
       not_142_out, not_143_out, not_144_out, not_145_out, not_146_out, not_147_out, not_148_out,
       not_149_out, not_150_out, not_151_out, not_152_out, not_153_out, not_154_out, not_155_out,
       not_156_out, not_157_out, not_158_out, not_159_out, not_160_out, not_161_out, not_162_out,
       not_163_out, not_164_out, not_165_out, not_166_out, not_167_out, not_168_out, not_169_out,
       not_170_out, not_171_out, not_172_out, not_173_out, not_174_out, not_175_out, not_176_out,
       not_177_out, not_178_out, not_179_out, not_180_out, not_181_out, not_182_out, not_183_out,
       not_184_out, not_185_out, not_186_out, not_187_out, not_188_out, not_189_out, not_190_out,
       not_191_out, not_192_out, not_193_out, not_194_out, not_195_out, not_196_out, not_197_out,
       not_198_out, not_199_out, not_200_out, not_201_out, not_202_out, not_203_out, not_204_out,
       not_205_out, not_206_out, not_207_out, not_208_out, not_209_out, not_210_out, not_211_out,
       not_212_out, not_213_out, not_214_out, not_215_out, not_216_out, not_217_out, not_218_out,
       not_219_out, not_220_out, not_221_out, not_222_out, not_223_out, not_224_out, not_225_out,
       not_226_out, not_227_out, not_228_out, not_229_out, not_230_out, not_231_out, not_232_out,
       not_233_out, not_234_out, not_235_out, not_236_out, not_237_out, not_238_out, not_239_out,
       not_240_out, not_241_out, not_242_out, not_243_out, not_244_out, not_245_out, not_246_out,
       not_247_out, not_248_out, not_249_out, not_250_out, not_251_out, not_252_out, not_253_out,
       not_254_out, not_255_out, not_256_out, not_257_out, not_258_out, not_259_out, not_260_out,
       not_261_out, not_262_out, not_263_out, not_264_out, not_265_out, not_266_out, not_267_out,
       not_268_out, not_269_out, not_270_out, not_271_out, not_272_out, not_273_out, not_274_out,
       not_275_out, not_276_out, not_277_out, not_278_out, not_279_out, not_280_out, not_281_out,
       not_282_out, not_283_out, not_284_out, not_285_out, not_286_out, not_287_out, not_288_out,
       not_289_out, not_290_out, not_291_out, not_292_out, not_293_out, not_294_out, not_295_out,
       not_296_out, not_297_out, not_298_out, not_299_out, not_300_out, not_301_out, not_302_out,
       not_303_out, not_304_out, not_305_out, not_306_out, not_307_out, not_308_out, not_309_out;

  not not_1 (not_1_out, OP5);
  not not_2 (not_2_out, OP4);
  not not_3 (not_3_out, OP3);
  not not_4 (not_4_out, OP2);
  not not_5 (not_5_out, OP1);
  not not_6 (not_6_out, OP0);
  not not_7 (not_7_out, F4);
  not not_8 (not_8_out, F3);
  not not_9 (not_9_out, F2);
  not not_10 (not_10_out, F1);
  not not_11 (not_11_out, F0);
  not not_12 (not_12_out, OP5);
  not not_13 (not_13_out, OP4);
  not not_14 (not_14_out, OP3);
  not not_15 (not_15_out, OP2);
  not not_16 (not_16_out, OP1);
  not not_17 (not_17_out, OP0);
  not not_18 (not_18_out, F4);
  not not_19 (not_19_out, F3);
  not not_20 (not_20_out, F2);
  not not_21 (not_21_out, F1);
  not not_22 (not_22_out, OP5);
  not not_23 (not_23_out, OP4);
  not not_24 (not_24_out, OP3);
  not not_25 (not_25_out, OP2);
  not not_26 (not_26_out, OP1);
  not not_27 (not_27_out, OP0);
  not not_28 (not_28_out, F4);
  not not_29 (not_29_out, F3);
  not not_30 (not_30_out, F2);
  not not_31 (not_31_out, F0);
  not not_32 (not_32_out, OP5);
  not not_33 (not_33_out, OP4);
  not not_34 (not_34_out, OP3);
  not not_35 (not_35_out, OP2);
  not not_36 (not_36_out, OP1);
  not not_37 (not_37_out, OP0);
  not not_38 (not_38_out, F4);
  not not_39 (not_39_out, F3);
  not not_40 (not_40_out, F1);
  not not_41 (not_41_out, F0);
  not not_42 (not_42_out, OP5);
  not not_43 (not_43_out, OP4);
  not not_44 (not_44_out, OP3);
  not not_45 (not_45_out, OP2);
  not not_46 (not_46_out, OP1);
  not not_47 (not_47_out, OP0);
  not not_48 (not_48_out, F4);
  not not_49 (not_49_out, F3);
  not not_50 (not_50_out, F1);
  not not_51 (not_51_out, OP5);
  not not_52 (not_52_out, OP4);
  not not_53 (not_53_out, OP3);
  not not_54 (not_54_out, OP2);
  not not_55 (not_55_out, OP1);
  not not_56 (not_56_out, OP0);
  not not_57 (not_57_out, F4);
  not not_58 (not_58_out, F3);
  not not_59 (not_59_out, OP5);
  not not_60 (not_60_out, OP4);
  not not_61 (not_61_out, OP3);
  not not_62 (not_62_out, OP2);
  not not_63 (not_63_out, OP1);
  not not_64 (not_64_out, OP0);
  not not_65 (not_65_out, F4);
  not not_66 (not_66_out, F2);
  not not_67 (not_67_out, F0);
  not not_68 (not_68_out, OP5);
  not not_69 (not_69_out, OP4);
  not not_70 (not_70_out, OP3);
  not not_71 (not_71_out, OP2);
  not not_72 (not_72_out, OP1);
  not not_73 (not_73_out, OP0);
  not not_74 (not_74_out, F4);
  not not_75 (not_75_out, F2);
  not not_76 (not_76_out, OP5);
  not not_77 (not_77_out, OP4);
  not not_78 (not_78_out, OP3);
  not not_79 (not_79_out, OP2);
  not not_80 (not_80_out, OP1);
  not not_81 (not_81_out, OP0);
  not not_82 (not_82_out, F5);
  not not_83 (not_83_out, F4);
  not not_84 (not_84_out, F2);
  not not_85 (not_85_out, F1);
  not not_86 (not_86_out, F0);
  not not_87 (not_87_out, OP5);
  not not_88 (not_88_out, OP4);
  not not_89 (not_89_out, OP3);
  not not_90 (not_90_out, OP2);
  not not_91 (not_91_out, OP1);
  not not_92 (not_92_out, OP0);
  not not_93 (not_93_out, F5);
  not not_94 (not_94_out, F4);
  not not_95 (not_95_out, F1);
  not not_96 (not_96_out, F0);
  not not_97 (not_97_out, OP5);
  not not_98 (not_98_out, OP4);
  not not_99 (not_99_out, OP3);
  not not_100 (not_100_out, OP1);
  not not_101 (not_101_out, OP0);
  not not_102 (not_102_out, OP5);
  not not_103 (not_103_out, OP4);
  not not_104 (not_104_out, OP3);
  not not_105 (not_105_out, OP1);
  not not_106 (not_106_out, OP5);
  not not_107 (not_107_out, OP4);
  not not_108 (not_108_out, OP2);
  not not_109 (not_109_out, OP1);
  not not_110 (not_110_out, OP0);
  not not_111 (not_111_out, OP5);
  not not_112 (not_112_out, OP4);
  not not_113 (not_113_out, OP1);
  not not_114 (not_114_out, OP0);
  not not_115 (not_115_out, OP5);
  not not_116 (not_116_out, OP4);
  not not_117 (not_117_out, OP2);
  not not_118 (not_118_out, OP1);
  not not_119 (not_119_out, OP5);
  not not_120 (not_120_out, OP4);
  not not_121 (not_121_out, OP2);
  not not_122 (not_122_out, OP0);
  not not_123 (not_123_out, OP5);
  not not_124 (not_124_out, OP4);
  not not_125 (not_125_out, OP1);
  not not_126 (not_126_out, OP4);
  not not_127 (not_127_out, OP3);
  not not_128 (not_128_out, OP2);
  not not_129 (not_129_out, OP4);
  not not_130 (not_130_out, OP2);
  not not_131 (not_131_out, OP5);
  not not_132 (not_132_out, OP4);
  not not_133 (not_133_out, OP3);
  not not_134 (not_134_out, OP2);
  not not_135 (not_135_out, OP1);
  not not_136 (not_136_out, OP0);
  not not_137 (not_137_out, F5);
  not not_138 (not_138_out, F4);
  not not_139 (not_139_out, F3);
  not not_140 (not_140_out, F1);
  not not_141 (not_141_out, F0);
  not not_142 (not_142_out, OP5);
  not not_143 (not_143_out, OP4);
  not not_144 (not_144_out, OP3);
  not not_145 (not_145_out, OP2);
  not not_146 (not_146_out, OP1);
  not not_147 (not_147_out, OP0);
  not not_148 (not_148_out, F4);
  not not_149 (not_149_out, F3);
  not not_150 (not_150_out, F2);
  not not_151 (not_151_out, OP4);
  not not_152 (not_152_out, OP3);
  not not_153 (not_153_out, OP2);
  not not_154 (not_154_out, OP1);
  not not_155 (not_155_out, OP0);
  not not_156 (not_156_out, OP5);
  not not_157 (not_157_out, OP4);
  not not_158 (not_158_out, OP3);
  not not_159 (not_159_out, OP2);
  not not_160 (not_160_out, OP1);
  not not_161 (not_161_out, OP5);
  not not_162 (not_162_out, OP4);
  not not_163 (not_163_out, OP3);
  not not_164 (not_164_out, OP2);
  not not_165 (not_165_out, OP1);
  not not_166 (not_166_out, OP0);
  not not_167 (not_167_out, F5);
  not not_168 (not_168_out, F4);
  not not_169 (not_169_out, F3);
  not not_170 (not_170_out, F2);
  not not_171 (not_171_out, F1);
  not not_172 (not_172_out, F0);
  not not_173 (not_173_out, OP5);
  not not_174 (not_174_out, OP4);
  not not_175 (not_175_out, OP3);
  not not_176 (not_176_out, OP2);
  not not_177 (not_177_out, OP1);
  not not_178 (not_178_out, OP0);
  not not_179 (not_179_out, F5);
  not not_180 (not_180_out, F4);
  not not_181 (not_181_out, F3);
  not not_182 (not_182_out, F2);
  not not_183 (not_183_out, OP5);
  not not_184 (not_184_out, OP4);
  not not_185 (not_185_out, OP3);
  not not_186 (not_186_out, OP2);
  not not_187 (not_187_out, OP1);
  not not_188 (not_188_out, OP0);
  not not_189 (not_189_out, F5);
  not not_190 (not_190_out, F4);
  not not_191 (not_191_out, F3);
  not not_192 (not_192_out, F2);
  not not_193 (not_193_out, F0);
  not not_194 (not_194_out, OP5);
  not not_195 (not_195_out, OP4);
  not not_196 (not_196_out, OP3);
  not not_197 (not_197_out, OP2);
  not not_198 (not_198_out, OP1);
  not not_199 (not_199_out, OP0);
  not not_200 (not_200_out, F4);
  not not_201 (not_201_out, F3);
  not not_202 (not_202_out, F2);
  not not_203 (not_203_out, F1);
  not not_204 (not_204_out, F0);
  not not_205 (not_205_out, OP5);
  not not_206 (not_206_out, OP4);
  not not_207 (not_207_out, OP3);
  not not_208 (not_208_out, OP2);
  not not_209 (not_209_out, OP1);
  not not_210 (not_210_out, OP0);
  not not_211 (not_211_out, F4);
  not not_212 (not_212_out, F3);
  not not_213 (not_213_out, F2);
  not not_214 (not_214_out, F1);
  not not_215 (not_215_out, OP5);
  not not_216 (not_216_out, OP4);
  not not_217 (not_217_out, OP3);
  not not_218 (not_218_out, OP2);
  not not_219 (not_219_out, OP1);
  not not_220 (not_220_out, OP0);
  not not_221 (not_221_out, F4);
  not not_222 (not_222_out, F3);
  not not_223 (not_223_out, F2);
  not not_224 (not_224_out, F0);
  not not_225 (not_225_out, OP5);
  not not_226 (not_226_out, OP4);
  not not_227 (not_227_out, OP3);
  not not_228 (not_228_out, OP2);
  not not_229 (not_229_out, OP1);
  not not_230 (not_230_out, OP0);
  not not_231 (not_231_out, F4);
  not not_232 (not_232_out, F3);
  not not_233 (not_233_out, F1);
  not not_234 (not_234_out, F0);
  not not_235 (not_235_out, OP5);
  not not_236 (not_236_out, OP4);
  not not_237 (not_237_out, OP3);
  not not_238 (not_238_out, OP2);
  not not_239 (not_239_out, OP1);
  not not_240 (not_240_out, OP0);
  not not_241 (not_241_out, F4);
  not not_242 (not_242_out, F3);
  not not_243 (not_243_out, F1);
  not not_244 (not_244_out, OP5);
  not not_245 (not_245_out, OP4);
  not not_246 (not_246_out, OP3);
  not not_247 (not_247_out, OP2);
  not not_248 (not_248_out, OP1);
  not not_249 (not_249_out, OP0);
  not not_250 (not_250_out, F4);
  not not_251 (not_251_out, F3);
  not not_252 (not_252_out, OP5);
  not not_253 (not_253_out, OP4);
  not not_254 (not_254_out, OP3);
  not not_255 (not_255_out, OP2);
  not not_256 (not_256_out, OP1);
  not not_257 (not_257_out, OP0);
  not not_258 (not_258_out, F4);
  not not_259 (not_259_out, F2);
  not not_260 (not_260_out, F0);
  not not_261 (not_261_out, OP5);
  not not_262 (not_262_out, OP4);
  not not_263 (not_263_out, OP3);
  not not_264 (not_264_out, OP2);
  not not_265 (not_265_out, OP1);
  not not_266 (not_266_out, OP0);
  not not_267 (not_267_out, F4);
  not not_268 (not_268_out, F2);
  not not_269 (not_269_out, OP5);
  not not_270 (not_270_out, OP4);
  not not_271 (not_271_out, OP3);
  not not_272 (not_272_out, OP2);
  not not_273 (not_273_out, OP1);
  not not_274 (not_274_out, OP0);
  not not_275 (not_275_out, F5);
  not not_276 (not_276_out, F4);
  not not_277 (not_277_out, F1);
  not not_278 (not_278_out, F0);
  not not_279 (not_279_out, OP5);
  not not_280 (not_280_out, OP4);
  not not_281 (not_281_out, OP3);
  not not_282 (not_282_out, OP1);
  not not_283 (not_283_out, OP0);
  not not_284 (not_284_out, OP5);
  not not_285 (not_285_out, OP4);
  not not_286 (not_286_out, OP3);
  not not_287 (not_287_out, OP1);
  not not_288 (not_288_out, OP4);
  not not_289 (not_289_out, OP2);
  not not_290 (not_290_out, OP5);
  not not_291 (not_291_out, OP4);
  not not_292 (not_292_out, OP3);
  not not_293 (not_293_out, OP2);
  not not_294 (not_294_out, OP1);
  not not_295 (not_295_out, OP0);
  not not_296 (not_296_out, F5);
  not not_297 (not_297_out, F4);
  not not_298 (not_298_out, F3);
  not not_299 (not_299_out, F1);
  not not_300 (not_300_out, F0);
  not not_301 (not_301_out, OP5);
  not not_302 (not_302_out, OP4);
  not not_303 (not_303_out, OP3);
  not not_304 (not_304_out, OP2);
  not not_305 (not_305_out, OP1);
  not not_306 (not_306_out, OP0);
  not not_307 (not_307_out, F4);
  not not_308 (not_308_out, F3);
  not not_309 (not_309_out, F2);
  and and_1 (and_1_out, not_1_out, not_2_out, not_3_out, not_4_out, not_5_out, not_6_out, F5, not_7_out, not_8_out, not_9_out, not_10_out, not_11_out);
  and and_2 (and_2_out, not_12_out, not_13_out, not_14_out, not_15_out, not_16_out, not_17_out, F5, not_18_out, not_19_out, not_20_out, not_21_out, F0);
  and and_3 (and_3_out, not_22_out, not_23_out, not_24_out, not_25_out, not_26_out, not_27_out, F5, not_28_out, not_29_out, not_30_out, F1, not_31_out);
  and and_4 (and_4_out, not_32_out, not_33_out, not_34_out, not_35_out, not_36_out, not_37_out, F5, not_38_out, not_39_out, F2, not_40_out, not_41_out);
  and and_5 (and_5_out, not_42_out, not_43_out, not_44_out, not_45_out, not_46_out, not_47_out, F5, not_48_out, not_49_out, F2, not_50_out, F0);
  and and_6 (and_6_out, not_51_out, not_52_out, not_53_out, not_54_out, not_55_out, not_56_out, F5, not_57_out, not_58_out, F2, F1, F0);
  and and_7 (and_7_out, not_59_out, not_60_out, not_61_out, not_62_out, not_63_out, not_64_out, F5, not_65_out, F3, not_66_out, F1, not_67_out);
  and and_8 (and_8_out, not_68_out, not_69_out, not_70_out, not_71_out, not_72_out, not_73_out, F5, not_74_out, F3, not_75_out, F1, F0);
  and and_9 (and_9_out, not_76_out, not_77_out, not_78_out, not_79_out, not_80_out, not_81_out, not_82_out, not_83_out, F3, not_84_out, not_85_out, not_86_out);
  and and_10 (and_10_out, not_87_out, not_88_out, not_89_out, not_90_out, not_91_out, not_92_out, not_93_out, not_94_out, F3, F2, not_95_out, not_96_out);
  and and_11 (and_11_out, not_97_out, not_98_out, not_99_out, OP2, not_100_out, not_101_out);
  and and_12 (and_12_out, not_102_out, not_103_out, not_104_out, OP2, not_105_out, OP0);
  and and_13 (and_13_out, not_106_out, not_107_out, OP3, not_108_out, not_109_out, not_110_out);
  and and_14 (and_14_out, not_111_out, not_112_out, OP3, OP2, not_113_out, not_114_out);
  and and_15 (and_15_out, not_115_out, not_116_out, OP3, not_117_out, not_118_out, OP0);
  and and_16 (and_16_out, not_119_out, not_120_out, OP3, not_121_out, OP1, not_122_out);
  and and_17 (and_17_out, not_123_out, not_124_out, OP3, OP2, not_125_out, OP0);
  and and_18 (and_18_out, OP5, not_126_out, not_127_out, not_128_out, OP1, OP0);
  and and_19 (and_19_out, OP5, not_129_out, OP3, not_130_out, OP1, OP0);
  and and_20 (and_20_out, not_131_out, not_132_out, not_133_out, not_134_out, not_135_out, not_136_out, not_137_out, not_138_out, not_139_out, F2, not_140_out, not_141_out);
  and and_21 (and_21_out, not_142_out, not_143_out, not_144_out, not_145_out, not_146_out, not_147_out, F5, not_148_out, not_149_out, not_150_out, F1, F0);
  and and_22 (and_22_out, OP5, not_151_out, not_152_out, not_153_out, not_154_out, not_155_out);
  and and_23 (and_23_out, not_156_out, not_157_out, not_158_out, not_159_out, not_160_out, OP0);
  and and_24 (and_24_out, not_161_out, not_162_out, not_163_out, not_164_out, not_165_out, not_166_out, not_167_out, not_168_out, not_169_out, not_170_out, not_171_out, not_172_out);
  and and_25 (and_25_out, not_173_out, not_174_out, not_175_out, not_176_out, not_177_out, not_178_out, not_179_out, not_180_out, not_181_out, not_182_out, F1, F0);
  and and_26 (and_26_out, not_183_out, not_184_out, not_185_out, not_186_out, not_187_out, not_188_out, not_189_out, not_190_out, not_191_out, not_192_out, F1, not_193_out);
  and and_27 (and_27_out, not_194_out, not_195_out, not_196_out, not_197_out, not_198_out, not_199_out, F5, not_200_out, not_201_out, not_202_out, not_203_out, not_204_out);
  and and_28 (and_28_out, not_205_out, not_206_out, not_207_out, not_208_out, not_209_out, not_210_out, F5, not_211_out, not_212_out, not_213_out, not_214_out, F0);
  and and_29 (and_29_out, not_215_out, not_216_out, not_217_out, not_218_out, not_219_out, not_220_out, F5, not_221_out, not_222_out, not_223_out, F1, not_224_out);
  and and_30 (and_30_out, not_225_out, not_226_out, not_227_out, not_228_out, not_229_out, not_230_out, F5, not_231_out, not_232_out, F2, not_233_out, not_234_out);
  and and_31 (and_31_out, not_235_out, not_236_out, not_237_out, not_238_out, not_239_out, not_240_out, F5, not_241_out, not_242_out, F2, not_243_out, F0);
  and and_32 (and_32_out, not_244_out, not_245_out, not_246_out, not_247_out, not_248_out, not_249_out, F5, not_250_out, not_251_out, F2, F1, F0);
  and and_33 (and_33_out, not_252_out, not_253_out, not_254_out, not_255_out, not_256_out, not_257_out, F5, not_258_out, F3, not_259_out, F1, not_260_out);
  and and_34 (and_34_out, not_261_out, not_262_out, not_263_out, not_264_out, not_265_out, not_266_out, F5, not_267_out, F3, not_268_out, F1, F0);
  and and_35 (and_35_out, not_269_out, not_270_out, not_271_out, not_272_out, not_273_out, not_274_out, not_275_out, not_276_out, F3, F2, not_277_out, not_278_out);
  and and_36 (and_36_out, not_279_out, not_280_out, not_281_out, OP2, not_282_out, not_283_out);
  and and_37 (and_37_out, not_284_out, not_285_out, not_286_out, OP2, not_287_out, OP0);
  and and_38 (and_38_out, OP5, not_288_out, OP3, not_289_out, OP1, OP0);
  and and_39 (and_39_out, not_290_out, not_291_out, not_292_out, not_293_out, not_294_out, not_295_out, not_296_out, not_297_out, not_298_out, F2, not_299_out, not_300_out);
  and and_40 (and_40_out, not_301_out, not_302_out, not_303_out, not_304_out, not_305_out, not_306_out, F5, not_307_out, not_308_out, not_309_out, F1, F0);
  or or_1 (R1_Used, and_1_out, and_2_out, and_3_out, and_4_out, and_5_out, and_6_out, and_7_out, and_8_out, and_9_out, and_10_out, and_11_out, and_12_out, and_13_out, and_14_out, and_15_out, and_16_out, and_17_out, and_18_out, and_19_out, and_20_out, and_21_out, and_22_out, and_23_out);
  or or_2 (R2_Used, and_24_out, and_25_out, and_26_out, and_27_out, and_28_out, and_29_out, and_30_out, and_31_out, and_32_out, and_33_out, and_34_out, and_35_out, and_36_out, and_37_out, and_38_out, and_39_out, and_40_out);
endmodule

module \数据相关检测  (
  input  [5:0] OP,
  input  [4:0] EX_WriteReg_num,
  input  EX_RegWrite,
  input  [4:0] MEM_WriteReg_num,
  input  MEM_RegWrite,
  input  [5:0] Func,
  input  [4:0] ID_R1_num,
  input  [4:0] ID_R2_num,
  output \数据相关 
);

  wire and_1_out, and_2_out, and_3_out, and_4_out, and_5_out, and_6_out, comparator_1_eq, comparator_2_eq,
       comparator_3_eq, comparator_4_eq, comparator_5_eq, comparator_6_eq, not_1_out, not_2_out, or_1_out,
       or_2_out, \源寄存器使用情况_1_r1_used , \源寄存器使用情况_1_r2_used ;

  \源寄存器使用情况  \u_源寄存器使用情况_1  (
    .OP0(OP[0]), .OP1(OP[1]), .OP2(OP[2]), .OP3(OP[3]), .OP4(OP[4]), .OP5(OP[5]), .F0(Func[0]), .F1(Func[1]),
    .F2(Func[2]), .F3(Func[3]), .F4(Func[4]), .F5(Func[5]), .R1_Used(\源寄存器使用情况_1_r1_used ),
    .R2_Used(\源寄存器使用情况_1_r2_used ));
  Comparator #(.width(5)) comparator_1 (.a({5{1'b0}}), .b(ID_R1_num), .eq(comparator_1_eq));  // open: gt, lt
  not not_1 (not_1_out, comparator_1_eq);
  Comparator #(.width(5)) comparator_2 (.a({5{1'b0}}), .b(ID_R2_num), .eq(comparator_2_eq));  // open: gt, lt
  not not_2 (not_2_out, comparator_2_eq);
  Comparator #(.width(5)) comparator_3 (.a(ID_R1_num), .b(EX_WriteReg_num), .eq(comparator_3_eq));  // open: gt, lt
  Comparator #(.width(5)) comparator_4 (.a(ID_R1_num), .b(MEM_WriteReg_num), .eq(comparator_4_eq));  // open: gt, lt
  Comparator #(.width(5)) comparator_5 (.a(ID_R2_num), .b(EX_WriteReg_num), .eq(comparator_5_eq));  // open: gt, lt
  Comparator #(.width(5)) comparator_6 (.a(ID_R2_num), .b(MEM_WriteReg_num), .eq(comparator_6_eq));  // open: gt, lt
  or or_1 (or_1_out, and_1_out, and_2_out);
  and and_1 (and_1_out, EX_RegWrite, comparator_3_eq);
  and and_2 (and_2_out, MEM_RegWrite, comparator_4_eq);
  and and_3 (and_3_out, EX_RegWrite, comparator_5_eq);
  and and_4 (and_4_out, MEM_RegWrite, comparator_6_eq);
  and and_5 (and_5_out, not_1_out, or_1_out, \源寄存器使用情况_1_r1_used );
  or or_2 (or_2_out, and_3_out, and_4_out);
  and and_6 (and_6_out, \源寄存器使用情况_1_r2_used , not_2_out, or_2_out);
  or or_3 (\数据相关 , and_5_out, and_6_out);

  // Other names for the same wires on the sheet: OP_CODE[5:0] = OP
endmodule

module IF_ID (
  input  En,
  input  rst,
  input  clk,
  input  [31:0] InstrCode_IN,
  input  [31:0] PC_IN,
  output [31:0] InstrCode_OUT,
  output [31:0] PC_OUT
);

  wire [31:0] multiplexer_1_out, multiplexer_2_out;

  Multiplexer #(.width(32), .enable("false")) multiplexer_1 (
    .in0(InstrCode_IN), .in1({32{1'b0}}), .out(multiplexer_1_out), .sel(rst));
  Multiplexer #(.width(32), .enable("false")) multiplexer_2 (
    .in0(PC_IN), .in1({32{1'b0}}), .out(multiplexer_2_out), .sel(rst));
  Register #(.width(32)) register_1 (.D(multiplexer_1_out), .en(En), .Q(InstrCode_OUT), .clk(clk));  // open: clr
  Register #(.width(32)) register_2 (.D(multiplexer_2_out), .en(En), .Q(PC_OUT), .clk(clk));  // open: clr
endmodule

module ID_EX (
  input  En,
  input  rst,
  input  clk,
  input  JAL_IN,
  input  [31:0] InstrCode_IN,
  input  [31:0] A_IN,
  input  LB_IN,
  input  RegW_IN,
  input  [31:0] PC_IN,
  input  [31:0] B_IN,
  input  RegDst_IN,
  input  syscall_IN,
  input  [31:0] Imm_IN,
  input  R1Equal22_IN,
  input  JMP_IN,
  input  [4:0] W__IN,
  input  JR_IN,
  input  Beq_IN,
  input  Bne_IN,
  input  AluEqual_IN,
  input  BLTZandAR1_IN,
  input  MemW_IN,
  input  [3:0] AluOP_IN,
  input  AluSrc_IN,
  input  BLTZ_IN,
  input  SLLV_IN,
  input  SignedExt_IN,
  input  M2R_IN,
  input  R2F2_IN,
  output JAL_OUT,
  output [31:0] InstrCode_OUT,
  output [31:0] A_OUT,
  output LB_OUT,
  output RegW_OUT,
  output [31:0] PC_OUT,
  output [31:0] B_OUT,
  output RegDst_OUT,
  output syscall_OUT,
  output [31:0] Imm_OUT,
  output R1Equal22_OUT,
  output JMP_OUT,
  output [4:0] W__OUT,
  output JR_OUT,
  output Beq_OUT,
  output Bne_OUT,
  output AluEqual_OUT,
  output BLTZandAR1_OUT,
  output MemW_OUT,
  output [3:0] AluOP_OUT,
  output AluSrc_OUT,
  output BLTZ_OUT,
  output SLLV_OUT,
  output SignedExt_OUT,
  output M2R_OUT,
  output R2F2_OUT
);

  wire multiplexer_3_out, multiplexer_4_out, multiplexer_5_out, multiplexer_6_out, multiplexer_7_out,
       multiplexer_8_out, multiplexer_9_out, multiplexer_10_out, multiplexer_11_out, multiplexer_12_out,
       multiplexer_13_out, multiplexer_14_out, multiplexer_15_out, multiplexer_17_out, multiplexer_18_out,
       multiplexer_19_out, multiplexer_20_out, multiplexer_21_out, multiplexer_22_out;
  wire [3:0] multiplexer_16_out;
  wire [4:0] multiplexer_26_out;
  wire [31:0] multiplexer_1_out, multiplexer_2_out, multiplexer_23_out, multiplexer_24_out,
       multiplexer_25_out;

  Multiplexer #(.width(32), .enable("false")) multiplexer_1 (
    .in0(InstrCode_IN), .in1({32{1'b0}}), .out(multiplexer_1_out), .sel(rst));
  Multiplexer #(.width(32), .enable("false")) multiplexer_2 (
    .in0(PC_IN), .in1({32{1'b0}}), .out(multiplexer_2_out), .sel(rst));
  Register #(.width(32)) register_1 (.D(multiplexer_1_out), .en(En), .Q(InstrCode_OUT), .clk(clk));  // open: clr
  Register #(.width(32)) register_2 (.D(multiplexer_2_out), .en(En), .Q(PC_OUT), .clk(clk));  // open: clr
  Multiplexer #(.enable("false")) multiplexer_3 (.in0(JAL_IN), .in1(1'b0), .out(multiplexer_3_out), .sel(rst));
  Multiplexer #(.enable("false")) multiplexer_4 (.in0(LB_IN), .in1(1'b0), .out(multiplexer_4_out), .sel(rst));
  Multiplexer #(.enable("false")) multiplexer_5 (.in0(RegW_IN), .in1(1'b0), .out(multiplexer_5_out), .sel(rst));
  Multiplexer #(.enable("false")) multiplexer_6 (.in0(RegDst_IN), .in1(1'b0), .out(multiplexer_6_out), .sel(rst));
  Multiplexer #(.enable("false")) multiplexer_7 (.in0(syscall_IN), .in1(1'b0), .out(multiplexer_7_out), .sel(rst));
  Multiplexer #(.enable("false")) multiplexer_8 (.in0(R1Equal22_IN), .in1(1'b0), .out(multiplexer_8_out), .sel(rst));
  Multiplexer #(.enable("false")) multiplexer_9 (.in0(JMP_IN), .in1(1'b0), .out(multiplexer_9_out), .sel(rst));
  Multiplexer #(.enable("false")) multiplexer_10 (.in0(JR_IN), .in1(1'b0), .out(multiplexer_10_out), .sel(rst));
  Multiplexer #(.enable("false")) multiplexer_11 (.in0(Beq_IN), .in1(1'b0), .out(multiplexer_11_out), .sel(rst));
  Multiplexer #(.enable("false")) multiplexer_12 (.in0(Bne_IN), .in1(1'b0), .out(multiplexer_12_out), .sel(rst));
  Multiplexer #(.enable("false")) multiplexer_13 (.in0(AluEqual_IN), .in1(1'b0), .out(multiplexer_13_out), .sel(rst));
  Multiplexer #(.enable("false")) multiplexer_14 (.in0(BLTZandAR1_IN), .in1(1'b0), .out(multiplexer_14_out), .sel(rst));
  Multiplexer #(.enable("false")) multiplexer_15 (.in0(MemW_IN), .in1(1'b0), .out(multiplexer_15_out), .sel(rst));
  Multiplexer #(.width(4), .enable("false")) multiplexer_16 (
    .in0(AluOP_IN), .in1(4'b0000), .out(multiplexer_16_out), .sel(rst));
  Multiplexer #(.enable("false")) multiplexer_17 (.in0(AluSrc_IN), .in1(1'b0), .out(multiplexer_17_out), .sel(rst));
  Multiplexer #(.enable("false")) multiplexer_18 (.in0(BLTZ_IN), .in1(1'b0), .out(multiplexer_18_out), .sel(rst));
  Multiplexer #(.enable("false")) multiplexer_19 (.in0(SLLV_IN), .in1(1'b0), .out(multiplexer_19_out), .sel(rst));
  Multiplexer #(.enable("false")) multiplexer_20 (.in0(SignedExt_IN), .in1(1'b0), .out(multiplexer_20_out), .sel(rst));
  Multiplexer #(.enable("false")) multiplexer_21 (.in0(M2R_IN), .in1(1'b0), .out(multiplexer_21_out), .sel(rst));
  Multiplexer #(.enable("false")) multiplexer_22 (.in0(R2F2_IN), .in1(1'b0), .out(multiplexer_22_out), .sel(rst));
  Register #(.width(1)) register_3 (.D(multiplexer_3_out), .en(En), .Q(JAL_OUT), .clk(clk));  // open: clr
  Register #(.width(1)) register_4 (.D(multiplexer_4_out), .en(En), .Q(LB_OUT), .clk(clk));  // open: clr
  Register #(.width(1)) register_5 (.D(multiplexer_5_out), .en(En), .Q(RegW_OUT), .clk(clk));  // open: clr
  Register #(.width(1)) register_6 (.D(multiplexer_6_out), .en(En), .Q(RegDst_OUT), .clk(clk));  // open: clr
  Register #(.width(1)) register_7 (.D(multiplexer_7_out), .en(En), .Q(syscall_OUT), .clk(clk));  // open: clr
  Register #(.width(1)) register_8 (.D(multiplexer_8_out), .en(En), .Q(R1Equal22_OUT), .clk(clk));  // open: clr
  Register #(.width(1)) register_9 (.D(multiplexer_9_out), .en(En), .Q(JMP_OUT), .clk(clk));  // open: clr
  Register #(.width(1)) register_10 (.D(multiplexer_10_out), .en(En), .Q(JR_OUT), .clk(clk));  // open: clr
  Register #(.width(1)) register_11 (.D(multiplexer_11_out), .en(En), .Q(Beq_OUT), .clk(clk));  // open: clr
  Register #(.width(1)) register_12 (.D(multiplexer_12_out), .en(En), .Q(Bne_OUT), .clk(clk));  // open: clr
  Register #(.width(1)) register_13 (.D(multiplexer_13_out), .en(En), .Q(AluEqual_OUT), .clk(clk));  // open: clr
  Register #(.width(1)) register_14 (.D(multiplexer_14_out), .en(En), .Q(BLTZandAR1_OUT), .clk(clk));  // open: clr
  Register #(.width(1)) register_15 (.D(multiplexer_15_out), .en(En), .Q(MemW_OUT), .clk(clk));  // open: clr
  Register #(.width(4)) register_16 (.D(multiplexer_16_out), .en(En), .Q(AluOP_OUT), .clk(clk));  // open: clr
  Register #(.width(1)) register_17 (.D(multiplexer_17_out), .en(En), .Q(AluSrc_OUT), .clk(clk));  // open: clr
  Register #(.width(1)) register_18 (.D(multiplexer_18_out), .en(En), .Q(BLTZ_OUT), .clk(clk));  // open: clr
  Register #(.width(1)) register_19 (.D(multiplexer_19_out), .en(En), .Q(SLLV_OUT), .clk(clk));  // open: clr
  Register #(.width(1)) register_20 (.D(multiplexer_20_out), .en(En), .Q(SignedExt_OUT), .clk(clk));  // open: clr
  Register #(.width(1)) register_21 (.D(multiplexer_21_out), .en(En), .Q(M2R_OUT), .clk(clk));  // open: clr
  Register #(.width(1)) register_22 (.D(multiplexer_22_out), .en(En), .Q(R2F2_OUT), .clk(clk));  // open: clr
  Multiplexer #(.width(32), .enable("false")) multiplexer_23 (
    .in0(A_IN), .in1({32{1'b0}}), .out(multiplexer_23_out), .sel(rst));
  Register #(.width(32)) register_23 (.D(multiplexer_23_out), .en(En), .Q(A_OUT), .clk(clk));  // open: clr
  Multiplexer #(.width(32), .enable("false")) multiplexer_24 (
    .in0(B_IN), .in1({32{1'b0}}), .out(multiplexer_24_out), .sel(rst));
  Register #(.width(32)) register_24 (.D(multiplexer_24_out), .en(En), .Q(B_OUT), .clk(clk));  // open: clr
  Multiplexer #(.width(32), .enable("false")) multiplexer_25 (
    .in0(Imm_IN), .in1({32{1'b0}}), .out(multiplexer_25_out), .sel(rst));
  Register #(.width(32)) register_25 (.D(multiplexer_25_out), .en(En), .Q(Imm_OUT), .clk(clk));  // open: clr
  Multiplexer #(.width(5), .enable("false")) multiplexer_26 (
    .in0(W__IN), .in1({5{1'b0}}), .out(multiplexer_26_out), .sel(rst));
  Register #(.width(5)) register_26 (.D(multiplexer_26_out), .en(En), .Q(W__OUT), .clk(clk));  // open: clr
endmodule

module EX_MEM (
  input  En,
  input  rst,
  input  clk,
  input  JAL_IN,
  input  [31:0] InstrCode_IN,
  input  [31:0] A_IN,
  input  LB_IN,
  input  RegW_IN,
  input  [31:0] PC_IN,
  input  [31:0] B_IN,
  input  RegDst_IN,
  input  syscall_IN,
  input  [31:0] AluResult_IN,
  input  R1Equal22_IN,
  input  JMP_IN,
  input  [4:0] W__IN,
  input  JR_IN,
  input  Beq_IN,
  input  Bne_IN,
  input  AluEqual_IN,
  input  BLTZandAR1_IN,
  input  MemW_IN,
  input  M2R_IN,
  output JAL_OUT,
  output [31:0] InstrCode_OUT,
  output [31:0] A_OUT,
  output LB_OUT,
  output RegW_OUT,
  output [31:0] PC_OUT,
  output [31:0] B_OUT,
  output RegDst_OUT,
  output syscall_OUT,
  output [31:0] AluResult_OUT,
  output R1Equal22_OUT,
  output JMP_OUT,
  output [4:0] W__OUT,
  output JR_OUT,
  output Beq_OUT,
  output Bne_OUT,
  output AluEqual_OUT,
  output BLTZandAR1_OUT,
  output MemW_OUT,
  output M2R_OUT
);

  wire and_1_out, and_2_out, and_3_out;

  Register #(.width(32)) register_1 (.D(InstrCode_IN), .en(En), .Q(InstrCode_OUT), .clk(clk), .clr(and_1_out));
  Register #(.width(32)) register_2 (.D(PC_IN), .en(En), .Q(PC_OUT), .clk(clk), .clr(and_1_out));
  and and_1 (and_1_out, clk, rst);
  Register #(.width(1)) register_3 (.D(JAL_IN), .en(En), .Q(JAL_OUT), .clk(clk), .clr(and_2_out));
  Register #(.width(1)) register_4 (.D(LB_IN), .en(En), .Q(LB_OUT), .clk(clk), .clr(and_2_out));
  Register #(.width(1)) register_5 (.D(RegW_IN), .en(En), .Q(RegW_OUT), .clk(clk), .clr(and_2_out));
  Register #(.width(1)) register_6 (.D(RegDst_IN), .en(En), .Q(RegDst_OUT), .clk(clk), .clr(and_2_out));
  Register #(.width(1)) register_7 (.D(syscall_IN), .en(En), .Q(syscall_OUT), .clk(clk), .clr(and_2_out));
  Register #(.width(1)) register_8 (.D(R1Equal22_IN), .en(En), .Q(R1Equal22_OUT), .clk(clk), .clr(and_2_out));
  Register #(.width(1)) register_9 (.D(JMP_IN), .en(En), .Q(JMP_OUT), .clk(clk), .clr(and_2_out));
  Register #(.width(1)) register_10 (.D(JR_IN), .en(En), .Q(JR_OUT), .clk(clk), .clr(and_2_out));
  Register #(.width(1)) register_11 (.D(Beq_IN), .en(En), .Q(Beq_OUT), .clk(clk), .clr(and_2_out));
  Register #(.width(1)) register_12 (.D(Bne_IN), .en(En), .Q(Bne_OUT), .clk(clk), .clr(and_2_out));
  Register #(.width(1)) register_13 (.D(AluEqual_IN), .en(En), .Q(AluEqual_OUT), .clk(clk), .clr(and_2_out));
  Register #(.width(1)) register_14 (.D(BLTZandAR1_IN), .en(En), .Q(BLTZandAR1_OUT), .clk(clk), .clr(and_2_out));
  Register #(.width(1)) register_15 (.D(MemW_IN), .en(En), .Q(MemW_OUT), .clk(clk), .clr(and_2_out));
  Register #(.width(1)) register_16 (.D(M2R_IN), .en(En), .Q(M2R_OUT), .clk(clk), .clr(and_2_out));
  and and_2 (and_2_out, clk, rst);
  Register #(.width(32)) register_17 (.D(A_IN), .en(En), .Q(A_OUT), .clk(clk), .clr(and_3_out));
  Register #(.width(32)) register_18 (.D(B_IN), .en(En), .Q(B_OUT), .clk(clk), .clr(and_3_out));
  Register #(.width(32)) register_19 (.D(AluResult_IN), .en(En), .Q(AluResult_OUT), .clk(clk), .clr(and_3_out));
  Register #(.width(5)) register_20 (.D(W__IN), .en(En), .Q(W__OUT), .clk(clk), .clr(and_3_out));
  and and_3 (and_3_out, clk, rst);
endmodule

module MEM_WB (
  input  En,
  input  rst,
  input  clk,
  input  JAL_IN,
  input  [31:0] InstrCode_IN,
  input  [31:0] A_IN,
  input  LB_IN,
  input  RegW_IN,
  input  [31:0] PC_IN,
  input  [31:0] MD_IN,
  input  RegDst_IN,
  input  syscall_IN,
  input  [31:0] AluResult_IN,
  input  R1Equal22_IN,
  input  JMP_IN,
  input  JR_IN,
  input  [31:0] B_IN,
  input  Beq_IN,
  input  Bne_IN,
  input  [4:0] W__IN,
  input  AluEqual_IN,
  input  BLTZandAR1_IN,
  input  M2R_IN,
  output JAL_OUT,
  output [31:0] InstrCode_OUT,
  output [31:0] A_OUT,
  output LB_OUT,
  output RegW_OUT,
  output [31:0] PC_OUT,
  output [31:0] MD_OUT,
  output RegDst_OUT,
  output syscall_OUT,
  output [31:0] AluResult_OUT,
  output R1Equal22_OUT,
  output JMP_OUT,
  output JR_OUT,
  output [31:0] B_OUT,
  output Beq_OUT,
  output Bne_OUT,
  output [4:0] W__OUT,
  output AluEqual_OUT,
  output BLTZandAR1_OUT,
  output M2R_OUT
);

  wire and_1_out, and_2_out, and_3_out;

  Register #(.width(32)) register_1 (.D(InstrCode_IN), .en(En), .Q(InstrCode_OUT), .clk(clk), .clr(and_1_out));
  Register #(.width(32)) register_2 (.D(PC_IN), .en(En), .Q(PC_OUT), .clk(clk), .clr(and_1_out));
  and and_1 (and_1_out, clk, rst);
  Register #(.width(1)) register_3 (.D(JAL_IN), .en(En), .Q(JAL_OUT), .clk(clk), .clr(and_2_out));
  Register #(.width(1)) register_4 (.D(LB_IN), .en(En), .Q(LB_OUT), .clk(clk), .clr(and_2_out));
  Register #(.width(1)) register_5 (.D(RegW_IN), .en(En), .Q(RegW_OUT), .clk(clk), .clr(and_2_out));
  Register #(.width(1)) register_6 (.D(RegDst_IN), .en(En), .Q(RegDst_OUT), .clk(clk), .clr(and_2_out));
  Register #(.width(1)) register_7 (.D(syscall_IN), .en(En), .Q(syscall_OUT), .clk(clk), .clr(and_2_out));
  Register #(.width(1)) register_8 (.D(R1Equal22_IN), .en(En), .Q(R1Equal22_OUT), .clk(clk), .clr(and_2_out));
  Register #(.width(1)) register_9 (.D(JMP_IN), .en(En), .Q(JMP_OUT), .clk(clk), .clr(and_2_out));
  Register #(.width(1)) register_10 (.D(JR_IN), .en(En), .Q(JR_OUT), .clk(clk), .clr(and_2_out));
  Register #(.width(1)) register_11 (.D(Beq_IN), .en(En), .Q(Beq_OUT), .clk(clk), .clr(and_2_out));
  Register #(.width(1)) register_12 (.D(Bne_IN), .en(En), .Q(Bne_OUT), .clk(clk), .clr(and_2_out));
  Register #(.width(1)) register_13 (.D(AluEqual_IN), .en(En), .Q(AluEqual_OUT), .clk(clk), .clr(and_2_out));
  Register #(.width(1)) register_14 (.D(BLTZandAR1_IN), .en(En), .Q(BLTZandAR1_OUT), .clk(clk), .clr(and_2_out));
  Register #(.width(1)) register_15 (.D(M2R_IN), .en(En), .Q(M2R_OUT), .clk(clk), .clr(and_2_out));
  and and_2 (and_2_out, clk, rst);
  Register #(.width(32)) register_16 (.D(A_IN), .en(En), .Q(A_OUT), .clk(clk), .clr(and_3_out));
  Register #(.width(32)) register_17 (.D(MD_IN), .en(En), .Q(MD_OUT), .clk(clk), .clr(and_3_out));
  Register #(.width(32)) register_18 (.D(AluResult_IN), .en(En), .Q(AluResult_OUT), .clk(clk), .clr(and_3_out));
  Register #(.width(32)) register_19 (.D(B_IN), .en(En), .Q(B_OUT), .clk(clk), .clr(and_3_out));
  Register #(.width(5)) register_20 (.D(W__IN), .en(En), .Q(W__OUT), .clk(clk), .clr(and_3_out));
  and and_3 (and_3_out, clk, rst);
endmodule

module \分支相关流水线  (
);

  wire and_1_out, and_2_out, and_3_out, and_4_out, and_5_out, and_6_out, and_7_out, CLK, comparator_1_eq,
       comparator_2_eq, ex_mem_1_aluequal_out, ex_mem_1_beq_out, ex_mem_1_bltzandar1_out, ex_mem_1_bne_out,
       ex_mem_1_jal_out, ex_mem_1_jmp_out, ex_mem_1_jr_out, ex_mem_1_lb_out, ex_mem_1_m2r_out,
       ex_mem_1_memw_out, ex_mem_1_r1equal22_out, ex_mem_1_regdst_out, ex_mem_1_regw_out,
       ex_mem_1_syscall_out, Go, id_ex_1_alusrc_out, id_ex_1_beq_out, id_ex_1_bltz_out, id_ex_1_bne_out,
       id_ex_1_jal_out, id_ex_1_jmp_out, id_ex_1_jr_out, id_ex_1_lb_out, id_ex_1_m2r_out, id_ex_1_memw_out,
       id_ex_1_r1equal22_out, id_ex_1_regdst_out, id_ex_1_regw_out, id_ex_1_sllv_out, id_ex_1_syscall_out,
       IR1, IR2, IR3, mem_wb_1_jal_out, mem_wb_1_lb_out, mem_wb_1_m2r_out, mem_wb_1_regw_out,
       mips_alu_1_equal, not_1_out, not_2_out, not_3_out, or_1_out, or_2_out, or_3_out, or_4_out, or_5_out,
       or_6_out, or_7_out, or_8_out, R1E22_4, RST, SignedExt, SYSCALL_4, W1, W2, W3, \硬布线控制器_1_alu_src ,
       \硬布线控制器_1_beq , \硬布线控制器_1_bltz , \硬布线控制器_1_bne , \硬布线控制器_1_jal , \硬布线控制器_1_jmp , \硬布线控制器_1_jr ,
       \硬布线控制器_1_lb , \硬布线控制器_1_memtoreg , \硬布线控制器_1_memwrite , \硬布线控制器_1_regdst , \硬布线控制器_1_regwrite ,
       \硬布线控制器_1_sllv , \硬布线控制器_1_syscall ;
  wire [3:0] id_ex_1_aluop_out, \硬布线控制器_1_alu_op ;
  wire [4:0] ex_mem_1_w__out, id_ex_1_a_out, id_ex_1_w__out, mem_wb_1_w__out, multiplexer_4_out,
       multiplexer_5_out, multiplexer_6_out, multiplexer_7_out, multiplexer_11_out;
  wire [7:0] multiplexer_13_out;
  wire [11:0] EX_PC, ID_PC, IF_PC, MEM_PC, WB_PC;
  wire [15:0] id_ex_1_instrcode_out, \LoadUse次数 , \总周期数 , \插入气泡数 , \无条件分支数 , \条件分支成功数 ;
  wire [27:0] PC_q;
  wire [31:0] adder_1_out, adder_2_out, adder_3_out, adder_4_out, bit_extender_1_out, bit_extender_2_out,
       bit_extender_3_out, bit_extender_4_out, ex_mem_1_a_out, ex_mem_1_aluresult_out, ex_mem_1_b_out,
       ex_mem_1_instrcode_out, ex_mem_1_pc_out, id_ex_1_b_out, id_ex_1_imm_out, id_ex_1_pc_out,
       if_id_1_instrcode_out, if_id_1_pc_out, LedData, mem_wb_1_a_out, mem_wb_1_aluresult_out,
       mem_wb_1_md_out, mem_wb_1_pc_out, mips_alu_1_result, mips_regifile_1_r1, mips_regifile_1_r2,
       multiplexer_1_out, multiplexer_2_out, multiplexer_3_out, multiplexer_8_out, multiplexer_9_out,
       multiplexer_10_out, multiplexer_12_out, multiplexer_14_out, multiplexer_15_out, ram_1_data,
       rom_1_data, shifter_1_out;
  wire [31:5] id_ex_1_a_out_2;
  wire [31:16] id_ex_1_instrcode_out_2;
  wire [31:28] PC_q_2;

  Button \u_总复位  (.out(RST));
  Button _1 (.out(IR1));
  Button _2 (.out(IR2));
  Button _3 (.out(IR3));
  Button \u_继续运行  (.out(Go));
  LED led_1 (.in(W1));
  LED led_2 (.in(W2));
  LED led_3 (.in(W3));
  Multiplexer #(.width(32), .enable("false")) multiplexer_1 (
    .in0(adder_1_out), .in1(adder_3_out), .out(multiplexer_1_out), .sel(or_8_out));
  Multiplexer #(.width(32), .enable("false")) multiplexer_2 (
    .in0(multiplexer_1_out), .in1({id_ex_1_a_out_2, id_ex_1_a_out}), .out(multiplexer_2_out),
    .sel(id_ex_1_jr_out));
  Hex_Digit_Display hex_digit_display_1 (.value(LedData[31:28]));  // open: dp
  or or_1 (or_1_out, or_3_out, not_1_out);
  or or_2 (or_2_out, id_ex_1_jmp_out, id_ex_1_jal_out);
  Multiplexer #(.width(32), .enable("false")) multiplexer_3 (
    .in0(multiplexer_2_out), .in1({PC_q_2, id_ex_1_instrcode_out_2[25:16], id_ex_1_instrcode_out, 2'b00}),
    .out(multiplexer_3_out), .sel(or_2_out));
  Hex_Digit_Display hex_digit_display_2 (.value(LedData[27:24]));  // open: dp
  Hex_Digit_Display hex_digit_display_3 (.value(LedData[23:20]));  // open: dp
  not not_1 (not_1_out, id_ex_1_syscall_out);
  or or_3 (or_3_out, and_1_out, Go);
  not not_2 (not_2_out, SYSCALL_4);
  or or_4 (or_4_out, and_2_out, Go);
  or or_5 (or_5_out, not_2_out, or_4_out);
  Register #(.width(32)) PC (.D(multiplexer_3_out), .en(or_1_out), .Q({PC_q_2, PC_q}), .clk(CLK), .clr(RST));
  Hex_Digit_Display hex_digit_display_4 (.value(LedData[15:12]));  // open: dp
  Hex_Digit_Display hex_digit_display_5 (.value(LedData[19:16]));  // open: dp
  and and_1 (and_1_out, id_ex_1_syscall_out, id_ex_1_r1equal22_out);
  and and_2 (and_2_out, SYSCALL_4, R1E22_4);
  Adder #(.width(32)) adder_1 (.a({PC_q_2, PC_q}), .b(32'h4), .out(adder_1_out));  // open: cin, cout
  Hex_Digit_Display hex_digit_display_6 (.value(LedData[11:8]));  // open: dp
  Hex_Digit_Display hex_digit_display_7 (.value(LedData[7:4]));  // open: dp
  Clock clock_1 (.out(CLK));
  Counter #(.width(16), .max('hffff)) counter_1 (
    .count(or_5_out), .Q(\总周期数 ), .clk(CLK), .clr(RST));  // open: load, D, carry
  ROM #(.addrWidth(10), .dataWidth(32)) rom_1 (.addr(PC_q[11:2]), .data(rom_1_data));  // open: sel
  Hex_Digit_Display hex_digit_display_8 (.value(LedData[3:0]));  // open: dp
  IF_ID if_id_1 (
    .rst(or_6_out), .clk(CLK), .InstrCode_IN(rom_1_data), .PC_IN({PC_q_2, PC_q}),
    .InstrCode_OUT(if_id_1_instrcode_out), .PC_OUT(if_id_1_pc_out), .En(or_1_out));
  Adder #(.width(32)) adder_2 (.a(32'h4), .b(id_ex_1_pc_out), .out(adder_2_out));  // open: cin, cout
  // Probe on \总周期数 
  // Probe on \无条件分支数 
  // Probe on \条件分支成功数 
  // Probe on \插入气泡数 
  // Probe on \LoadUse次数 
  Adder #(.width(32)) adder_3 (.a(adder_2_out), .b(shifter_1_out), .out(adder_3_out));  // open: cin, cout
  // Probe on IF_PC
  // Probe on ID_PC
  \硬布线控制器  \u_硬布线控制器_1  (
    .OP(if_id_1_instrcode_out[31:26]), .Func(if_id_1_instrcode_out[5:0]), .ALU_OP(\硬布线控制器_1_alu_op ),
    .MemToReg(\硬布线控制器_1_memtoreg ), .MemWrite(\硬布线控制器_1_memwrite ), .ALU_SRC(\硬布线控制器_1_alu_src ),
    .RegWrite(\硬布线控制器_1_regwrite ), .SysCALL(\硬布线控制器_1_syscall ), .SignedExt(SignedExt),
    .RegDst(\硬布线控制器_1_regdst ), .Beq(\硬布线控制器_1_beq ), .Bne(\硬布线控制器_1_bne ), .JR(\硬布线控制器_1_jr ),
    .JMP(\硬布线控制器_1_jmp ), .JAL(\硬布线控制器_1_jal ), .SLLV(\硬布线控制器_1_sllv ), .LB(\硬布线控制器_1_lb ),
    .BLTZ(\硬布线控制器_1_bltz ));  // open: MFC0, MTC0, ERET, RS
  Multiplexer #(.width(5), .enable("false")) multiplexer_4 (
    .in0(if_id_1_instrcode_out[20:16]), .in1(if_id_1_instrcode_out[15:11]), .out(multiplexer_4_out),
    .sel(\硬布线控制器_1_regdst ));
  Multiplexer #(.width(5), .enable("false")) multiplexer_5 (
    .in0(multiplexer_4_out), .in1({5{1'b1}}), .out(multiplexer_5_out), .sel(\硬布线控制器_1_jal ));
  assign bit_extender_1_out = {{16{1'b0}}, if_id_1_instrcode_out[15:0]};  // Bit_Extender bit_extender_1
  assign bit_extender_2_out = {{16{if_id_1_instrcode_out[15]}}, if_id_1_instrcode_out[15:0]};  // Bit_Extender bit_extender_2
  // Probe on MEM_PC
  // Probe on EX_PC
  Multiplexer #(.width(5), .enable("false")) multiplexer_6 (
    .in0(if_id_1_instrcode_out[25:21]), .in1(5'b00010), .out(multiplexer_6_out), .sel(\硬布线控制器_1_syscall ));
  and and_3 (and_3_out, \硬布线控制器_1_syscall , comparator_1_eq);
  Multiplexer #(.width(5), .enable("false")) multiplexer_7 (
    .in0(if_id_1_instrcode_out[20:16]), .in1(5'b00100), .out(multiplexer_7_out), .sel(and_3_out));
  // Probe on WB_PC
  Multiplexer #(.width(32), .enable("false")) multiplexer_8 (
    .in0(bit_extender_1_out), .in1(bit_extender_2_out), .out(multiplexer_8_out), .sel(SignedExt));
  Shifter #(.width(32)) shifter_1 (.in(bit_extender_3_out), .\dist (5'b00010), .out(shifter_1_out));
  MIPS_Regifile mips_regifile_1 (
    .Din(multiplexer_15_out), .Clk(CLK), .R1(mips_regifile_1_r1), .R2(mips_regifile_1_r2),
    .WE(mem_wb_1_regw_out), .W_num(mem_wb_1_w__out), .R1_num(multiplexer_6_out), .R2_num(multiplexer_7_out));
  Comparator #(.width(32)) comparator_1 (.a(32'h22), .b(mips_regifile_1_r1), .eq(comparator_1_eq));  // open: gt, lt
  or or_6 (or_6_out, or_7_out, or_8_out);
  ID_EX id_ex_1 (
    .rst(or_6_out), .clk(CLK), .JAL_IN(\硬布线控制器_1_jal ), .InstrCode_IN(if_id_1_instrcode_out),
    .A_IN(mips_regifile_1_r1), .LB_IN(\硬布线控制器_1_lb ), .RegW_IN(\硬布线控制器_1_regwrite ), .PC_IN(if_id_1_pc_out),
    .B_IN(mips_regifile_1_r2), .RegDst_IN(\硬布线控制器_1_regdst ), .syscall_IN(\硬布线控制器_1_syscall ),
    .Imm_IN(multiplexer_8_out), .R1Equal22_IN(comparator_1_eq), .JMP_IN(\硬布线控制器_1_jmp ),
    .JR_IN(\硬布线控制器_1_jr ), .Beq_IN(\硬布线控制器_1_beq ), .Bne_IN(\硬布线控制器_1_bne ), .MemW_IN(\硬布线控制器_1_memwrite ),
    .AluOP_IN(\硬布线控制器_1_alu_op ), .AluSrc_IN(\硬布线控制器_1_alu_src ), .BLTZ_IN(\硬布线控制器_1_bltz ),
    .SLLV_IN(\硬布线控制器_1_sllv ), .JAL_OUT(id_ex_1_jal_out),
    .InstrCode_OUT({id_ex_1_instrcode_out_2, id_ex_1_instrcode_out}),
    .A_OUT({id_ex_1_a_out_2, id_ex_1_a_out}), .LB_OUT(id_ex_1_lb_out), .RegW_OUT(id_ex_1_regw_out),
    .PC_OUT(id_ex_1_pc_out), .B_OUT(id_ex_1_b_out), .RegDst_OUT(id_ex_1_regdst_out),
    .syscall_OUT(id_ex_1_syscall_out), .Imm_OUT(id_ex_1_imm_out), .R1Equal22_OUT(id_ex_1_r1equal22_out),
    .JMP_OUT(id_ex_1_jmp_out), .JR_OUT(id_ex_1_jr_out), .Beq_OUT(id_ex_1_beq_out), .Bne_OUT(id_ex_1_bne_out),
    .MemW_OUT(id_ex_1_memw_out), .AluOP_OUT(id_ex_1_aluop_out), .AluSrc_OUT(id_ex_1_alusrc_out),
    .BLTZ_OUT(id_ex_1_bltz_out), .SLLV_OUT(id_ex_1_sllv_out), .M2R_IN(\硬布线控制器_1_memtoreg ),
    .M2R_OUT(id_ex_1_m2r_out), .W__IN(multiplexer_5_out), .W__OUT(id_ex_1_w__out), .En(or_1_out));  // open: AluEqual_IN, BLTZandAR1_IN, SignedExt_IN, AluEqual_OUT, BLTZandAR1_OUT, SignedExt_OUT, R2F2_IN, R2F2_OUT
  assign bit_extender_3_out = {{16{id_ex_1_instrcode_out[15]}}, id_ex_1_instrcode_out};  // Bit_Extender bit_extender_3
  Multiplexer #(.width(32), .enable("false")) multiplexer_9 (
    .in0(id_ex_1_b_out), .in1(id_ex_1_imm_out), .out(multiplexer_9_out), .sel(id_ex_1_alusrc_out));
  Multiplexer #(.width(32), .enable("false")) multiplexer_10 (
    .in0(multiplexer_9_out), .in1({32{1'b0}}), .out(multiplexer_10_out), .sel(id_ex_1_bltz_out));
  MIPS_ALU mips_alu_1 (
    .X({id_ex_1_a_out_2, id_ex_1_a_out}), .Y(multiplexer_10_out), .AluOP(id_ex_1_aluop_out),
    .Equal(mips_alu_1_equal), .Result(mips_alu_1_result), .shamt(multiplexer_11_out));  // open: Result_2
  Multiplexer #(.width(5), .enable("false")) multiplexer_11 (
    .in0(id_ex_1_instrcode_out[10:6]), .in1(id_ex_1_a_out), .out(multiplexer_11_out), .sel(id_ex_1_sllv_out));
  Comparator #(.width(32)) comparator_2 (.a(mips_alu_1_result), .b(32'h1), .eq(comparator_2_eq));  // open: gt, lt
  and and_4 (and_4_out, comparator_2_eq, id_ex_1_bltz_out);
  EX_MEM ex_mem_1 (
    .rst(RST), .clk(CLK), .JAL_IN(id_ex_1_jal_out),
    .InstrCode_IN({id_ex_1_instrcode_out_2, id_ex_1_instrcode_out}), .LB_IN(id_ex_1_lb_out),
    .RegW_IN(id_ex_1_regw_out), .PC_IN(id_ex_1_pc_out), .B_IN(id_ex_1_b_out), .RegDst_IN(id_ex_1_regdst_out),
    .syscall_IN(id_ex_1_syscall_out), .AluResult_IN(mips_alu_1_result), .R1Equal22_IN(id_ex_1_r1equal22_out),
    .JMP_IN(id_ex_1_jmp_out), .JR_IN(id_ex_1_jr_out), .Beq_IN(id_ex_1_beq_out), .Bne_IN(id_ex_1_bne_out),
    .AluEqual_IN(mips_alu_1_equal), .BLTZandAR1_IN(and_4_out), .MemW_IN(id_ex_1_memw_out),
    .JAL_OUT(ex_mem_1_jal_out), .InstrCode_OUT(ex_mem_1_instrcode_out), .LB_OUT(ex_mem_1_lb_out),
    .RegW_OUT(ex_mem_1_regw_out), .PC_OUT(ex_mem_1_pc_out), .B_OUT(ex_mem_1_b_out),
    .RegDst_OUT(ex_mem_1_regdst_out), .syscall_OUT(ex_mem_1_syscall_out),
    .AluResult_OUT(ex_mem_1_aluresult_out), .R1Equal22_OUT(ex_mem_1_r1equal22_out),
    .JMP_OUT(ex_mem_1_jmp_out), .JR_OUT(ex_mem_1_jr_out), .Beq_OUT(ex_mem_1_beq_out),
    .Bne_OUT(ex_mem_1_bne_out), .AluEqual_OUT(ex_mem_1_aluequal_out),
    .BLTZandAR1_OUT(ex_mem_1_bltzandar1_out), .MemW_OUT(ex_mem_1_memw_out),
    .A_IN({id_ex_1_a_out_2, id_ex_1_a_out}), .A_OUT(ex_mem_1_a_out), .M2R_IN(id_ex_1_m2r_out),
    .M2R_OUT(ex_mem_1_m2r_out), .W__IN(id_ex_1_w__out), .W__OUT(ex_mem_1_w__out));  // open: En
  // Probe on ex_mem_1_b_out
  RAM #(.addrWidth(10), .dataWidth(32), .bus("separate")) ram_1 (
    .addr(ex_mem_1_aluresult_out[11:2]), .din(ex_mem_1_b_out), .data(ram_1_data), .str(ex_mem_1_memw_out),
    .clk(CLK), .clr(RST));  // open: sel, ld
  MEM_WB mem_wb_1 (
    .rst(RST), .clk(CLK), .JAL_IN(ex_mem_1_jal_out), .InstrCode_IN(ex_mem_1_instrcode_out),
    .LB_IN(ex_mem_1_lb_out), .RegW_IN(ex_mem_1_regw_out), .PC_IN(ex_mem_1_pc_out), .MD_IN(ram_1_data),
    .RegDst_IN(ex_mem_1_regdst_out), .syscall_IN(ex_mem_1_syscall_out),
    .AluResult_IN(ex_mem_1_aluresult_out), .R1Equal22_IN(ex_mem_1_r1equal22_out), .JMP_IN(ex_mem_1_jmp_out),
    .JR_IN(ex_mem_1_jr_out), .Beq_IN(ex_mem_1_beq_out), .Bne_IN(ex_mem_1_bne_out),
    .AluEqual_IN(ex_mem_1_aluequal_out), .BLTZandAR1_IN(ex_mem_1_bltzandar1_out), .JAL_OUT(mem_wb_1_jal_out),
    .LB_OUT(mem_wb_1_lb_out), .RegW_OUT(mem_wb_1_regw_out), .PC_OUT(mem_wb_1_pc_out),
    .MD_OUT(mem_wb_1_md_out), .syscall_OUT(SYSCALL_4), .AluResult_OUT(mem_wb_1_aluresult_out),
    .R1Equal22_OUT(R1E22_4), .A_IN(ex_mem_1_a_out), .A_OUT(mem_wb_1_a_out), .B_IN(ex_mem_1_b_out),
    .M2R_IN(ex_mem_1_m2r_out), .M2R_OUT(mem_wb_1_m2r_out), .W__IN(ex_mem_1_w__out), .W__OUT(mem_wb_1_w__out));  // open: InstrCode_OUT, RegDst_OUT, JMP_OUT, JR_OUT, Beq_OUT, Bne_OUT, AluEqual_OUT, BLTZandAR1_OUT, B_OUT, En
  Multiplexer #(.width(32), .enable("false")) multiplexer_12 (
    .in0(mem_wb_1_aluresult_out), .in1(mem_wb_1_md_out), .out(multiplexer_12_out), .sel(mem_wb_1_m2r_out));
  not not_3 (not_3_out, mips_alu_1_equal);
  or or_7 (or_7_out, id_ex_1_jal_out, id_ex_1_jmp_out, id_ex_1_jr_out);
  and and_5 (and_5_out, id_ex_1_beq_out, mips_alu_1_equal);
  and and_6 (and_6_out, id_ex_1_bne_out, not_3_out);
  and and_7 (and_7_out, id_ex_1_r1equal22_out, id_ex_1_syscall_out);
  // Probe on id_ex_1_b_out
  Multiplexer #(.select(2), .width(8), .enable("false")) multiplexer_13 (
    .in0(multiplexer_12_out[7:0]), .in1(multiplexer_12_out[15:8]), .in2(multiplexer_12_out[23:16]),
    .in3(multiplexer_12_out[31:24]), .out(multiplexer_13_out), .sel(mem_wb_1_aluresult_out[1:0]));
  Counter #(.width(16), .max('hffff)) counter_2 (
    .count(or_7_out), .Q(\无条件分支数 ), .clk(CLK), .clr(RST));  // open: load, D, carry
  or or_8 (or_8_out, and_5_out, and_4_out, and_6_out);
  Register #(.width(32)) register_1 (.D(id_ex_1_b_out), .en(and_7_out), .Q(LedData), .clk(CLK), .clr(RST));
  Adder #(.width(32)) adder_4 (.a(mem_wb_1_pc_out), .b(32'h4), .out(adder_4_out));  // open: cin, cout
  Multiplexer #(.width(32), .enable("false")) multiplexer_14 (
    .in0(multiplexer_12_out), .in1(adder_4_out), .out(multiplexer_14_out), .sel(mem_wb_1_jal_out));
  assign bit_extender_4_out = {{24{multiplexer_13_out[7]}}, multiplexer_13_out};  // Bit_Extender bit_extender_4
  Counter #(.width(16), .max('hffff)) counter_3 (
    .count(or_8_out), .Q(\条件分支成功数 ), .clk(CLK), .clr(RST));  // open: load, D, carry
  Multiplexer #(.width(32), .enable("false")) multiplexer_15 (
    .in0(multiplexer_14_out), .in1(bit_extender_4_out), .out(multiplexer_15_out), .sel(mem_wb_1_lb_out));

  // Notes on the sheet:
  //   中断源
  //   中断等待指示
  //   数码管输出
  //   指令存储器
  //   contents of rom_1 (hex, n*v repeats v):
  //   20110020 20020022 8000c06 20110000 20110000 2002000a 10000003 20110000 20110000 2002000a 14110003
  //   20110000 20110000 2002000a c000c14 2002000a 0 0 0 c 2231ffff 0 0 0 112020 0 0 0 c 1620fff6 3e00008
  //   Op
  //   Func
  //   Beq
  //   Bne
  //   MemToReg
  //   MemWrite
  //   AluOP
  //   AluSrcB
  //   RegWrite
  //   RegDst
  //   流水调试日志用
endmodule

module \气泡流水线  (
);

  wire and_1_out, and_2_out, and_3_out, and_4_out, and_5_out, and_6_out, and_7_out, and_8_out, CLK,
       comparator_1_eq, comparator_2_eq, DATA_DETC, ex_mem_1_aluequal_out, ex_mem_1_beq_out,
       ex_mem_1_bltzandar1_out, ex_mem_1_bne_out, ex_mem_1_jal_out, ex_mem_1_jmp_out, ex_mem_1_jr_out,
       ex_mem_1_lb_out, ex_mem_1_m2r_out, ex_mem_1_memw_out, ex_mem_1_r1equal22_out, ex_mem_1_regdst_out,
       ex_mem_1_syscall_out, EX_RW, Go, id_ex_1_alusrc_out, id_ex_1_beq_out, id_ex_1_bltz_out,
       id_ex_1_bne_out, id_ex_1_jal_out, id_ex_1_jmp_out, id_ex_1_jr_out, id_ex_1_lb_out, id_ex_1_m2r_out,
       id_ex_1_memw_out, id_ex_1_r1equal22_out, id_ex_1_regdst_out, id_ex_1_sllv_out, id_ex_1_syscall_out,
       IR1, IR2, IR3, MEM_RW, mem_wb_1_jal_out, mem_wb_1_lb_out, mem_wb_1_m2r_out, mem_wb_1_regw_out,
       mips_alu_1_equal, not_1_out, not_2_out, not_3_out, or_1_out, or_2_out, or_3_out, or_4_out, or_5_out,
       or_6_out, or_7_out, or_8_out, or_9_out, R1E22_4, RST, SignedExt, SYSCALL_4, W1, W2, W3,
       \硬布线控制器_1_alu_src , \硬布线控制器_1_beq , \硬布线控制器_1_bltz , \硬布线控制器_1_bne , \硬布线控制器_1_jal , \硬布线控制器_1_jmp ,
       \硬布线控制器_1_jr , \硬布线控制器_1_lb , \硬布线控制器_1_memtoreg , \硬布线控制器_1_memwrite , \硬布线控制器_1_regdst ,
       \硬布线控制器_1_regwrite , \硬布线控制器_1_sllv , \硬布线控制器_1_syscall ;
  wire [3:0] id_ex_1_aluop_out, \硬布线控制器_1_alu_op ;
  wire [4:0] EX_WR_num, id_ex_1_a_out, mem_wb_1_w__out, MEM_WR_num, multiplexer_4_out, multiplexer_5_out,
       multiplexer_6_out, multiplexer_7_out, multiplexer_11_out;
  wire [5:0] if_id_1_instrcode_out_2;
  wire [7:0] multiplexer_13_out;
  wire [15:0] \LoadUse次数 , \总周期数 , \插入气泡数 , \无条件分支数 , \条件分支成功数 ;
  wire [25:0] if_id_1_instrcode_out;
  wire [31:0] adder_1_out, adder_2_out, adder_3_out, adder_4_out, bit_extender_1_out, bit_extender_2_out,
       bit_extender_3_out, bit_extender_4_out, ex_mem_1_a_out, ex_mem_1_aluresult_out, ex_mem_1_b_out,
       ex_mem_1_instrcode_out, EX_PC, id_ex_1_b_out, id_ex_1_imm_out, id_ex_1_instrcode_out, ID_PC, IF_PC,
       LedData, MEM_PC, mem_wb_1_a_out, mem_wb_1_aluresult_out, mem_wb_1_md_out, mips_alu_1_result,
       mips_regifile_1_r1, mips_regifile_1_r2, multiplexer_1_out, multiplexer_2_out, multiplexer_3_out,
       multiplexer_8_out, multiplexer_9_out, multiplexer_10_out, multiplexer_12_out, multiplexer_14_out,
       multiplexer_15_out, ram_1_data, rom_2_data, shifter_1_out, WB_PC;
  wire [31:5] id_ex_1_a_out_2;

  Button \u_总复位  (.out(RST));
  Button _1 (.out(IR1));
  Button _2 (.out(IR2));
  Button _3 (.out(IR3));
  Button \u_继续运行  (.out(Go));
  LED led_1 (.in(W1));
  LED led_2 (.in(W2));
  LED led_3 (.in(W3));
  Multiplexer #(.width(32), .enable("false")) multiplexer_1 (
    .in0(adder_1_out), .in1(adder_3_out), .out(multiplexer_1_out), .sel(or_9_out));
  Multiplexer #(.width(32), .enable("false")) multiplexer_2 (
    .in0(multiplexer_1_out), .in1({id_ex_1_a_out_2, id_ex_1_a_out}), .out(multiplexer_2_out),
    .sel(id_ex_1_jr_out));
  // Probe on {EX_PC[31:28], id_ex_1_instrcode_out[25:0], 2'b00}
  Hex_Digit_Display hex_digit_display_1 (.value(LedData[31:28]));  // open: dp
  or or_1 (or_1_out, or_3_out, not_1_out);
  or or_2 (or_2_out, id_ex_1_jmp_out, id_ex_1_jal_out);
  Multiplexer #(.width(32), .enable("false")) multiplexer_3 (
    .in0(multiplexer_2_out), .in1({EX_PC[31:28], id_ex_1_instrcode_out[25:0], 2'b00}),
    .out(multiplexer_3_out), .sel(or_2_out));
  Hex_Digit_Display hex_digit_display_2 (.value(LedData[23:20]));  // open: dp
  Hex_Digit_Display hex_digit_display_3 (.value(LedData[27:24]));  // open: dp
  not not_1 (not_1_out, id_ex_1_syscall_out);
  or or_3 (or_3_out, and_1_out, Go);
  not not_2 (not_2_out, SYSCALL_4);
  or or_4 (or_4_out, and_2_out, Go);
  or or_5 (or_5_out, not_2_out, or_4_out);
  Register #(.width(32)) PC (.D(multiplexer_3_out), .en(and_3_out), .Q(IF_PC), .clk(CLK), .clr(RST));
  Hex_Digit_Display hex_digit_display_4 (.value(LedData[15:12]));  // open: dp
  Hex_Digit_Display hex_digit_display_5 (.value(LedData[19:16]));  // open: dp
  ROM #(.addrWidth(10), .dataWidth(32)) rom_1 ();  // open: addr, data, sel
  and and_1 (and_1_out, id_ex_1_syscall_out, id_ex_1_r1equal22_out);
  and and_2 (and_2_out, SYSCALL_4, R1E22_4);
  // Probe on id_ex_1_instrcode_out[25:0]
  Adder #(.width(32)) adder_1 (.a(IF_PC), .b(32'h4), .out(adder_1_out));  // open: cin, cout
  Hex_Digit_Display hex_digit_display_6 (.value(LedData[11:8]));  // open: dp
  Hex_Digit_Display hex_digit_display_7 (.value(LedData[7:4]));  // open: dp
  Clock clock_1 (.out(CLK));
  Counter #(.width(16), .max('hffff)) counter_1 (
    .count(or_5_out), .Q(\总周期数 ), .clk(CLK), .clr(RST));  // open: load, D, carry
  ROM #(.addrWidth(10), .dataWidth(32)) rom_2 (.addr(IF_PC[11:2]), .data(rom_2_data));  // open: sel
  // Probe on id_ex_1_instrcode_out
  and and_3 (and_3_out, ~DATA_DETC, or_1_out);  // AND_Gate
  Hex_Digit_Display hex_digit_display_8 (.value(LedData[3:0]));  // open: dp
  // Probe on {if_id_1_instrcode_out_2, if_id_1_instrcode_out}
  IF_ID if_id_1 (
    .rst(or_6_out), .clk(CLK), .InstrCode_IN(rom_2_data), .PC_IN(IF_PC),
    .InstrCode_OUT({if_id_1_instrcode_out_2, if_id_1_instrcode_out}), .PC_OUT(ID_PC), .En(and_3_out));
  Adder #(.width(32)) adder_2 (.a(32'h4), .b(EX_PC), .out(adder_2_out));  // open: cin, cout
  // Probe on \总周期数 
  // Probe on \无条件分支数 
  // Probe on \条件分支成功数 
  // Probe on \插入气泡数 
  // Probe on \LoadUse次数 
  // Probe on {if_id_1_instrcode_out_2, if_id_1_instrcode_out}
  Adder #(.width(32)) adder_3 (.a(adder_2_out), .b(shifter_1_out), .out(adder_3_out));  // open: cin, cout
  // Probe on IF_PC[11:0]
  \数据相关检测  \u_数据相关检测_1  (
    .OP(if_id_1_instrcode_out_2), .EX_WriteReg_num(EX_WR_num), .EX_RegWrite(EX_RW),
    .MEM_WriteReg_num(MEM_WR_num), .MEM_RegWrite(MEM_RW), .\数据相关 (DATA_DETC),
    .Func(if_id_1_instrcode_out[5:0]), .ID_R1_num(multiplexer_6_out), .ID_R2_num(multiplexer_7_out));
  // Probe on ID_PC[11:0]
  \硬布线控制器  \u_硬布线控制器_1  (
    .OP(if_id_1_instrcode_out_2), .Func(if_id_1_instrcode_out[5:0]), .ALU_OP(\硬布线控制器_1_alu_op ),
    .MemToReg(\硬布线控制器_1_memtoreg ), .MemWrite(\硬布线控制器_1_memwrite ), .ALU_SRC(\硬布线控制器_1_alu_src ),
    .RegWrite(\硬布线控制器_1_regwrite ), .SysCALL(\硬布线控制器_1_syscall ), .SignedExt(SignedExt),
    .RegDst(\硬布线控制器_1_regdst ), .Beq(\硬布线控制器_1_beq ), .Bne(\硬布线控制器_1_bne ), .JR(\硬布线控制器_1_jr ),
    .JMP(\硬布线控制器_1_jmp ), .JAL(\硬布线控制器_1_jal ), .SLLV(\硬布线控制器_1_sllv ), .LB(\硬布线控制器_1_lb ),
    .BLTZ(\硬布线控制器_1_bltz ));  // open: MFC0, MTC0, ERET, RS
  Multiplexer #(.width(5), .enable("false")) multiplexer_4 (
    .in0(if_id_1_instrcode_out[20:16]), .in1(if_id_1_instrcode_out[15:11]), .out(multiplexer_4_out),
    .sel(\硬布线控制器_1_regdst ));
  Multiplexer #(.width(5), .enable("false")) multiplexer_5 (
    .in0(multiplexer_4_out), .in1({5{1'b1}}), .out(multiplexer_5_out), .sel(\硬布线控制器_1_jal ));
  assign bit_extender_1_out = {{16{1'b0}}, if_id_1_instrcode_out[15:0]};  // Bit_Extender bit_extender_1
  assign bit_extender_2_out = {{16{if_id_1_instrcode_out[15]}}, if_id_1_instrcode_out[15:0]};  // Bit_Extender bit_extender_2
  // Probe on MEM_PC[11:0]
  // Probe on EX_PC[11:0]
  Multiplexer #(.width(5), .enable("false")) multiplexer_6 (
    .in0(if_id_1_instrcode_out[25:21]), .in1(5'b00010), .out(multiplexer_6_out), .sel(\硬布线控制器_1_syscall ));
  and and_4 (and_4_out, \硬布线控制器_1_syscall , comparator_1_eq);
  Multiplexer #(.width(5), .enable("false")) multiplexer_7 (
    .in0(if_id_1_instrcode_out[20:16]), .in1(5'b00100), .out(multiplexer_7_out), .sel(and_4_out));
  // Probe on WB_PC[11:0]
  Multiplexer #(.width(32), .enable("false")) multiplexer_8 (
    .in0(bit_extender_1_out), .in1(bit_extender_2_out), .out(multiplexer_8_out), .sel(SignedExt));
  Shifter #(.width(32)) shifter_1 (.in(bit_extender_3_out), .\dist (5'b00010), .out(shifter_1_out));
  Counter #(.width(16), .max('hffff)) counter_2 (
    .count(DATA_DETC), .Q(\插入气泡数 ), .clk(CLK), .clr(RST));  // open: load, D, carry
  MIPS_Regifile mips_regifile_1 (
    .Din(multiplexer_15_out), .Clk(CLK), .R1(mips_regifile_1_r1), .R2(mips_regifile_1_r2),
    .WE(mem_wb_1_regw_out), .W_num(mem_wb_1_w__out), .R1_num(multiplexer_6_out), .R2_num(multiplexer_7_out));
  Comparator #(.width(32)) comparator_1 (.a(32'h22), .b(mips_regifile_1_r1), .eq(comparator_1_eq));  // open: gt, lt
  or or_6 (or_6_out, or_8_out, or_9_out);
  or or_7 (or_7_out, DATA_DETC, or_6_out);
  ID_EX id_ex_1 (
    .rst(or_7_out), .clk(CLK), .JAL_IN(\硬布线控制器_1_jal ),
    .InstrCode_IN({if_id_1_instrcode_out_2, if_id_1_instrcode_out}), .A_IN(mips_regifile_1_r1),
    .LB_IN(\硬布线控制器_1_lb ), .RegW_IN(\硬布线控制器_1_regwrite ), .PC_IN(ID_PC), .B_IN(mips_regifile_1_r2),
    .RegDst_IN(\硬布线控制器_1_regdst ), .syscall_IN(\硬布线控制器_1_syscall ), .Imm_IN(multiplexer_8_out),
    .R1Equal22_IN(comparator_1_eq), .JMP_IN(\硬布线控制器_1_jmp ), .JR_IN(\硬布线控制器_1_jr ), .Beq_IN(\硬布线控制器_1_beq ),
    .Bne_IN(\硬布线控制器_1_bne ), .MemW_IN(\硬布线控制器_1_memwrite ), .AluOP_IN(\硬布线控制器_1_alu_op ),
    .AluSrc_IN(\硬布线控制器_1_alu_src ), .BLTZ_IN(\硬布线控制器_1_bltz ), .SLLV_IN(\硬布线控制器_1_sllv ),
    .JAL_OUT(id_ex_1_jal_out), .InstrCode_OUT(id_ex_1_instrcode_out),
    .A_OUT({id_ex_1_a_out_2, id_ex_1_a_out}), .LB_OUT(id_ex_1_lb_out), .RegW_OUT(EX_RW), .PC_OUT(EX_PC),
    .B_OUT(id_ex_1_b_out), .RegDst_OUT(id_ex_1_regdst_out), .syscall_OUT(id_ex_1_syscall_out),
    .Imm_OUT(id_ex_1_imm_out), .R1Equal22_OUT(id_ex_1_r1equal22_out), .JMP_OUT(id_ex_1_jmp_out),
    .JR_OUT(id_ex_1_jr_out), .Beq_OUT(id_ex_1_beq_out), .Bne_OUT(id_ex_1_bne_out),
    .MemW_OUT(id_ex_1_memw_out), .AluOP_OUT(id_ex_1_aluop_out), .AluSrc_OUT(id_ex_1_alusrc_out),
    .BLTZ_OUT(id_ex_1_bltz_out), .SLLV_OUT(id_ex_1_sllv_out), .M2R_IN(\硬布线控制器_1_memtoreg ),
    .M2R_OUT(id_ex_1_m2r_out), .W__IN(multiplexer_5_out), .W__OUT(EX_WR_num), .En(or_1_out));  // open: AluEqual_IN, BLTZandAR1_IN, SignedExt_IN, AluEqual_OUT, BLTZandAR1_OUT, SignedExt_OUT, R2F2_IN, R2F2_OUT
  // Probe on id_ex_1_instrcode_out
  assign bit_extender_3_out = {{16{id_ex_1_instrcode_out[15]}}, id_ex_1_instrcode_out[15:0]};  // Bit_Extender bit_extender_3
  Multiplexer #(.width(32), .enable("false")) multiplexer_9 (
    .in0(id_ex_1_b_out), .in1(id_ex_1_imm_out), .out(multiplexer_9_out), .sel(id_ex_1_alusrc_out));
  Multiplexer #(.width(32), .enable("false")) multiplexer_10 (
    .in0(multiplexer_9_out), .in1({32{1'b0}}), .out(multiplexer_10_out), .sel(id_ex_1_bltz_out));
  // Probe on id_ex_1_instrcode_out
  MIPS_ALU mips_alu_1 (
    .X({id_ex_1_a_out_2, id_ex_1_a_out}), .Y(multiplexer_10_out), .AluOP(id_ex_1_aluop_out),
    .Equal(mips_alu_1_equal), .Result(mips_alu_1_result), .shamt(multiplexer_11_out));  // open: Result_2
  Multiplexer #(.width(5), .enable("false")) multiplexer_11 (
    .in0(id_ex_1_instrcode_out[10:6]), .in1(id_ex_1_a_out), .out(multiplexer_11_out), .sel(id_ex_1_sllv_out));
  Comparator #(.width(32)) comparator_2 (.a(mips_alu_1_result), .b(32'h1), .eq(comparator_2_eq));  // open: gt, lt
  and and_5 (and_5_out, comparator_2_eq, id_ex_1_bltz_out);
  EX_MEM ex_mem_1 (
    .rst(RST), .clk(CLK), .JAL_IN(id_ex_1_jal_out), .InstrCode_IN(id_ex_1_instrcode_out),
    .LB_IN(id_ex_1_lb_out), .RegW_IN(EX_RW), .PC_IN(EX_PC), .B_IN(id_ex_1_b_out),
    .RegDst_IN(id_ex_1_regdst_out), .syscall_IN(id_ex_1_syscall_out), .AluResult_IN(mips_alu_1_result),
    .R1Equal22_IN(id_ex_1_r1equal22_out), .JMP_IN(id_ex_1_jmp_out), .JR_IN(id_ex_1_jr_out),
    .Beq_IN(id_ex_1_beq_out), .Bne_IN(id_ex_1_bne_out), .AluEqual_IN(mips_alu_1_equal),
    .BLTZandAR1_IN(and_5_out), .MemW_IN(id_ex_1_memw_out), .JAL_OUT(ex_mem_1_jal_out),
    .InstrCode_OUT(ex_mem_1_instrcode_out), .LB_OUT(ex_mem_1_lb_out), .RegW_OUT(MEM_RW), .PC_OUT(MEM_PC),
    .B_OUT(ex_mem_1_b_out), .RegDst_OUT(ex_mem_1_regdst_out), .syscall_OUT(ex_mem_1_syscall_out),
    .AluResult_OUT(ex_mem_1_aluresult_out), .R1Equal22_OUT(ex_mem_1_r1equal22_out),
    .JMP_OUT(ex_mem_1_jmp_out), .JR_OUT(ex_mem_1_jr_out), .Beq_OUT(ex_mem_1_beq_out),
    .Bne_OUT(ex_mem_1_bne_out), .AluEqual_OUT(ex_mem_1_aluequal_out),
    .BLTZandAR1_OUT(ex_mem_1_bltzandar1_out), .MemW_OUT(ex_mem_1_memw_out),
    .A_IN({id_ex_1_a_out_2, id_ex_1_a_out}), .A_OUT(ex_mem_1_a_out), .M2R_IN(id_ex_1_m2r_out),
    .M2R_OUT(ex_mem_1_m2r_out), .W__IN(EX_WR_num), .W__OUT(MEM_WR_num));  // open: En
  // Probe on ex_mem_1_b_out
  RAM #(.addrWidth(10), .dataWidth(32), .bus("separate")) ram_1 (
    .addr(ex_mem_1_aluresult_out[11:2]), .din(ex_mem_1_b_out), .data(ram_1_data), .str(ex_mem_1_memw_out),
    .clk(CLK), .clr(RST));  // open: sel, ld
  // Probe on ex_mem_1_instrcode_out
  MEM_WB mem_wb_1 (
    .rst(RST), .clk(CLK), .JAL_IN(ex_mem_1_jal_out), .InstrCode_IN(ex_mem_1_instrcode_out),
    .LB_IN(ex_mem_1_lb_out), .RegW_IN(MEM_RW), .PC_IN(MEM_PC), .MD_IN(ram_1_data),
    .RegDst_IN(ex_mem_1_regdst_out), .syscall_IN(ex_mem_1_syscall_out),
    .AluResult_IN(ex_mem_1_aluresult_out), .R1Equal22_IN(ex_mem_1_r1equal22_out), .JMP_IN(ex_mem_1_jmp_out),
    .JR_IN(ex_mem_1_jr_out), .Beq_IN(ex_mem_1_beq_out), .Bne_IN(ex_mem_1_bne_out),
    .AluEqual_IN(ex_mem_1_aluequal_out), .BLTZandAR1_IN(ex_mem_1_bltzandar1_out), .JAL_OUT(mem_wb_1_jal_out),
    .LB_OUT(mem_wb_1_lb_out), .RegW_OUT(mem_wb_1_regw_out), .PC_OUT(WB_PC), .MD_OUT(mem_wb_1_md_out),
    .syscall_OUT(SYSCALL_4), .AluResult_OUT(mem_wb_1_aluresult_out), .R1Equal22_OUT(R1E22_4),
    .A_IN(ex_mem_1_a_out), .A_OUT(mem_wb_1_a_out), .B_IN(ex_mem_1_b_out), .M2R_IN(ex_mem_1_m2r_out),
    .M2R_OUT(mem_wb_1_m2r_out), .W__IN(MEM_WR_num), .W__OUT(mem_wb_1_w__out));  // open: InstrCode_OUT, RegDst_OUT, JMP_OUT, JR_OUT, Beq_OUT, Bne_OUT, AluEqual_OUT, BLTZandAR1_OUT, B_OUT, En
  // Probe on nothing
  Multiplexer #(.width(32), .enable("false")) multiplexer_12 (
    .in0(mem_wb_1_aluresult_out), .in1(mem_wb_1_md_out), .out(multiplexer_12_out), .sel(mem_wb_1_m2r_out));
  not not_3 (not_3_out, mips_alu_1_equal);
  or or_8 (or_8_out, id_ex_1_jal_out, id_ex_1_jmp_out, id_ex_1_jr_out);
  and and_6 (and_6_out, id_ex_1_beq_out, mips_alu_1_equal);
  and and_7 (and_7_out, id_ex_1_bne_out, not_3_out);
  and and_8 (and_8_out, id_ex_1_r1equal22_out, id_ex_1_syscall_out);
  // Probe on id_ex_1_b_out
  Multiplexer #(.select(2), .width(8), .enable("false")) multiplexer_13 (
    .in0(multiplexer_12_out[7:0]), .in1(multiplexer_12_out[15:8]), .in2(multiplexer_12_out[23:16]),
    .in3(multiplexer_12_out[31:24]), .out(multiplexer_13_out), .sel(mem_wb_1_aluresult_out[1:0]));
  Counter #(.width(16), .max('hffff)) counter_3 (
    .count(or_8_out), .Q(\无条件分支数 ), .clk(CLK), .clr(RST));  // open: load, D, carry
  or or_9 (or_9_out, and_6_out, and_5_out, and_7_out);
  Register #(.width(32)) register_1 (.D(id_ex_1_b_out), .en(and_8_out), .Q(LedData), .clk(CLK), .clr(RST));
  Adder #(.width(32)) adder_4 (.a(WB_PC), .b(32'h4), .out(adder_4_out));  // open: cin, cout
  Multiplexer #(.width(32), .enable("false")) multiplexer_14 (
    .in0(multiplexer_12_out), .in1(adder_4_out), .out(multiplexer_14_out), .sel(mem_wb_1_jal_out));
  assign bit_extender_4_out = {{24{multiplexer_13_out[7]}}, multiplexer_13_out};  // Bit_Extender bit_extender_4
  Counter #(.width(16), .max('hffff)) counter_4 (
    .count(or_9_out), .Q(\条件分支成功数 ), .clk(CLK), .clr(RST));  // open: load, D, carry
  Multiplexer #(.width(32), .enable("false")) multiplexer_15 (
    .in0(multiplexer_14_out), .in1(bit_extender_4_out), .out(multiplexer_15_out), .sel(mem_wb_1_lb_out));

  // Notes on the sheet:
  //   中断源
  //   中断等待指示
  //   数码管输出
  //   contents of rom_1 (hex, n*v repeats v):
  //   20110001 8000c05 20110001 20120002 20130003 8000c09 20110001 20120002 20130003 8000c0d 20110001
  //   20120002 20130003 8000c11 20110001 20120002 20130003 c000cb8 20100001 20110001 118fc0 112020
  //   20020022 c 118882 12200001 8000c15 112020 20020022 c 20110001 118880 112020 20020022 c 12200001
  //   8000c1f 20110001 118fc0 112020 20020022 c 1188c3 112020 20020022 c 118903 112020 20020022 c 118903
  //   112020 20020022 c 118903 112020 20020022 c 118903 112020 20020022 c 118903 112020 20020022 c 118903
  //   112020 20020022 c 118903 112020 20020022 c 20100001 109fc0 139fc3 8021 2012000c 24160003 26100001
  //   3210000f 20080008 20090001 139900 2709825 132020 20020022 c 1094022 1500fff9 22100001 2018000f
  //   2188024 108700 20080008 20090001 139902 2709825 132021 20020022 c 1094022 1500fff9 108702 2c9b022
  //   12c00001 8000c50 4020 1084027 84400 3508ffff 82021 20020022 c 2010ffff 20110000 ae300000 22100001
  //   22310004 ae300000 22100001 22310004 ae300000 22100001 22310004 ae300000 22100001 22310004 ae300000
  //   22100001 22310004 ae300000 22100001 22310004 ae300000 22100001 22310004 ae300000 22100001 22310004
  //   ae300000 22100001 22310004 ae300000 22100001 22310004 ae300000 22100001 22310004 ae300000 22100001
  //   22310004 ae300000 22100001 22310004 ae300000 22100001 22310004 ae300000 22100001 22310004 ae300000
  //   22100001 22310004 22100001 8020 2011003c 8e130000 8e340000 274402a 11000002 ae330000 ae140000
  //   2231fffc 1611fff8 102020 20020022 c 22100004 2011003c 1611fff2 2002000a c 20100000 22100001 102020
  //   20020022 c 22100002 102020 20020022 c 22100003 102020 20020022 c 22100004 102020 20020022 c 22100005
  //   102020 20020022 c 22100006 102020 20020022 c 22100007 102020 20020022 c 22100008 102020 20020022
  //   20020022 c 3e00008
  //   指令存储器
  //   contents of rom_2 (hex, n*v repeats v):
  //   20110001 8000c05 20110001 20120002 20130003 8000c09 20110001 20120002 20130003 8000c0d 20110001
  //   20120002 20130003 8000c11 20110001 20120002 20130003 c000cf8 20100001 20110001 118fc0 112020
  //   20020022 c 118882 12200001 8000c15 112020 20020022 c 20110001 118880 112020 20020022 c 12200001
  //   8000c1f 20110001 118fc0 112020 20020022 c 1188c3 112020 20020022 c 118903 112020 20020022 c 118903
  //   112020 20020022 c 118903 112020 20020022 c 118903 112020 20020022 c 118903 112020 20020022 c 118903
  //   112020 20020022 c 118903 112020 20020022 c 20100001 109fc0 139fc3 8021 2012000c 24160003 26100001
  //   3210000f 20080008 20090001 139900 2709825 132020 20020022 c 1094022 1500fff9 22100001 2018000f
  //   2188024 108700 20080008 20090001 139902 2709825 132021 20020022 c 1094022 1500fff9 108702 2c9b022
  //   12c00001 8000c50 4020 1084027 84400 3508ffff 82021 20020022 c 2010ffff 20110000 ae300000 22100001
  //   22310004 ae300000 22100001 22310004 ae300000 22100001 22310004 ae300000 22100001 22310004 ae300000
  //   22100001 22310004 ae300000 22100001 22310004 ae300000 22100001 22310004 ae300000 22100001 22310004
  //   ae300000 22100001 22310004 ae300000 22100001 22310004 ae300000 22100001 22310004 ae300000 22100001
  //   22310004 ae300000 22100001 22310004 ae300000 22100001 22310004 ae300000 22100001 22310004 ae300000
  //   22100001 22310004 22100001 8020 2011003c 8e130000 8e340000 274402a 11000002 ae330000 ae140000
  //   2231fffc 1611fff8 102020 20020022 c 22100004 2011003c 1611fff2 20020032 c 20080001 20090003 20110876
  //   112020 20020022 c 200b0008 1118804 1318804 112020 20020022 c 216bffff 1560fff9 2002000a c 20080001
  //   20110010 112020 20020022 c 200b0020 2288823 112020 20020022 c 216bffff 1560fffa 2002000a c 20090000
  //   200b0010 34118483 20120404 118c00 129400 36318281 22520404 ad310000 2328820 21290004 216bffff
  //   1560fffb 200b0020 20090000 81310000 112020 20020022 c 21290001 216bffff 1560fff9 2002000a c 2011fff1
  //   112020 20020022 c 22310001 620fffb 2002000a c 2002000a c 20100000 22100001 102020 20020022 c
  //   22100002 102020 20020022 c 22100003 102020 20020022 c 22100004 102020 20020022 c 22100005 102020
  //   20020022 c 22100006 102020 20020022 c 22100007 102020 20020022 c 22100008 102020 20020022 20020022 c
  //   3e00008
  //   Op
  //   Func
  //   Beq
  //   Bne
  //   MemToReg
  //   MemWrite
  //   AluOP
  //   AluSrcB
  //   RegWrite
  //   RegDst
  //   流水调试日志用
endmodule

module \重定向流水线  (
);

  wire and_1_out, and_2_out, and_3_out, and_4_out, and_6_out, and_7_out, and_8_out, and_9_out, CLK,
       comparator_1_eq, comparator_2_eq, comparator_3_eq, comparator_4_eq, comparator_5_eq, comparator_6_eq,
       comparator_7_eq, ex_mem_1_aluequal_out, ex_mem_1_beq_out, ex_mem_1_bltzandar1_out, ex_mem_1_bne_out,
       ex_mem_1_jal_out, ex_mem_1_jmp_out, ex_mem_1_jr_out, ex_mem_1_lb_out, ex_mem_1_m2r_out,
       ex_mem_1_memw_out, ex_mem_1_r1equal22_out, ex_mem_1_regdst_out, ex_mem_1_syscall_out, EX_RW, Go,
       id_ex_1_alusrc_out, id_ex_1_beq_out, id_ex_1_bltz_out, id_ex_1_bne_out, id_ex_1_jal_out,
       id_ex_1_jmp_out, id_ex_1_jr_out, id_ex_1_lb_out, id_ex_1_m2r_out, id_ex_1_memw_out,
       id_ex_1_r1equal22_out, id_ex_1_regdst_out, id_ex_1_sllv_out, id_ex_1_syscall_out, IR1, IR2, IR3,
       LoadUse, MEM_RW, mem_wb_1_jal_out, mem_wb_1_lb_out, mem_wb_1_m2r_out, mem_wb_1_regw_out,
       mips_alu_1_equal, not_1_out, not_2_out, not_3_out, or_1_out, or_2_out, or_3_out, or_4_out, or_5_out,
       or_6_out, or_7_out, or_8_out, or_9_out, or_10_out, or_11_out, R1E22_4, R1EX, r1forward_1_r1forward1,
       r1forward_1_r1forward2, r1forward_2_r1forward1, r1forward_2_r1forward2, R1MEM, R2EX, R2MEM, RST,
       SignedExt, SYSCALL_4, W1, W2, W3, \硬布线控制器_1_alu_src , \硬布线控制器_1_beq , \硬布线控制器_1_bltz , \硬布线控制器_1_bne ,
       \硬布线控制器_1_jal , \硬布线控制器_1_jmp , \硬布线控制器_1_jr , \硬布线控制器_1_lb , \硬布线控制器_1_memtoreg ,
       \硬布线控制器_1_memwrite , \硬布线控制器_1_regdst , \硬布线控制器_1_regwrite , \硬布线控制器_1_sllv , \硬布线控制器_1_syscall ;
  wire [1:0] id_ex_1_bltzandar1_out, id_ex_1_r2f2_out;
  wire [3:0] id_ex_1_aluop_out, \硬布线控制器_1_alu_op ;
  wire [4:0] EX_WR_num, mem_wb_1_w__out, MEM_WR_num, multiplexer_4_out, multiplexer_5_out, multiplexer_6_out,
       multiplexer_7_out, multiplexer_13_out;
  wire [5:0] id_ex_1_instrcode_out_3, if_id_1_instrcode_out, if_id_1_instrcode_out_3;
  wire [7:0] multiplexer_15_out;
  wire [15:0] id_ex_1_instrcode_out, \LoadUse次数 , \总周期数 , \插入气泡数 , \无条件分支数 , \条件分支成功数 ;
  wire [25:6] if_id_1_instrcode_out_2;
  wire [27:18] id_ex_1_instrcode_out_2;
  wire [31:0] adder_1_out, adder_2_out, adder_3_out, adder_4_out, bit_extender_1_out, bit_extender_2_out,
       bit_extender_3_out, bit_extender_4_out, ex_mem_1_a_out, ex_mem_1_b_out, ex_mem_1_instrcode_out, EX_PC,
       id_ex_1_a_out, id_ex_1_b_out, id_ex_1_imm_out, ID_PC, IF_PC, LedData, MEM_ALUR, MEM_PC, Mem_ReadData,
       mem_wb_1_a_out, mips_alu_1_result, mips_regifile_1_r1, mips_regifile_1_r2, multiplexer_1_out,
       multiplexer_2_out, multiplexer_3_out, multiplexer_8_out, multiplexer_9_out, multiplexer_10_out,
       multiplexer_11_out, multiplexer_12_out, multiplexer_14_out, multiplexer_16_out, ram_1_data,
       rom_2_data, shifter_1_out, WB_ALUR, WB_DATA, WB_PC;

  Button \u_总复位  (.out(RST));
  Button _1 (.out(IR1));
  Button _2 (.out(IR2));
  Button _3 (.out(IR3));
  Button \u_继续运行  (.out(Go));
  LED led_1 (.in(W1));
  LED led_2 (.in(W2));
  LED led_3 (.in(W3));
  Multiplexer #(.width(32), .enable("false")) multiplexer_1 (
    .in0(adder_1_out), .in1(adder_3_out), .out(multiplexer_1_out), .sel(or_11_out));
  Multiplexer #(.width(32), .enable("false")) multiplexer_2 (
    .in0(multiplexer_1_out), .in1(multiplexer_9_out), .out(multiplexer_2_out), .sel(id_ex_1_jr_out));
  Hex_Digit_Display hex_digit_display_1 (.value(LedData[31:28]));  // open: dp
  or or_1 (or_1_out, or_3_out, not_1_out);
  or or_2 (or_2_out, id_ex_1_jmp_out, id_ex_1_jal_out);
  Multiplexer #(.width(32), .enable("false")) multiplexer_3 (
    .in0(multiplexer_2_out), .in1({IF_PC[31:28], id_ex_1_instrcode_out_2, id_ex_1_instrcode_out, 2'b00}),
    .out(multiplexer_3_out), .sel(or_2_out));
  Hex_Digit_Display hex_digit_display_2 (.value(LedData[27:24]));  // open: dp
  Hex_Digit_Display hex_digit_display_3 (.value(LedData[23:20]));  // open: dp
  not not_1 (not_1_out, id_ex_1_syscall_out);
  or or_3 (or_3_out, and_1_out, Go);
  not not_2 (not_2_out, SYSCALL_4);
  or or_4 (or_4_out, and_2_out, Go);
  or or_5 (or_5_out, not_2_out, or_4_out);
  Register #(.width(32)) PC (.D(multiplexer_3_out), .en(and_3_out), .Q(IF_PC), .clk(CLK), .clr(RST));
  Hex_Digit_Display hex_digit_display_4 (.value(LedData[19:16]));  // open: dp
  Hex_Digit_Display hex_digit_display_5 (.value(LedData[15:12]));  // open: dp
  ROM #(.addrWidth(10), .dataWidth(32)) rom_1 ();  // open: addr, data, sel
  and and_1 (and_1_out, id_ex_1_syscall_out, comparator_4_eq);
  and and_2 (and_2_out, SYSCALL_4, R1E22_4);
  Adder #(.width(32)) adder_1 (.a(IF_PC), .b(32'h4), .out(adder_1_out));  // open: cin, cout
  Hex_Digit_Display hex_digit_display_6 (.value(LedData[7:4]));  // open: dp
  Hex_Digit_Display hex_digit_display_7 (.value(LedData[11:8]));  // open: dp
  Clock clock_1 (.out(CLK));
  Counter #(.width(16), .max('hffff)) counter_1 (
    .count(or_5_out), .Q(\总周期数 ), .clk(CLK), .clr(RST));  // open: load, D, carry
  ROM #(.addrWidth(10), .dataWidth(32)) rom_2 (.addr(IF_PC[11:2]), .data(rom_2_data));  // open: sel
  Hex_Digit_Display hex_digit_display_8 (.value(LedData[3:0]));  // open: dp
  and and_3 (and_3_out, ~LoadUse, or_1_out);  // AND_Gate
  IF_ID if_id_1 (
    .rst(or_7_out), .clk(CLK), .InstrCode_IN(rom_2_data), .PC_IN(IF_PC),
    .InstrCode_OUT({if_id_1_instrcode_out_3, if_id_1_instrcode_out_2, if_id_1_instrcode_out}),
    .PC_OUT(ID_PC), .En(and_3_out));
  Adder #(.width(32)) adder_2 (.a(32'h4), .b(EX_PC), .out(adder_2_out));  // open: cin, cout
  // Probe on \总周期数 
  // Probe on \无条件分支数 
  // Probe on \条件分支成功数 
  // Probe on \插入气泡数 
  // Probe on \LoadUse次数 
  \重定向数据相关检测  \u_重定向数据相关检测_1  (
    .OP(if_id_1_instrcode_out_3), .EX_WriteReg_num(EX_WR_num), .EX_RegWrite(EX_RW),
    .MEM_WriteReg_num(MEM_WR_num), .MEM_RegWrite(MEM_RW), .Func(if_id_1_instrcode_out),
    .ID_R1_num(multiplexer_6_out), .ID_R2_num(multiplexer_7_out), .\R1EX数据相关 (R1EX), .\R1MEM数据相关 (R1MEM),
    .\R2EX数据相关 (R2EX), .\R2MEM数据相关 (R2MEM));
  Adder #(.width(32)) adder_3 (.a(adder_2_out), .b(shifter_1_out), .out(adder_3_out));  // open: cin, cout
  // Probe on IF_PC[11:0]
  // Probe on ID_PC[11:0]
  \硬布线控制器  \u_硬布线控制器_1  (
    .OP(if_id_1_instrcode_out_3), .Func(if_id_1_instrcode_out), .ALU_OP(\硬布线控制器_1_alu_op ),
    .MemToReg(\硬布线控制器_1_memtoreg ), .MemWrite(\硬布线控制器_1_memwrite ), .ALU_SRC(\硬布线控制器_1_alu_src ),
    .RegWrite(\硬布线控制器_1_regwrite ), .SysCALL(\硬布线控制器_1_syscall ), .SignedExt(SignedExt),
    .RegDst(\硬布线控制器_1_regdst ), .Beq(\硬布线控制器_1_beq ), .Bne(\硬布线控制器_1_bne ), .JR(\硬布线控制器_1_jr ),
    .JMP(\硬布线控制器_1_jmp ), .JAL(\硬布线控制器_1_jal ), .SLLV(\硬布线控制器_1_sllv ), .LB(\硬布线控制器_1_lb ),
    .BLTZ(\硬布线控制器_1_bltz ));  // open: MFC0, MTC0, ERET, RS
  Multiplexer #(.width(5), .enable("false")) multiplexer_4 (
    .in0(if_id_1_instrcode_out_2[20:16]), .in1(if_id_1_instrcode_out_2[15:11]), .out(multiplexer_4_out),
    .sel(\硬布线控制器_1_regdst ));
  Multiplexer #(.width(5), .enable("false")) multiplexer_5 (
    .in0(multiplexer_4_out), .in1({5{1'b1}}), .out(multiplexer_5_out), .sel(\硬布线控制器_1_jal ));
  Comparator #(.width(5)) comparator_1 (.a(multiplexer_7_out), .b(EX_WR_num), .eq(comparator_1_eq));  // open: gt, lt
  Comparator #(.width(5)) comparator_2 (.a(multiplexer_6_out), .b(EX_WR_num), .eq(comparator_2_eq));  // open: gt, lt
  assign bit_extender_1_out = {{16{1'b0}}, {if_id_1_instrcode_out_2[15:6], if_id_1_instrcode_out}};  // Bit_Extender bit_extender_1
  assign bit_extender_2_out = {{16{if_id_1_instrcode_out_2[15]}}, {if_id_1_instrcode_out_2[15:6], if_id_1_instrcode_out}};  // Bit_Extender bit_extender_2
  // Probe on EX_PC[11:0]
  // Probe on MEM_PC[11:0]
  Multiplexer #(.width(5), .enable("false")) multiplexer_6 (
    .in0(if_id_1_instrcode_out_2[25:21]), .in1(5'b00010), .out(multiplexer_6_out), .sel(\硬布线控制器_1_syscall ));
  and and_4 (and_4_out, \硬布线控制器_1_syscall , comparator_3_eq);
  Multiplexer #(.width(5), .enable("false")) multiplexer_7 (
    .in0(if_id_1_instrcode_out_2[20:16]), .in1(5'b00100), .out(multiplexer_7_out), .sel(and_4_out));
  or or_6 (or_6_out, comparator_1_eq, comparator_2_eq);
  and and_5 (LoadUse, or_9_out, or_6_out);
  // Probe on WB_PC[11:0]
  R1Forward r1forward_1 (
    .R1EX(R1EX), .R1MEM(R1MEM), .R1Forward1(r1forward_1_r1forward1), .R1Forward2(r1forward_1_r1forward2));
  R1Forward r1forward_2 (
    .R1EX(R2EX), .R1MEM(R2MEM), .R1Forward1(r1forward_2_r1forward1), .R1Forward2(r1forward_2_r1forward2));
  Multiplexer #(.width(32), .enable("false")) multiplexer_8 (
    .in0(bit_extender_1_out), .in1(bit_extender_2_out), .out(multiplexer_8_out), .sel(SignedExt));
  Shifter #(.width(32)) shifter_1 (.in(bit_extender_3_out), .\dist (5'b00010), .out(shifter_1_out));
  Counter #(.width(16), .max('hffff)) counter_2 (
    .count(LoadUse), .Q(\LoadUse次数 ), .clk(CLK), .clr(RST));  // open: load, D, carry
  MIPS_Regifile mips_regifile_1 (
    .Din(WB_DATA), .Clk(CLK), .R1(mips_regifile_1_r1), .R2(mips_regifile_1_r2), .WE(mem_wb_1_regw_out),
    .W_num(mem_wb_1_w__out), .R1_num(multiplexer_6_out), .R2_num(multiplexer_7_out));
  Comparator #(.width(32)) comparator_3 (.a(32'h22), .b(mips_regifile_1_r1), .eq(comparator_3_eq));  // open: gt, lt
  or or_7 (or_7_out, or_10_out, or_11_out);
  or or_8 (or_8_out, LoadUse, or_7_out);
  ID_EX id_ex_1 (
    .rst(or_8_out), .clk(CLK), .JAL_IN(\硬布线控制器_1_jal ),
    .InstrCode_IN({if_id_1_instrcode_out_3, if_id_1_instrcode_out_2, if_id_1_instrcode_out}),
    .A_IN(mips_regifile_1_r1), .LB_IN(\硬布线控制器_1_lb ), .RegW_IN(\硬布线控制器_1_regwrite ), .PC_IN(ID_PC),
    .B_IN(mips_regifile_1_r2), .RegDst_IN(\硬布线控制器_1_regdst ), .syscall_IN(\硬布线控制器_1_syscall ),
    .Imm_IN(multiplexer_8_out), .R1Equal22_IN(comparator_3_eq), .JMP_IN(\硬布线控制器_1_jmp ),
    .JR_IN(\硬布线控制器_1_jr ), .Beq_IN(\硬布线控制器_1_beq ), .Bne_IN(\硬布线控制器_1_bne ),
    .AluEqual_IN(r1forward_1_r1forward1), .BLTZandAR1_IN(r1forward_1_r1forward2),
    .MemW_IN(\硬布线控制器_1_memwrite ), .AluOP_IN(\硬布线控制器_1_alu_op ), .AluSrc_IN(\硬布线控制器_1_alu_src ),
    .BLTZ_IN(\硬布线控制器_1_bltz ), .SLLV_IN(\硬布线控制器_1_sllv ), .SignedExt_IN(r1forward_2_r1forward1),
    .JAL_OUT(id_ex_1_jal_out),
    .InstrCode_OUT({id_ex_1_instrcode_out_3, id_ex_1_instrcode_out_2, id_ex_1_instrcode_out}),
    .A_OUT(id_ex_1_a_out), .LB_OUT(id_ex_1_lb_out), .RegW_OUT(EX_RW), .PC_OUT(EX_PC), .B_OUT(id_ex_1_b_out),
    .RegDst_OUT(id_ex_1_regdst_out), .syscall_OUT(id_ex_1_syscall_out), .Imm_OUT(id_ex_1_imm_out),
    .R1Equal22_OUT(id_ex_1_r1equal22_out), .JMP_OUT(id_ex_1_jmp_out), .JR_OUT(id_ex_1_jr_out),
    .Beq_OUT(id_ex_1_beq_out), .Bne_OUT(id_ex_1_bne_out), .AluEqual_OUT(id_ex_1_bltzandar1_out[1]),
    .BLTZandAR1_OUT(id_ex_1_bltzandar1_out[0]), .MemW_OUT(id_ex_1_memw_out), .AluOP_OUT(id_ex_1_aluop_out),
    .AluSrc_OUT(id_ex_1_alusrc_out), .BLTZ_OUT(id_ex_1_bltz_out), .SLLV_OUT(id_ex_1_sllv_out),
    .SignedExt_OUT(id_ex_1_r2f2_out[1]), .M2R_IN(\硬布线控制器_1_memtoreg ), .M2R_OUT(id_ex_1_m2r_out),
    .W__IN(multiplexer_5_out), .W__OUT(EX_WR_num), .En(or_1_out), .R2F2_IN(r1forward_2_r1forward2),
    .R2F2_OUT(id_ex_1_r2f2_out[0]));
  Multiplexer #(.select(2), .width(32), .enable("false")) multiplexer_9 (
    .in0(id_ex_1_a_out), .in1(WB_DATA), .in3(MEM_ALUR), .out(multiplexer_9_out), .sel(id_ex_1_bltzandar1_out));  // open: in2
  Multiplexer #(.select(2), .width(32), .enable("false")) multiplexer_10 (
    .in0(id_ex_1_b_out), .in1(WB_DATA), .in3(MEM_ALUR), .out(multiplexer_10_out), .sel(id_ex_1_r2f2_out));  // open: in2
  assign bit_extender_3_out = {{16{id_ex_1_instrcode_out[15]}}, id_ex_1_instrcode_out};  // Bit_Extender bit_extender_3
  Comparator #(.width(32)) comparator_4 (.a(32'h22), .b(multiplexer_9_out), .eq(comparator_4_eq));  // open: gt, lt
  Multiplexer #(.width(32), .enable("false")) multiplexer_11 (
    .in0(multiplexer_10_out), .in1(id_ex_1_imm_out), .out(multiplexer_11_out), .sel(id_ex_1_alusrc_out));
  Multiplexer #(.width(32), .enable("false")) multiplexer_12 (
    .in0(multiplexer_11_out), .in1({32{1'b0}}), .out(multiplexer_12_out), .sel(id_ex_1_bltz_out));
  Comparator #(.width(6)) comparator_5 (
    .a(id_ex_1_instrcode_out_3), .b(6'b100011), .eq(comparator_5_eq));  // open: gt, lt
  Comparator #(.width(6)) comparator_6 (
    .a(id_ex_1_instrcode_out_3), .b(6'b100000), .eq(comparator_6_eq));  // open: gt, lt
  MIPS_ALU mips_alu_1 (
    .X(multiplexer_9_out), .Y(multiplexer_12_out), .AluOP(id_ex_1_aluop_out), .Equal(mips_alu_1_equal),
    .Result(mips_alu_1_result), .shamt(multiplexer_13_out));  // open: Result_2
  Multiplexer #(.width(5), .enable("false")) multiplexer_13 (
    .in0(id_ex_1_instrcode_out[10:6]), .in1(id_ex_1_a_out[4:0]), .out(multiplexer_13_out),
    .sel(id_ex_1_sllv_out));
  or or_9 (or_9_out, comparator_5_eq, comparator_6_eq);
  Comparator #(.width(32)) comparator_7 (.a(mips_alu_1_result), .b(32'h1), .eq(comparator_7_eq));  // open: gt, lt
  and and_6 (and_6_out, comparator_7_eq, id_ex_1_bltz_out);
  EX_MEM ex_mem_1 (
    .rst(RST), .clk(CLK), .JAL_IN(id_ex_1_jal_out),
    .InstrCode_IN({id_ex_1_instrcode_out_3, id_ex_1_instrcode_out_2, id_ex_1_instrcode_out}),
    .LB_IN(id_ex_1_lb_out), .RegW_IN(EX_RW), .PC_IN(EX_PC), .B_IN(multiplexer_10_out),
    .RegDst_IN(id_ex_1_regdst_out), .syscall_IN(id_ex_1_syscall_out), .AluResult_IN(mips_alu_1_result),
    .R1Equal22_IN(comparator_4_eq), .JMP_IN(id_ex_1_jmp_out), .JR_IN(id_ex_1_jr_out),
    .Beq_IN(id_ex_1_beq_out), .Bne_IN(id_ex_1_bne_out), .AluEqual_IN(mips_alu_1_equal),
    .BLTZandAR1_IN(and_6_out), .MemW_IN(id_ex_1_memw_out), .JAL_OUT(ex_mem_1_jal_out),
    .InstrCode_OUT(ex_mem_1_instrcode_out), .LB_OUT(ex_mem_1_lb_out), .RegW_OUT(MEM_RW), .PC_OUT(MEM_PC),
    .B_OUT(ex_mem_1_b_out), .RegDst_OUT(ex_mem_1_regdst_out), .syscall_OUT(ex_mem_1_syscall_out),
    .AluResult_OUT(MEM_ALUR), .R1Equal22_OUT(ex_mem_1_r1equal22_out), .JMP_OUT(ex_mem_1_jmp_out),
    .JR_OUT(ex_mem_1_jr_out), .Beq_OUT(ex_mem_1_beq_out), .Bne_OUT(ex_mem_1_bne_out),
    .AluEqual_OUT(ex_mem_1_aluequal_out), .BLTZandAR1_OUT(ex_mem_1_bltzandar1_out),
    .MemW_OUT(ex_mem_1_memw_out), .A_IN(multiplexer_9_out), .A_OUT(ex_mem_1_a_out), .M2R_IN(id_ex_1_m2r_out),
    .M2R_OUT(ex_mem_1_m2r_out), .W__IN(EX_WR_num), .W__OUT(MEM_WR_num));  // open: En
  // Probe on ex_mem_1_b_out
  RAM #(.addrWidth(10), .dataWidth(32), .bus("separate")) ram_1 (
    .addr(MEM_ALUR[11:2]), .din(ex_mem_1_b_out), .data(ram_1_data), .str(ex_mem_1_memw_out), .clk(CLK),
    .clr(RST));  // open: sel, ld
  MEM_WB mem_wb_1 (
    .rst(RST), .clk(CLK), .JAL_IN(ex_mem_1_jal_out), .InstrCode_IN(ex_mem_1_instrcode_out),
    .LB_IN(ex_mem_1_lb_out), .RegW_IN(MEM_RW), .PC_IN(MEM_PC), .MD_IN(ram_1_data),
    .RegDst_IN(ex_mem_1_regdst_out), .syscall_IN(ex_mem_1_syscall_out), .AluResult_IN(MEM_ALUR),
    .R1Equal22_IN(ex_mem_1_r1equal22_out), .JMP_IN(ex_mem_1_jmp_out), .JR_IN(ex_mem_1_jr_out),
    .Beq_IN(ex_mem_1_beq_out), .Bne_IN(ex_mem_1_bne_out), .AluEqual_IN(ex_mem_1_aluequal_out),
    .BLTZandAR1_IN(ex_mem_1_bltzandar1_out), .JAL_OUT(mem_wb_1_jal_out), .LB_OUT(mem_wb_1_lb_out),
    .RegW_OUT(mem_wb_1_regw_out), .PC_OUT(WB_PC), .MD_OUT(Mem_ReadData), .syscall_OUT(SYSCALL_4),
    .AluResult_OUT(WB_ALUR), .R1Equal22_OUT(R1E22_4), .A_IN(ex_mem_1_a_out), .A_OUT(mem_wb_1_a_out),
    .B_IN(ex_mem_1_b_out), .M2R_IN(ex_mem_1_m2r_out), .M2R_OUT(mem_wb_1_m2r_out), .W__IN(MEM_WR_num),
    .W__OUT(mem_wb_1_w__out));  // open: InstrCode_OUT, RegDst_OUT, JMP_OUT, JR_OUT, Beq_OUT, Bne_OUT, AluEqual_OUT, BLTZandAR1_OUT, B_OUT, En
  Multiplexer #(.width(32), .enable("false")) multiplexer_14 (
    .in0(WB_ALUR), .in1(Mem_ReadData), .out(multiplexer_14_out), .sel(mem_wb_1_m2r_out));
  not not_3 (not_3_out, mips_alu_1_equal);
  or or_10 (or_10_out, id_ex_1_jal_out, id_ex_1_jmp_out, id_ex_1_jr_out);
  and and_7 (and_7_out, id_ex_1_beq_out, mips_alu_1_equal);
  and and_8 (and_8_out, id_ex_1_bne_out, not_3_out);
  and and_9 (and_9_out, comparator_4_eq, id_ex_1_syscall_out);
  // Probe on multiplexer_10_out
  Multiplexer #(.select(2), .width(8), .enable("false")) multiplexer_15 (
    .in0(multiplexer_14_out[7:0]), .in1(multiplexer_14_out[15:8]), .in2(multiplexer_14_out[23:16]),
    .in3(multiplexer_14_out[31:24]), .out(multiplexer_15_out), .sel(WB_ALUR[1:0]));
  Counter #(.width(16), .max('hffff)) counter_3 (
    .count(or_10_out), .Q(\无条件分支数 ), .clk(CLK), .clr(RST));  // open: load, D, carry
  or or_11 (or_11_out, and_7_out, and_6_out, and_8_out);
  Register #(.width(32)) register_1 (.D(multiplexer_10_out), .en(and_9_out), .Q(LedData), .clk(CLK), .clr(RST));
  Adder #(.width(32)) adder_4 (.a(WB_PC), .b(32'h4), .out(adder_4_out));  // open: cin, cout
  Multiplexer #(.width(32), .enable("false")) multiplexer_16 (
    .in0(multiplexer_14_out), .in1(adder_4_out), .out(multiplexer_16_out), .sel(mem_wb_1_jal_out));
  assign bit_extender_4_out = {{24{multiplexer_15_out[7]}}, multiplexer_15_out};  // Bit_Extender bit_extender_4
  Counter #(.width(16), .max('hffff)) counter_4 (
    .count(or_11_out), .Q(\条件分支成功数 ), .clk(CLK), .clr(RST));  // open: load, D, carry
  Multiplexer #(.width(32), .enable("false")) multiplexer_17 (
    .in0(multiplexer_16_out), .in1(bit_extender_4_out), .out(WB_DATA), .sel(mem_wb_1_lb_out));

  // Notes on the sheet:
  //   中断源
  //   中断等待指示
  //   数码管输出
  //   contents of rom_1 (hex, n*v repeats v):
  //   20110001 8000c05 20110001 20120002 20130003 8000c09 20110001 20120002 20130003 8000c0d 20110001
  //   20120002 20130003 8000c11 20110001 20120002 20130003 c000cf8 20100001 20110001 118fc0 112020
  //   20020022 c 118882 12200001 8000c15 112020 20020022 c 20110001 118880 112020 20020022 c 12200001
  //   8000c1f 20110001 118fc0 112020 20020022 c 1188c3 112020 20020022 c 118903 112020 20020022 c 118903
  //   112020 20020022 c 118903 112020 20020022 c 118903 112020 20020022 c 118903 112020 20020022 c 118903
  //   112020 20020022 c 118903 112020 20020022 c 20100001 109fc0 139fc3 8021 2012000c 24160003 26100001
  //   3210000f 20080008 20090001 139900 2709825 132020 20020022 c 1094022 1500fff9 22100001 2018000f
  //   2188024 108700 20080008 20090001 139902 2709825 132021 20020022 c 1094022 1500fff9 108702 2c9b022
  //   12c00001 8000c50 4020 1084027 84400 3508ffff 82021 20020022 c 2010ffff 20110000 ae300000 22100001
  //   22310004 ae300000 22100001 22310004 ae300000 22100001 22310004 ae300000 22100001 22310004 ae300000
  //   22100001 22310004 ae300000 22100001 22310004 ae300000 22100001 22310004 ae300000 22100001 22310004
  //   ae300000 22100001 22310004 ae300000 22100001 22310004 ae300000 22100001 22310004 ae300000 22100001
  //   22310004 ae300000 22100001 22310004 ae300000 22100001 22310004 ae300000 22100001 22310004 ae300000
  //   22100001 22310004 22100001 8020 2011003c 8e130000 8e340000 274402a 11000002 ae330000 ae140000
  //   2231fffc 1611fff8 102020 20020022 c 22100004 2011003c 1611fff2 20020032 c 20080001 20090003 20110876
  //   112020 20020022 c 200b0008 1118804 1318804 112020 20020022 c 216bffff 1560fff9 2002000a c 20080001
  //   20110010 112020 20020022 c 200b0020 2288823 112020 20020022 c 216bffff 1560fffa 2002000a c 20090000
  //   200b0010 34118483 20120404 118c00 129400 36318281 22520404 ad310000 2328820 21290004 216bffff
  //   1560fffb 200b0020 20090000 81310000 112020 20020022 c 21290001 216bffff 1560fff9 2002000a c 2011fff1
  //   112020 20020022 c 22310001 620fffb 2002000a c 2002000a c 20100000 22100001 102020 20020022 c
  //   22100002 102020 20020022 c 22100003 102020 20020022 c 22100004 102020 20020022 c 22100005 102020
  //   20020022 c 22100006 102020 20020022 c 22100007 102020 20020022 c 22100008 102020 20020022 20020022 c
  //   3e00008
  //   指令存储器
  //   contents of rom_2 (hex, n*v repeats v):
  //   20110001 8000c05 20110001 20120002 20130003 8000c09 20110001 20120002 20130003 8000c0d 20110001
  //   20120002 20130003 8000c11 20110001 20120002 20130003 c000cf8 20100001 20110001 118fc0 112020
  //   20020022 c 118882 12200001 8000c15 112020 20020022 c 20110001 118880 112020 20020022 c 12200001
  //   8000c1f 20110001 118fc0 112020 20020022 c 1188c3 112020 20020022 c 118903 112020 20020022 c 118903
  //   112020 20020022 c 118903 112020 20020022 c 118903 112020 20020022 c 118903 112020 20020022 c 118903
  //   112020 20020022 c 118903 112020 20020022 c 20100001 109fc0 139fc3 8021 2012000c 24160003 26100001
  //   3210000f 20080008 20090001 139900 2709825 132020 20020022 c 1094022 1500fff9 22100001 2018000f
  //   2188024 108700 20080008 20090001 139902 2709825 132021 20020022 c 1094022 1500fff9 108702 2c9b022
  //   12c00001 8000c50 4020 1084027 84400 3508ffff 82021 20020022 c 2010ffff 20110000 ae300000 22100001
  //   22310004 ae300000 22100001 22310004 ae300000 22100001 22310004 ae300000 22100001 22310004 ae300000
  //   22100001 22310004 ae300000 22100001 22310004 ae300000 22100001 22310004 ae300000 22100001 22310004
  //   ae300000 22100001 22310004 ae300000 22100001 22310004 ae300000 22100001 22310004 ae300000 22100001
  //   22310004 ae300000 22100001 22310004 ae300000 22100001 22310004 ae300000 22100001 22310004 ae300000
  //   22100001 22310004 22100001 8020 2011003c 8e130000 8e340000 274402a 11000002 ae330000 ae140000
  //   2231fffc 1611fff8 102020 20020022 c 22100004 2011003c 1611fff2 20020032 c 20080001 20090003 20110876
  //   112020 20020022 c 200b0008 1118804 1318804 112020 20020022 c 216bffff 1560fff9 2002000a c 20080001
  //   20110010 112020 20020022 c 200b0020 2288823 112020 20020022 c 216bffff 1560fffa 2002000a c 20090000
  //   200b0010 34118483 20120404 118c00 129400 36318281 22520404 ad310000 2328820 21290004 216bffff
  //   1560fffb 200b0020 20090000 81310000 112020 20020022 c 21290001 216bffff 1560fff9 2002000a c 2011fff1
  //   112020 20020022 c 22310001 620fffb 2002000a c 2002000a c 20100000 22100001 102020 20020022 c
  //   22100002 102020 20020022 c 22100003 102020 20020022 c 22100004 102020 20020022 c 22100005 102020
  //   20020022 c 22100006 102020 20020022 c 22100007 102020 20020022 c 22100008 102020 20020022 20020022 c
  //   3e00008
  //   Op
  //   Func
  //   Beq
  //   Bne
  //   MemToReg
  //   MemWrite
  //   AluOP
  //   AluSrcB
  //   RegWrite
  //   RegDst
  //   流水调试日志用
endmodule

module \重定向数据相关检测  (
  input  [5:0] OP,
  input  [4:0] EX_WriteReg_num,
  input  EX_RegWrite,
  input  [4:0] MEM_WriteReg_num,
  input  MEM_RegWrite,
  input  [5:0] Func,
  input  [4:0] ID_R1_num,
  input  [4:0] ID_R2_num,
  output \R1EX数据相关 ,
  output \R1MEM数据相关 ,
  output \R2EX数据相关 ,
  output \R2MEM数据相关 
);

  wire and_1_out, and_2_out, and_3_out, and_4_out, comparator_1_eq, comparator_2_eq, comparator_3_eq,
       comparator_4_eq, comparator_5_eq, comparator_6_eq, not_1_out, not_2_out, \源寄存器使用情况_1_r1_used ,
       \源寄存器使用情况_1_r2_used ;

  \源寄存器使用情况  \u_源寄存器使用情况_1  (
    .OP0(OP[0]), .OP1(OP[1]), .OP2(OP[2]), .OP3(OP[3]), .OP4(OP[4]), .OP5(OP[5]), .F0(Func[0]), .F1(Func[1]),
    .F2(Func[2]), .F3(Func[3]), .F4(Func[4]), .F5(Func[5]), .R1_Used(\源寄存器使用情况_1_r1_used ),
    .R2_Used(\源寄存器使用情况_1_r2_used ));
  Comparator #(.width(5)) comparator_1 (.a({5{1'b0}}), .b(ID_R1_num), .eq(comparator_1_eq));  // open: gt, lt
  not not_1 (not_1_out, comparator_1_eq);
  not not_2 (not_2_out, comparator_2_eq);
  Comparator #(.width(5)) comparator_2 (.a({5{1'b0}}), .b(ID_R2_num), .eq(comparator_2_eq));  // open: gt, lt
  Comparator #(.width(5)) comparator_3 (.a(ID_R1_num), .b(EX_WriteReg_num), .eq(comparator_3_eq));  // open: gt, lt
  Comparator #(.width(5)) comparator_4 (.a(ID_R1_num), .b(MEM_WriteReg_num), .eq(comparator_4_eq));  // open: gt, lt
  Comparator #(.width(5)) comparator_5 (.a(ID_R2_num), .b(EX_WriteReg_num), .eq(comparator_5_eq));  // open: gt, lt
  Comparator #(.width(5)) comparator_6 (.a(ID_R2_num), .b(MEM_WriteReg_num), .eq(comparator_6_eq));  // open: gt, lt
  and and_1 (and_1_out, EX_RegWrite, comparator_3_eq);
  and and_2 (and_2_out, MEM_RegWrite, comparator_4_eq);
  and and_3 (and_3_out, EX_RegWrite, comparator_5_eq);
  and and_4 (and_4_out, MEM_RegWrite, comparator_6_eq);
  and and_5 (\R1EX数据相关 , not_1_out, and_1_out, \源寄存器使用情况_1_r1_used );
  and and_6 (\R1MEM数据相关 , not_1_out, and_2_out, \源寄存器使用情况_1_r1_used );
  and and_7 (\R2EX数据相关 , \源寄存器使用情况_1_r2_used , not_2_out, and_3_out);
  and and_8 (\R2MEM数据相关 , \源寄存器使用情况_1_r2_used , not_2_out, and_4_out);

  // Other names for the same wires on the sheet: OP_CODE[5:0] = OP
endmodule

module R1Forward (
  input  R1EX,
  input  R1MEM,
  output R1Forward1,
  output R1Forward2
);

  or or_1 (R1Forward2, R1MEM, R1EX);

  assign R1Forward1 = R1EX;
endmodule
module \动态分支预测  (
);

  wire and_1_out, and_2_out, and_3_out, and_4_out, and_5_out, and_6_out, and_7_out, and_8_out, and_10_out,
       and_11_out, and_12_out, and_13_out, CLK, comparator_1_eq, comparator_2_eq, comparator_3_eq,
       comparator_4_eq, comparator_5_eq, comparator_6_eq, comparator_7_eq, EN_IDEX, EX,
       ex_mem_1_aluequal_out, ex_mem_1_beq_out, ex_mem_1_bltzandar1_out, ex_mem_1_bne_out, ex_mem_1_jal_out,
       ex_mem_1_jmp_out, ex_mem_1_jr_out, ex_mem_1_lb_out, ex_mem_1_m2r_out, ex_mem_1_memw_out,
       ex_mem_1_r1equal22_out, ex_mem_1_regdst_out, ex_mem_1_syscall_out, EX_RW, Go, Hit, id_ex_1_alusrc_out,
       id_ex_1_beq_out, id_ex_1_bltz_out, id_ex_1_bne_out, id_ex_1_jal_out, id_ex_1_jmp_out, id_ex_1_jr_out,
       id_ex_1_lb_out, id_ex_1_m2r_out, id_ex_1_memw_out, id_ex_1_r1equal22_out, id_ex_1_regdst_out,
       id_ex_1_sllv_out, id_ex_1_syscall_out, IR1, IR2, IR3, LoadUse, MEM_RW, mem_wb_1_jal_out,
       mem_wb_1_lb_out, mem_wb_1_m2r_out, mem_wb_1_regw_out, mips_alu_1_equal, Miss, not_1_out, not_2_out,
       not_3_out, or_1_out, or_3_out, or_4_out, or_5_out, or_6_out, or_7_out, or_8_out, or_9_out, or_10_out,
       or_11_out, R1E22_4, R1EX, r1forward_1_r1forward1, r1forward_1_r1forward2, r1forward_2_r1forward1,
       r1forward_2_r1forward2, R1MEM, R2EX, R2MEM, RST, SignedExt, SYSCALL_4, Take_branch,
       two_level_adaptive_training_1_pre_take_branch, W1, W2, W3, \条件跳转 , \硬布线控制器_1_alu_src , \硬布线控制器_1_beq ,
       \硬布线控制器_1_bltz , \硬布线控制器_1_bne , \硬布线控制器_1_jal , \硬布线控制器_1_jmp , \硬布线控制器_1_jr , \硬布线控制器_1_lb ,
       \硬布线控制器_1_memtoreg , \硬布线控制器_1_memwrite , \硬布线控制器_1_regdst , \硬布线控制器_1_regwrite , \硬布线控制器_1_sllv ,
       \硬布线控制器_1_syscall ;
  wire [1:0] id_ex_1_bltzandar1_out, id_ex_1_r2f2_out;
  wire [3:0] id_ex_1_aluop_out, \硬布线控制器_1_alu_op ;
  wire [4:0] EX_WR_num, mem_wb_1_w__out, MEM_WR_num, multiplexer_7_out, multiplexer_8_out, multiplexer_9_out,
       multiplexer_10_out, multiplexer_16_out;
  wire [5:0] id_ex_1_instrcode_out_2, if_id_1_instrcode_out;
  wire [7:0] multiplexer_18_out;
  wire [15:0] \Hit次数 , \LoadUse次数 , \Miss次数 , \总周期数 , \插入气泡数 , \无条件分支数 , \条件分支成功数 ;
  wire [27:2] id_ex_1_instrcode_out;
  wire [31:0] adder_1_out, adder_2_out, adder_3_out, adder_4_out, adder_5_out, bit_extender_1_out,
       bit_extender_2_out, bit_extender_3_out, bit_extender_4_out, BRANCH_ADDR, ex_mem_1_a_out,
       ex_mem_1_b_out, ex_mem_1_instrcode_out, EX_PC, id_ex_1_a_out, id_ex_1_b_out, id_ex_1_imm_out, ID_PC,
       IF_PC, LedData, MEM_ALUR, MEM_PC, Mem_ReadData, mem_wb_1_a_out, mips_alu_1_result, mips_regifile_1_r1,
       mips_regifile_1_r2, multiplexer_1_out, multiplexer_2_out, multiplexer_3_out, multiplexer_4_out,
       multiplexer_5_out, multiplexer_6_out, multiplexer_11_out, multiplexer_12_out, multiplexer_13_out,
       multiplexer_14_out, multiplexer_15_out, multiplexer_17_out, multiplexer_19_out, ram_1_data,
       rom_2_data, shifter_1_out, WB_ALUR, WB_DATA, WB_PC;
  wire [31:6] if_id_1_instrcode_out_2;

  Button \u_总复位  (.out(RST));
  Button _1 (.out(IR1));
  Button _2 (.out(IR2));
  Button _3 (.out(IR3));
  Multiplexer #(.width(32), .enable("false")) multiplexer_1 (
    .in0(adder_2_out), .in1(adder_4_out), .out(multiplexer_1_out), .sel(\条件跳转 ));
  Button \u_继续运行  (.out(Go));
  LED led_1 (.in(W1));
  LED led_2 (.in(W2));
  LED led_3 (.in(W3));
  or or_1 (or_1_out, id_ex_1_jmp_out, id_ex_1_jal_out);
  Multiplexer #(.width(32), .enable("false")) multiplexer_2 (
    .in0(multiplexer_1_out), .in1(multiplexer_12_out), .out(multiplexer_2_out), .sel(id_ex_1_jr_out));
  Multiplexer #(.width(32), .enable("false")) multiplexer_3 (
    .in0(multiplexer_2_out), .in1({IF_PC[31:28], id_ex_1_instrcode_out, 2'b00}), .out(multiplexer_3_out),
    .sel(or_1_out));
  and and_1 (and_1_out, Miss, ~\条件跳转 , two_level_adaptive_training_1_pre_take_branch);  // AND_Gate
  Hex_Digit_Display hex_digit_display_1 (.value(LedData[31:28]));  // open: dp
  or or_2 (EN_IDEX, not_1_out, or_3_out);
  and and_2 (and_2_out, Hit, two_level_adaptive_training_1_pre_take_branch);
  Multiplexer #(.width(32), .enable("false")) multiplexer_4 (
    .in0(multiplexer_3_out), .in1(adder_2_out), .out(multiplexer_4_out), .sel(and_2_out));
  Multiplexer #(.width(32), .enable("false")) multiplexer_5 (
    .in0(multiplexer_4_out), .in1(BRANCH_ADDR), .out(multiplexer_5_out), .sel(Take_branch));
  Multiplexer #(.width(32), .enable("false")) multiplexer_6 (
    .in0(multiplexer_5_out), .in1(adder_1_out), .out(multiplexer_6_out), .sel(and_1_out));
  Adder #(.width(32)) adder_1 (.a(EX_PC), .b(32'h4), .out(adder_1_out));  // open: cin, cout
  Hex_Digit_Display hex_digit_display_2 (.value(LedData[27:24]));  // open: dp
  Hex_Digit_Display hex_digit_display_3 (.value(LedData[23:20]));  // open: dp
  Counter #(.width(16), .max('hffff), .trigger("falling")) counter_1 (
    .count(and_1_out), .Q(\Miss次数 ), .clk(CLK), .clr(RST));  // open: load, D, carry
  Counter #(.width(16), .max('hffff), .trigger("falling")) counter_2 (
    .count(and_2_out), .Q(\Hit次数 ), .clk(CLK), .clr(RST));  // open: load, D, carry
  not not_1 (not_1_out, id_ex_1_syscall_out);
  or or_3 (or_3_out, and_3_out, Go);
  Register #(.width(32)) PC (.D(multiplexer_6_out), .en(and_6_out), .Q(IF_PC), .clk(CLK), .clr(RST));
  or or_4 (or_4_out, and_4_out, Go);
  or or_5 (or_5_out, not_2_out, or_4_out);
  Hex_Digit_Display hex_digit_display_4 (.value(LedData[19:16]));  // open: dp
  Hex_Digit_Display hex_digit_display_5 (.value(LedData[15:12]));  // open: dp
  ROM #(.addrWidth(10), .dataWidth(32)) rom_1 ();  // open: addr, data, sel
  and and_3 (and_3_out, id_ex_1_syscall_out, comparator_4_eq);
  Adder #(.width(32)) adder_2 (.a(IF_PC), .b(32'h4), .out(adder_2_out));  // open: cin, cout
  not not_2 (not_2_out, SYSCALL_4);
  and and_4 (and_4_out, SYSCALL_4, R1E22_4);
  Hex_Digit_Display hex_digit_display_6 (.value(LedData[11:8]));  // open: dp
  Hex_Digit_Display hex_digit_display_7 (.value(LedData[7:4]));  // open: dp
  Clock clock_1 (.out(CLK));
  Two_Level_Adaptive_Training two_level_adaptive_training_1 (
    .PC(rom_2_data), .PRE_PC({id_ex_1_instrcode_out_2, id_ex_1_instrcode_out}),
    .PRE_BRANCH_ADDR(multiplexer_3_out), .BRANCH_ADDRESS(BRANCH_ADDR), .TAKE_BRANCH(Take_branch),
    .MISS(Miss), .HIT(Hit), .PRE_TAKE_BRANCH(two_level_adaptive_training_1_pre_take_branch), .clk(CLK),
    .rst(RST), .EXIST(EX));
  ROM #(.addrWidth(10), .dataWidth(32)) rom_2 (.addr(IF_PC[11:2]), .data(rom_2_data));  // open: sel
  Hex_Digit_Display hex_digit_display_8 (.value(LedData[3:0]));  // open: dp
  and and_5 (and_5_out, Miss, two_level_adaptive_training_1_pre_take_branch);
  and and_6 (and_6_out, ~LoadUse, EN_IDEX);  // AND_Gate
  Counter #(.width(16), .max('hffff)) counter_3 (
    .count(or_5_out), .Q(\总周期数 ), .clk(CLK), .clr(RST));  // open: load, D, carry
  IF_ID if_id_1 (
    .rst(or_6_out), .clk(CLK), .InstrCode_IN(rom_2_data), .PC_IN(IF_PC),
    .InstrCode_OUT({if_id_1_instrcode_out_2, if_id_1_instrcode_out}), .PC_OUT(ID_PC), .En(and_6_out));
  Adder #(.width(32)) adder_3 (.a(32'h4), .b(EX_PC), .out(adder_3_out));  // open: cin, cout
  // Probe on \总周期数 
  // Probe on \无条件分支数 
  // Probe on \条件分支成功数 
  // Probe on \插入气泡数 
  // Probe on \LoadUse次数 
  \重定向数据相关检测  \u_重定向数据相关检测_1  (
    .OP(if_id_1_instrcode_out_2[31:26]), .EX_WriteReg_num(EX_WR_num), .EX_RegWrite(EX_RW),
    .MEM_WriteReg_num(MEM_WR_num), .MEM_RegWrite(MEM_RW), .Func(if_id_1_instrcode_out),
    .ID_R1_num(multiplexer_9_out), .ID_R2_num(multiplexer_10_out), .\R1EX数据相关 (R1EX), .\R1MEM数据相关 (R1MEM),
    .\R2EX数据相关 (R2EX), .\R2MEM数据相关 (R2MEM));
  Adder #(.width(32)) adder_4 (.a(adder_3_out), .b(shifter_1_out), .out(adder_4_out));  // open: cin, cout
  // Probe on IF_PC[11:0]
  // Probe on ID_PC[11:0]
  \硬布线控制器  \u_硬布线控制器_1  (
    .OP(if_id_1_instrcode_out_2[31:26]), .Func(if_id_1_instrcode_out), .ALU_OP(\硬布线控制器_1_alu_op ),
    .MemToReg(\硬布线控制器_1_memtoreg ), .MemWrite(\硬布线控制器_1_memwrite ), .ALU_SRC(\硬布线控制器_1_alu_src ),
    .RegWrite(\硬布线控制器_1_regwrite ), .SysCALL(\硬布线控制器_1_syscall ), .SignedExt(SignedExt),
    .RegDst(\硬布线控制器_1_regdst ), .Beq(\硬布线控制器_1_beq ), .Bne(\硬布线控制器_1_bne ), .JR(\硬布线控制器_1_jr ),
    .JMP(\硬布线控制器_1_jmp ), .JAL(\硬布线控制器_1_jal ), .SLLV(\硬布线控制器_1_sllv ), .LB(\硬布线控制器_1_lb ),
    .BLTZ(\硬布线控制器_1_bltz ));  // open: MFC0, MTC0, ERET, RS
  Multiplexer #(.width(5), .enable("false")) multiplexer_7 (
    .in0(if_id_1_instrcode_out_2[20:16]), .in1(if_id_1_instrcode_out_2[15:11]), .out(multiplexer_7_out),
    .sel(\硬布线控制器_1_regdst ));
  Multiplexer #(.width(5), .enable("false")) multiplexer_8 (
    .in0(multiplexer_7_out), .in1({5{1'b1}}), .out(multiplexer_8_out), .sel(\硬布线控制器_1_jal ));
  Comparator #(.width(5)) comparator_1 (.a(multiplexer_10_out), .b(EX_WR_num), .eq(comparator_1_eq));  // open: gt, lt
  Comparator #(.width(5)) comparator_2 (.a(multiplexer_9_out), .b(EX_WR_num), .eq(comparator_2_eq));  // open: gt, lt
  assign bit_extender_1_out = {{16{1'b0}}, {if_id_1_instrcode_out_2[15:6], if_id_1_instrcode_out}};  // Bit_Extender bit_extender_1
  assign bit_extender_2_out = {{16{if_id_1_instrcode_out_2[15]}}, {if_id_1_instrcode_out_2[15:6], if_id_1_instrcode_out}};  // Bit_Extender bit_extender_2
  // Probe on EX_PC[11:0]
  // Probe on MEM_PC[11:0]
  and and_7 (and_7_out, or_8_out, ~Hit);  // AND_Gate
  or or_6 (or_6_out, and_5_out, and_7_out);
  Multiplexer #(.width(5), .enable("false")) multiplexer_9 (
    .in0(if_id_1_instrcode_out_2[25:21]), .in1(5'b00010), .out(multiplexer_9_out), .sel(\硬布线控制器_1_syscall ));
  and and_8 (and_8_out, \硬布线控制器_1_syscall , comparator_3_eq);
  Multiplexer #(.width(5), .enable("false")) multiplexer_10 (
    .in0(if_id_1_instrcode_out_2[20:16]), .in1(5'b00100), .out(multiplexer_10_out), .sel(and_8_out));
  or or_7 (or_7_out, comparator_1_eq, comparator_2_eq);
  and and_9 (LoadUse, or_10_out, or_7_out);
  // Probe on WB_PC[11:0]
  R1Forward r1forward_1 (
    .R1EX(R1EX), .R1MEM(R1MEM), .R1Forward1(r1forward_1_r1forward1), .R1Forward2(r1forward_1_r1forward2));
  R1Forward r1forward_2 (
    .R1EX(R2EX), .R1MEM(R2MEM), .R1Forward1(r1forward_2_r1forward1), .R1Forward2(r1forward_2_r1forward2));
  Multiplexer #(.width(32), .enable("false")) multiplexer_11 (
    .in0(bit_extender_1_out), .in1(bit_extender_2_out), .out(multiplexer_11_out), .sel(SignedExt));
  Shifter #(.width(32)) shifter_1 (.in(bit_extender_3_out), .\dist (5'b00010), .out(shifter_1_out));
  // Probe on \Hit次数 
  Counter #(.width(16), .max('hffff)) counter_4 (
    .count(LoadUse), .Q(\LoadUse次数 ), .clk(CLK), .clr(RST));  // open: load, D, carry
  MIPS_Regifile mips_regifile_1 (
    .Din(WB_DATA), .Clk(CLK), .R1(mips_regifile_1_r1), .R2(mips_regifile_1_r2), .WE(mem_wb_1_regw_out),
    .W_num(mem_wb_1_w__out), .R1_num(multiplexer_9_out), .R2_num(multiplexer_10_out));
  // Probe on \Miss次数 
  Comparator #(.width(32)) comparator_3 (.a(32'h22), .b(mips_regifile_1_r1), .eq(comparator_3_eq));  // open: gt, lt
  or or_8 (or_8_out, or_11_out, \条件跳转 );
  or or_9 (or_9_out, LoadUse, or_6_out);
  ID_EX id_ex_1 (
    .rst(or_9_out), .clk(CLK), .JAL_IN(\硬布线控制器_1_jal ),
    .InstrCode_IN({if_id_1_instrcode_out_2, if_id_1_instrcode_out}), .A_IN(mips_regifile_1_r1),
    .LB_IN(\硬布线控制器_1_lb ), .RegW_IN(\硬布线控制器_1_regwrite ), .PC_IN(ID_PC), .B_IN(mips_regifile_1_r2),
    .RegDst_IN(\硬布线控制器_1_regdst ), .syscall_IN(\硬布线控制器_1_syscall ), .Imm_IN(multiplexer_11_out),
    .R1Equal22_IN(comparator_3_eq), .JMP_IN(\硬布线控制器_1_jmp ), .JR_IN(\硬布线控制器_1_jr ), .Beq_IN(\硬布线控制器_1_beq ),
    .Bne_IN(\硬布线控制器_1_bne ), .AluEqual_IN(r1forward_1_r1forward1), .BLTZandAR1_IN(r1forward_1_r1forward2),
    .MemW_IN(\硬布线控制器_1_memwrite ), .AluOP_IN(\硬布线控制器_1_alu_op ), .AluSrc_IN(\硬布线控制器_1_alu_src ),
    .BLTZ_IN(\硬布线控制器_1_bltz ), .SLLV_IN(\硬布线控制器_1_sllv ), .SignedExt_IN(r1forward_2_r1forward1),
    .JAL_OUT(id_ex_1_jal_out), .InstrCode_OUT({id_ex_1_instrcode_out_2, id_ex_1_instrcode_out}),
    .A_OUT(id_ex_1_a_out), .LB_OUT(id_ex_1_lb_out), .RegW_OUT(EX_RW), .PC_OUT(EX_PC), .B_OUT(id_ex_1_b_out),
    .RegDst_OUT(id_ex_1_regdst_out), .syscall_OUT(id_ex_1_syscall_out), .Imm_OUT(id_ex_1_imm_out),
    .R1Equal22_OUT(id_ex_1_r1equal22_out), .JMP_OUT(id_ex_1_jmp_out), .JR_OUT(id_ex_1_jr_out),
    .Beq_OUT(id_ex_1_beq_out), .Bne_OUT(id_ex_1_bne_out), .AluEqual_OUT(id_ex_1_bltzandar1_out[1]),
    .BLTZandAR1_OUT(id_ex_1_bltzandar1_out[0]), .MemW_OUT(id_ex_1_memw_out), .AluOP_OUT(id_ex_1_aluop_out),
    .AluSrc_OUT(id_ex_1_alusrc_out), .BLTZ_OUT(id_ex_1_bltz_out), .SLLV_OUT(id_ex_1_sllv_out),
    .SignedExt_OUT(id_ex_1_r2f2_out[1]), .M2R_IN(\硬布线控制器_1_memtoreg ), .M2R_OUT(id_ex_1_m2r_out),
    .W__IN(multiplexer_8_out), .W__OUT(EX_WR_num), .En(EN_IDEX), .R2F2_IN(r1forward_2_r1forward2),
    .R2F2_OUT(id_ex_1_r2f2_out[0]));
  Multiplexer #(.select(2), .width(32), .enable("false")) multiplexer_12 (
    .in0(id_ex_1_a_out), .in1(WB_DATA), .in3(MEM_ALUR), .out(multiplexer_12_out), .sel(id_ex_1_bltzandar1_out));  // open: in2
  Multiplexer #(.select(2), .width(32), .enable("false")) multiplexer_13 (
    .in0(id_ex_1_b_out), .in1(WB_DATA), .in3(MEM_ALUR), .out(multiplexer_13_out), .sel(id_ex_1_r2f2_out));  // open: in2
  assign bit_extender_3_out = {{16{id_ex_1_instrcode_out[17]}}, id_ex_1_instrcode_out[17:2]};  // Bit_Extender bit_extender_3
  Comparator #(.width(32)) comparator_4 (.a(32'h22), .b(multiplexer_12_out), .eq(comparator_4_eq));  // open: gt, lt
  Multiplexer #(.width(32), .enable("false")) multiplexer_14 (
    .in0(multiplexer_13_out), .in1(id_ex_1_imm_out), .out(multiplexer_14_out), .sel(id_ex_1_alusrc_out));
  Multiplexer #(.width(32), .enable("false")) multiplexer_15 (
    .in0(multiplexer_14_out), .in1({32{1'b0}}), .out(multiplexer_15_out), .sel(id_ex_1_bltz_out));
  Comparator #(.width(6)) comparator_5 (
    .a(id_ex_1_instrcode_out_2), .b(6'b100011), .eq(comparator_5_eq));  // open: gt, lt
  Comparator #(.width(6)) comparator_6 (
    .a(id_ex_1_instrcode_out_2), .b(6'b100000), .eq(comparator_6_eq));  // open: gt, lt
  MIPS_ALU mips_alu_1 (
    .X(multiplexer_12_out), .Y(multiplexer_15_out), .AluOP(id_ex_1_aluop_out), .Equal(mips_alu_1_equal),
    .Result(mips_alu_1_result), .shamt(multiplexer_16_out));  // open: Result_2
  Multiplexer #(.width(5), .enable("false")) multiplexer_16 (
    .in0(id_ex_1_instrcode_out[12:8]), .in1(id_ex_1_a_out[4:0]), .out(multiplexer_16_out),
    .sel(id_ex_1_sllv_out));
  or or_10 (or_10_out, comparator_5_eq, comparator_6_eq);
  Comparator #(.width(32)) comparator_7 (.a(mips_alu_1_result), .b(32'h1), .eq(comparator_7_eq));  // open: gt, lt
  and and_10 (and_10_out, comparator_7_eq, id_ex_1_bltz_out);
  EX_MEM ex_mem_1 (
    .rst(RST), .clk(CLK), .JAL_IN(id_ex_1_jal_out),
    .InstrCode_IN({id_ex_1_instrcode_out_2, id_ex_1_instrcode_out}), .LB_IN(id_ex_1_lb_out), .RegW_IN(EX_RW),
    .PC_IN(EX_PC), .B_IN(multiplexer_13_out), .RegDst_IN(id_ex_1_regdst_out),
    .syscall_IN(id_ex_1_syscall_out), .AluResult_IN(mips_alu_1_result), .R1Equal22_IN(comparator_4_eq),
    .JMP_IN(id_ex_1_jmp_out), .JR_IN(id_ex_1_jr_out), .Beq_IN(id_ex_1_beq_out), .Bne_IN(id_ex_1_bne_out),
    .AluEqual_IN(mips_alu_1_equal), .BLTZandAR1_IN(and_10_out), .MemW_IN(id_ex_1_memw_out),
    .JAL_OUT(ex_mem_1_jal_out), .InstrCode_OUT(ex_mem_1_instrcode_out), .LB_OUT(ex_mem_1_lb_out),
    .RegW_OUT(MEM_RW), .PC_OUT(MEM_PC), .B_OUT(ex_mem_1_b_out), .RegDst_OUT(ex_mem_1_regdst_out),
    .syscall_OUT(ex_mem_1_syscall_out), .AluResult_OUT(MEM_ALUR), .R1Equal22_OUT(ex_mem_1_r1equal22_out),
    .JMP_OUT(ex_mem_1_jmp_out), .JR_OUT(ex_mem_1_jr_out), .Beq_OUT(ex_mem_1_beq_out),
    .Bne_OUT(ex_mem_1_bne_out), .AluEqual_OUT(ex_mem_1_aluequal_out),
    .BLTZandAR1_OUT(ex_mem_1_bltzandar1_out), .MemW_OUT(ex_mem_1_memw_out), .A_IN(multiplexer_12_out),
    .A_OUT(ex_mem_1_a_out), .M2R_IN(id_ex_1_m2r_out), .M2R_OUT(ex_mem_1_m2r_out), .W__IN(EX_WR_num),
    .W__OUT(MEM_WR_num));  // open: En
  // Probe on ex_mem_1_b_out
  RAM #(.addrWidth(10), .dataWidth(32), .bus("separate")) ram_1 (
    .addr(MEM_ALUR[11:2]), .din(ex_mem_1_b_out), .data(ram_1_data), .str(ex_mem_1_memw_out), .clk(CLK),
    .clr(RST));  // open: sel, ld
  MEM_WB mem_wb_1 (
    .rst(RST), .clk(CLK), .JAL_IN(ex_mem_1_jal_out), .InstrCode_IN(ex_mem_1_instrcode_out),
    .LB_IN(ex_mem_1_lb_out), .RegW_IN(MEM_RW), .PC_IN(MEM_PC), .MD_IN(ram_1_data),
    .RegDst_IN(ex_mem_1_regdst_out), .syscall_IN(ex_mem_1_syscall_out), .AluResult_IN(MEM_ALUR),
    .R1Equal22_IN(ex_mem_1_r1equal22_out), .JMP_IN(ex_mem_1_jmp_out), .JR_IN(ex_mem_1_jr_out),
    .Beq_IN(ex_mem_1_beq_out), .Bne_IN(ex_mem_1_bne_out), .AluEqual_IN(ex_mem_1_aluequal_out),
    .BLTZandAR1_IN(ex_mem_1_bltzandar1_out), .JAL_OUT(mem_wb_1_jal_out), .LB_OUT(mem_wb_1_lb_out),
    .RegW_OUT(mem_wb_1_regw_out), .PC_OUT(WB_PC), .MD_OUT(Mem_ReadData), .syscall_OUT(SYSCALL_4),
    .AluResult_OUT(WB_ALUR), .R1Equal22_OUT(R1E22_4), .A_IN(ex_mem_1_a_out), .A_OUT(mem_wb_1_a_out),
    .B_IN(ex_mem_1_b_out), .M2R_IN(ex_mem_1_m2r_out), .M2R_OUT(mem_wb_1_m2r_out), .W__IN(MEM_WR_num),
    .W__OUT(mem_wb_1_w__out));  // open: InstrCode_OUT, RegDst_OUT, JMP_OUT, JR_OUT, Beq_OUT, Bne_OUT, AluEqual_OUT, BLTZandAR1_OUT, B_OUT, En
  Multiplexer #(.width(32), .enable("false")) multiplexer_17 (
    .in0(WB_ALUR), .in1(Mem_ReadData), .out(multiplexer_17_out), .sel(mem_wb_1_m2r_out));
  not not_3 (not_3_out, mips_alu_1_equal);
  or or_11 (or_11_out, id_ex_1_jal_out, id_ex_1_jmp_out, id_ex_1_jr_out);
  and and_11 (and_11_out, id_ex_1_beq_out, mips_alu_1_equal);
  and and_12 (and_12_out, id_ex_1_bne_out, not_3_out);
  and and_13 (and_13_out, comparator_4_eq, id_ex_1_syscall_out);
  // Probe on multiplexer_13_out
  Multiplexer #(.select(2), .width(8), .enable("false")) multiplexer_18 (
    .in0(multiplexer_17_out[7:0]), .in1(multiplexer_17_out[15:8]), .in2(multiplexer_17_out[23:16]),
    .in3(multiplexer_17_out[31:24]), .out(multiplexer_18_out), .sel(WB_ALUR[1:0]));
  Counter #(.width(16), .max('hffff)) counter_5 (
    .count(or_11_out), .Q(\无条件分支数 ), .clk(CLK), .clr(RST));  // open: load, D, carry
  or or_12 (\条件跳转 , and_11_out, and_10_out, and_12_out);
  Register #(.width(32)) register_1 (.D(multiplexer_13_out), .en(and_13_out), .Q(LedData), .clk(CLK), .clr(RST));
  Adder #(.width(32)) adder_5 (.a(WB_PC), .b(32'h4), .out(adder_5_out));  // open: cin, cout
  Multiplexer #(.width(32), .enable("false")) multiplexer_19 (
    .in0(multiplexer_17_out), .in1(adder_5_out), .out(multiplexer_19_out), .sel(mem_wb_1_jal_out));
  assign bit_extender_4_out = {{24{multiplexer_18_out[7]}}, multiplexer_18_out};  // Bit_Extender bit_extender_4
  Counter #(.width(16), .max('hffff)) counter_6 (
    .count(\条件跳转 ), .Q(\条件分支成功数 ), .clk(CLK), .clr(RST));  // open: load, D, carry
  Multiplexer #(.width(32), .enable("false")) multiplexer_20 (
    .in0(multiplexer_19_out), .in1(bit_extender_4_out), .out(WB_DATA), .sel(mem_wb_1_lb_out));

  // Notes on the sheet:
  //   中断源
  //   中断等待指示
  //   数码管输出
  //   指令存储器
  //   contents of rom_2 (hex, n*v repeats v):
  //   20110001 8000c05 20110001 20120002 20130003 8000c09 20110001 20120002 20130003 8000c0d 20110001
  //   20120002 20130003 8000c11 20110001 20120002 20130003 c000cf8 20100001 20110001 118fc0 112020
  //   20020022 c 118882 12200001 8000c15 112020 20020022 c 20110001 118880 112020 20020022 c 12200001
  //   8000c1f 20110001 118fc0 112020 20020022 c 1188c3 112020 20020022 c 118903 112020 20020022 c 118903
  //   112020 20020022 c 118903 112020 20020022 c 118903 112020 20020022 c 118903 112020 20020022 c 118903
  //   112020 20020022 c 118903 112020 20020022 c 20100001 109fc0 139fc3 8021 2012000c 24160003 26100001
  //   3210000f 20080008 20090001 139900 2709825 132020 20020022 c 1094022 1500fff9 22100001 2018000f
  //   2188024 108700 20080008 20090001 139902 2709825 132021 20020022 c 1094022 1500fff9 108702 2c9b022
  //   12c00001 8000c50 4020 1084027 84400 3508ffff 82021 20020022 c 2010ffff 20110000 ae300000 22100001
  //   22310004 ae300000 22100001 22310004 ae300000 22100001 22310004 ae300000 22100001 22310004 ae300000
  //   22100001 22310004 ae300000 22100001 22310004 ae300000 22100001 22310004 ae300000 22100001 22310004
  //   ae300000 22100001 22310004 ae300000 22100001 22310004 ae300000 22100001 22310004 ae300000 22100001
  //   22310004 ae300000 22100001 22310004 ae300000 22100001 22310004 ae300000 22100001 22310004 ae300000
  //   22100001 22310004 22100001 8020 2011003c 8e130000 8e340000 274402a 11000002 ae330000 ae140000
  //   2231fffc 1611fff8 102020 20020022 c 22100004 2011003c 1611fff2 20020032 c 20080001 20090003 20110876
  //   112020 20020022 c 200b0008 1118804 1318804 112020 20020022 c 216bffff 1560fff9 2002000a c 20080001
  //   20110010 112020 20020022 c 200b0020 2288823 112020 20020022 c 216bffff 1560fffa 2002000a c 20090000
  //   200b0010 34118483 20120404 118c00 129400 36318281 22520404 ad310000 2328820 21290004 216bffff
  //   1560fffb 200b0020 20090000 81310000 112020 20020022 c 21290001 216bffff 1560fff9 2002000a c 2011fff1
  //   112020 20020022 c 22310001 620fffb 2002000a c 2002000a c 20100000 22100001 102020 20020022 c
  //   22100002 102020 20020022 c 22100003 102020 20020022 c 22100004 102020 20020022 c 22100005 102020
  //   20020022 c 22100006 102020 20020022 c 22100007 102020 20020022 c 22100008 102020 20020022 20020022 c
  //   3e00008
  //   Op
  //   Func
  //   Beq
  //   Bne
  //   MemToReg
  //   MemWrite
  //   AluOP
  //   AluSrcB
  //   RegWrite
  //   RegDst
  //   流水调试日志用
endmodule

module Two_Level_Adaptive_Training (
  input  clk,
  input  rst,
  input  [31:0] PC,
  input  [31:0] PRE_PC,
  input  [31:0] PRE_BRANCH_ADDR,
  output EXIST,
  output [31:0] BRANCH_ADDRESS,
  output TAKE_BRANCH,
  output MISS,
  output HIT,
  output PRE_TAKE_BRANCH
);

  wire adder_1_cout, adder_2_cout, adder_3_cout, adder_4_cout, adder_5_cout, adder_6_cout, adder_7_cout,
       adder_8_cout, and_1_out, and_2_out, and_22_out, and_23_out, and_24_out, and_25_out, and_26_out,
       and_27_out, and_28_out, and_29_out, and_30_out, and_35_out, and_36_out, and_37_out, and_38_out,
       and_39_out, and_40_out, and_41_out, and_42_out, BRANCH0, BRANCH1, BRANCH2, BRANCH3, clr_LRU0,
       clr_LRU1, clr_LRU2, clr_LRU3, comparator_1_eq, comparator_2_eq, comparator_3_eq, comparator_4_eq,
       comparator_5_eq, comparator_6_eq, comparator_7_eq, comparator_8_eq, comparator_9_eq, comparator_10_eq,
       comparator_11_eq, comparator_12_eq, comparator_13_eq, comparator_14_eq, comparator_15_eq,
       comparator_16_eq, comparator_17_eq, comparator_18_eq, comparator_19_eq, comparator_20_eq,
       comparator_21_eq, comparator_22_eq, comparator_23_eq, decoder_1_out0, decoder_1_out1, decoder_1_out2,
       decoder_1_out3, Fix_LRU0, Fix_LRU1, Fix_LRU2, Fix_LRU3, not_1_out, not_2_out, not_3_out, not_4_out,
       not_5_out, not_6_out, not_7_out, not_8_out, not_9_out, or_1_out, or_2_out, or_4_out, or_5_out,
       or_6_out, or_7_out, or_8_out, or_9_out, or_10_out, or_11_out, or_16_out, or_17_out, or_18_out,
       or_19_out, or_20_out, or_21_out, or_22_out, or_23_out, PRE_BRANCH0, PRE_BRANCH1, PRE_BRANCH2,
       PRE_BRANCH3, Set, Set0, Set1, Set2, Set3, subtractor_1_bout, subtractor_2_bout, subtractor_3_bout,
       subtractor_4_bout, Use_State0, Use_State1, Use_State2, Use_State3, V0, V1, V2, V3;
  wire [0:0] multiplexer_13_out, multiplexer_16_out;
  wire [1:0] adder_5_out, adder_6_out, adder_7_out, adder_8_out, B_State0, B_State1, B_State2, B_State3,
       max2_1_max_num, max2_2_max_num, max2_3_max_num, multiplexer_2_out, multiplexer_4_out,
       multiplexer_6_out, multiplexer_9_out, multiplexer_10_out, multiplexer_14_out, multiplexer_21_out,
       multiplexer_22_out, multiplexer_23_out, multiplexer_24_out, multiplexer_29_out, multiplexer_30_out,
       multiplexer_31_out, multiplexer_32_out, multiplexer_33_out, New_B_State0, New_B_State1, New_B_State2,
       New_B_State3, priority_encoder_1_out, subtractor_1_out, subtractor_2_out, subtractor_3_out,
       subtractor_4_out;
  wire [15:0] adder_1_out, adder_2_out, adder_3_out, adder_4_out, LRU0, LRU1, LRU2, LRU3, max2_1_max,
       max2_2_max, multiplexer_25_out, multiplexer_26_out, multiplexer_27_out, multiplexer_28_out, New_LRU0,
       New_LRU1, New_LRU2, New_LRU3;
  wire [31:0] Branch_Addr0, Branch_Addr1, Branch_Addr2, Branch_Addr3, multiplexer_1_out, multiplexer_3_out,
       multiplexer_5_out, multiplexer_7_out, multiplexer_8_out, multiplexer_11_out, multiplexer_15_out,
       Pre_PC0, Pre_PC1, Pre_PC2, Pre_PC3;

  // Probe on PC
  Comparator #(.width(32)) comparator_1 (.a(PC), .b(Pre_PC0), .eq(comparator_1_eq));  // open: gt, lt
  Comparator #(.width(32)) comparator_2 (.a(PC), .b(Pre_PC1), .eq(comparator_2_eq));  // open: gt, lt
  Comparator #(.width(32)) comparator_3 (.a(PC), .b(Pre_PC2), .eq(comparator_3_eq));  // open: gt, lt
  Comparator #(.width(32)) comparator_4 (.a(PC), .b(Pre_PC3), .eq(comparator_4_eq));  // open: gt, lt
  Multiplexer #(.width(32), .enable("false")) multiplexer_1 (
    .in0({32{1'b0}}), .in1(Branch_Addr0), .out(multiplexer_1_out), .sel(BRANCH0));
  Multiplexer #(.width(2), .enable("false")) multiplexer_2 (
    .in0(2'b00), .in1(B_State0), .out(multiplexer_2_out), .sel(BRANCH0));
  Comparator #(.width(6)) comparator_5 (.a(PC[31:26]), .b({6{1'b0}}), .eq(comparator_5_eq));  // open: gt, lt
  Comparator #(.width(6)) comparator_6 (.a(PC[5:0]), .b(6'b001000), .eq(comparator_6_eq));  // open: gt, lt
  Comparator #(.width(6)) comparator_7 (.a(PC[31:26]), .b(6'b000010), .eq(comparator_7_eq));  // open: gt, lt
  Comparator #(.width(6)) comparator_8 (.a(PC[31:26]), .b(6'b000011), .eq(comparator_8_eq));  // open: gt, lt
  Comparator #(.width(6)) comparator_9 (.a(PC[31:26]), .b(6'b000100), .eq(comparator_9_eq));  // open: gt, lt
  Comparator #(.width(6)) comparator_10 (.a(PC[31:26]), .b(6'b000101), .eq(comparator_10_eq));  // open: gt, lt
  Comparator #(.width(6)) comparator_11 (.a(PC[31:26]), .b(6'b000001), .eq(comparator_11_eq));  // open: gt, lt
  Multiplexer #(.width(32), .enable("false")) multiplexer_3 (
    .in0(multiplexer_1_out), .in1(Branch_Addr1), .out(multiplexer_3_out), .sel(BRANCH1));
  Multiplexer #(.width(2), .enable("false")) multiplexer_4 (
    .in0(multiplexer_2_out), .in1(B_State1), .out(multiplexer_4_out), .sel(BRANCH1));
  Comparator #(.width(6)) comparator_12 (.a(PRE_PC[31:26]), .b({6{1'b0}}), .eq(comparator_12_eq));  // open: gt, lt
  Comparator #(.width(6)) comparator_13 (.a(PRE_PC[5:0]), .b(6'b001000), .eq(comparator_13_eq));  // open: gt, lt
  Comparator #(.width(6)) comparator_14 (.a(PRE_PC[31:26]), .b(6'b000010), .eq(comparator_14_eq));  // open: gt, lt
  Comparator #(.width(6)) comparator_15 (.a(PRE_PC[31:26]), .b(6'b000011), .eq(comparator_15_eq));  // open: gt, lt
  Comparator #(.width(6)) comparator_16 (.a(PRE_PC[31:26]), .b(6'b000100), .eq(comparator_16_eq));  // open: gt, lt
  Comparator #(.width(6)) comparator_17 (.a(PRE_PC[31:26]), .b(6'b000101), .eq(comparator_17_eq));  // open: gt, lt
  Comparator #(.width(6)) comparator_18 (.a(PRE_PC[31:26]), .b(6'b000001), .eq(comparator_18_eq));  // open: gt, lt
  Comparator #(.width(32)) comparator_19 (.a(PRE_PC), .b(Pre_PC0), .eq(comparator_19_eq));  // open: gt, lt
  Comparator #(.width(32)) comparator_20 (.a(PRE_PC), .b(Pre_PC1), .eq(comparator_20_eq));  // open: gt, lt
  Comparator #(.width(32)) comparator_21 (.a(PRE_PC), .b(Pre_PC2), .eq(comparator_21_eq));  // open: gt, lt
  Comparator #(.width(32)) comparator_22 (.a(PRE_PC), .b(Pre_PC3), .eq(comparator_22_eq));  // open: gt, lt
  Multiplexer #(.width(32), .enable("false")) multiplexer_5 (
    .in0({32{1'b0}}), .in1(Branch_Addr0), .out(multiplexer_5_out), .sel(PRE_BRANCH0));
  Multiplexer #(.width(2), .enable("false")) multiplexer_6 (
    .in0(2'b00), .in1(B_State0), .out(multiplexer_6_out), .sel(PRE_BRANCH0));
  and and_1 (and_1_out, comparator_5_eq, comparator_6_eq);
  Multiplexer #(.width(32), .enable("false")) multiplexer_7 (
    .in0(multiplexer_3_out), .in1(Branch_Addr2), .out(multiplexer_7_out), .sel(BRANCH2));
  and and_2 (and_2_out, comparator_12_eq, comparator_13_eq);
  Multiplexer #(.width(32), .enable("false")) multiplexer_8 (
    .in0(multiplexer_5_out), .in1(Branch_Addr1), .out(multiplexer_8_out), .sel(PRE_BRANCH1));
  Multiplexer #(.width(2), .enable("false")) multiplexer_9 (
    .in0(multiplexer_6_out), .in1(B_State1), .out(multiplexer_9_out), .sel(PRE_BRANCH1));
  Multiplexer #(.width(2), .enable("false")) multiplexer_10 (
    .in0(multiplexer_4_out), .in1(B_State2), .out(multiplexer_10_out), .sel(BRANCH2));
  Multiplexer #(.width(32), .enable("false")) multiplexer_11 (
    .in0(multiplexer_8_out), .in1(Branch_Addr2), .out(multiplexer_11_out), .sel(PRE_BRANCH2));
  or or_1 (or_1_out, and_1_out, comparator_7_eq, comparator_8_eq, comparator_9_eq, comparator_10_eq, comparator_11_eq);
  // Probe on BRANCH_ADDRESS
  Multiplexer #(.width(32), .enable("false")) multiplexer_12 (
    .in0(multiplexer_7_out), .in1(Branch_Addr3), .out(BRANCH_ADDRESS), .sel(BRANCH3));
  Multiplexer #(.width(2), .enable("false")) multiplexer_13 (
    .in0(multiplexer_10_out), .in1(B_State3), .out({TAKE_BRANCH, multiplexer_13_out[0]}), .sel(BRANCH3));
  or or_2 (or_2_out, and_2_out, comparator_14_eq, comparator_15_eq, comparator_16_eq, comparator_17_eq, comparator_18_eq);
  Multiplexer #(.width(2), .enable("false")) multiplexer_14 (
    .in0(multiplexer_9_out), .in1(B_State2), .out(multiplexer_14_out), .sel(PRE_BRANCH2));
  or or_3 (EXIST, BRANCH0, BRANCH1, BRANCH2, BRANCH3);
  and and_3 (BRANCH0, or_1_out, comparator_1_eq, V0);
  and and_4 (BRANCH1, or_1_out, comparator_2_eq, V1);
  and and_5 (BRANCH2, or_1_out, comparator_3_eq, V2);
  and and_6 (BRANCH3, or_1_out, comparator_4_eq, V3);
  Multiplexer #(.width(32), .enable("false")) multiplexer_15 (
    .in0(multiplexer_11_out), .in1(Branch_Addr3), .out(multiplexer_15_out), .sel(PRE_BRANCH3));
  Multiplexer #(.width(2), .enable("false")) multiplexer_16 (
    .in0(multiplexer_14_out), .in1(B_State3), .out({PRE_TAKE_BRANCH, multiplexer_16_out[0]}),
    .sel(PRE_BRANCH3));
  or or_4 (or_4_out, PRE_BRANCH0, PRE_BRANCH1, PRE_BRANCH2, PRE_BRANCH3);
  and and_7 (PRE_BRANCH0, comparator_19_eq, V0);
  and and_8 (PRE_BRANCH1, comparator_20_eq, V1);
  and and_9 (PRE_BRANCH2, comparator_21_eq, V2);
  and and_10 (PRE_BRANCH3, comparator_22_eq, V3);
  Comparator #(.width(32)) comparator_23 (
    .a(multiplexer_15_out), .b(PRE_BRANCH_ADDR), .eq(comparator_23_eq));  // open: gt, lt
  and and_11 (Set, or_2_out, ~or_4_out);  // AND_Gate
  not not_1 (not_1_out, comparator_23_eq);
  and and_12 (HIT, comparator_23_eq, PRE_TAKE_BRANCH);
  and and_13 (MISS, or_4_out, not_1_out);
  Register #(.width(1)) register_1 (.D(1'b1), .en(Set0), .Q(V0), .clk(clk), .clr(rst));
  Register #(.width(1)) register_2 (.D(1'b1), .en(Set1), .Q(V1), .clk(clk), .clr(rst));
  Register #(.width(1)) register_3 (.D(1'b1), .en(Set2), .Q(V2), .clk(clk), .clr(rst));
  Register #(.width(1)) register_4 (.D(1'b1), .en(Set3), .Q(V3), .clk(clk), .clr(rst));
  Register #(.width(32)) register_5 (.D(PRE_PC), .en(Set0), .Q(Pre_PC0), .clk(clk), .clr(rst));
  Register #(.width(32)) register_6 (.D(PRE_PC), .en(Set1), .Q(Pre_PC1), .clk(clk), .clr(rst));
  Register #(.width(32)) register_7 (.D(PRE_PC), .en(Set2), .Q(Pre_PC2), .clk(clk), .clr(rst));
  Register #(.width(32)) register_8 (.D(PRE_PC), .en(Set3), .Q(Pre_PC3), .clk(clk), .clr(rst));
  Adder #(.width(16)) adder_1 (.a(LRU0), .b(16'h1), .out(adder_1_out), .cout(adder_1_cout));  // open: cin
  Adder #(.width(16)) adder_2 (.a(LRU1), .b(16'h1), .out(adder_2_out), .cout(adder_2_cout));  // open: cin
  Adder #(.width(16)) adder_3 (.a(LRU2), .b(16'h1), .out(adder_3_out), .cout(adder_3_cout));  // open: cin
  Adder #(.width(16)) adder_4 (.a(LRU3), .b(16'h1), .out(adder_4_out), .cout(adder_4_cout));  // open: cin
  or or_5 (or_5_out, Set0, Set1, Set2, Set3);
  Multiplexer #(.width(16), .enable("false")) multiplexer_17 (
    .in0(LRU0), .in1(adder_1_out), .out(New_LRU0), .sel(not_2_out));
  not not_2 (not_2_out, adder_1_cout);
  Multiplexer #(.width(16), .enable("false")) multiplexer_18 (
    .in0(LRU1), .in1(adder_2_out), .out(New_LRU1), .sel(not_3_out));
  not not_3 (not_3_out, adder_2_cout);
  Multiplexer #(.width(16), .enable("false")) multiplexer_19 (
    .in0(LRU2), .in1(adder_3_out), .out(New_LRU2), .sel(not_4_out));
  not not_4 (not_4_out, adder_3_cout);
  Multiplexer #(.width(16), .enable("false")) multiplexer_20 (
    .in0(LRU3), .in1(adder_4_out), .out(New_LRU3), .sel(not_5_out));
  not not_5 (not_5_out, adder_4_cout);
  or or_6 (or_6_out, HIT, MISS);
  Register #(.width(32)) register_9 (.D(PRE_BRANCH_ADDR), .en(Set0), .Q(Branch_Addr0), .clk(clk), .clr(rst));
  Register #(.width(32)) register_10 (.D(PRE_BRANCH_ADDR), .en(Set1), .Q(Branch_Addr1), .clk(clk), .clr(rst));
  Register #(.width(32)) register_11 (.D(PRE_BRANCH_ADDR), .en(Set2), .Q(Branch_Addr2), .clk(clk), .clr(rst));
  Register #(.width(32)) register_12 (.D(PRE_BRANCH_ADDR), .en(Set3), .Q(Branch_Addr3), .clk(clk), .clr(rst));
  and and_14 (Use_State0, PRE_BRANCH0, or_6_out);
  and and_15 (Use_State1, PRE_BRANCH1, or_6_out);
  and and_16 (Use_State2, PRE_BRANCH2, or_6_out);
  and and_17 (Use_State3, PRE_BRANCH3, or_6_out);
  and and_18 (clr_LRU0, PRE_BRANCH0, HIT);
  and and_19 (clr_LRU1, PRE_BRANCH1, HIT);
  and and_20 (clr_LRU2, PRE_BRANCH2, HIT);
  and and_21 (clr_LRU3, PRE_BRANCH3, HIT);
  or or_7 (or_7_out, clr_LRU3, clr_LRU2, clr_LRU1, clr_LRU0);
  and and_22 (and_22_out, ~clr_LRU0, or_7_out);  // AND_Gate
  and and_23 (and_23_out, ~clr_LRU1, or_7_out);  // AND_Gate
  and and_24 (and_24_out, ~clr_LRU2, or_7_out);  // AND_Gate
  and and_25 (and_25_out, ~clr_LRU3, or_7_out);  // AND_Gate
  and and_26 (and_26_out, ~Set0, or_5_out);  // AND_Gate
  and and_27 (and_27_out, ~Set1, or_5_out);  // AND_Gate
  and and_28 (and_28_out, ~Set2, or_5_out);  // AND_Gate
  and and_29 (and_29_out, ~Set3, or_5_out);  // AND_Gate
  or or_8 (or_8_out, Set0, Use_State0);
  or or_9 (or_9_out, Set1, Use_State1);
  or or_10 (or_10_out, Set2, Use_State2);
  or or_11 (or_11_out, Set3, Use_State3);
  or or_12 (Fix_LRU0, and_22_out, and_26_out);
  or or_13 (Fix_LRU1, and_23_out, and_27_out);
  or or_14 (Fix_LRU2, and_24_out, and_28_out);
  or or_15 (Fix_LRU3, and_25_out, and_29_out);
  Multiplexer #(.width(2), .enable("false")) multiplexer_21 (
    .in0(New_B_State0), .in1(2'b10), .out(multiplexer_21_out), .sel(Set0));
  Multiplexer #(.width(2), .enable("false")) multiplexer_22 (
    .in0(New_B_State1), .in1(2'b10), .out(multiplexer_22_out), .sel(Set1));
  Multiplexer #(.width(2), .enable("false")) multiplexer_23 (
    .in0(New_B_State2), .in1(2'b10), .out(multiplexer_23_out), .sel(Set2));
  Multiplexer #(.width(2), .enable("false")) multiplexer_24 (
    .in0(New_B_State3), .in1(2'b10), .out(multiplexer_24_out), .sel(Set3));
  Register #(.width(2)) register_13 (.D(multiplexer_21_out), .en(or_8_out), .Q(B_State0), .clk(clk), .clr(rst));
  Register #(.width(2)) register_14 (.D(multiplexer_22_out), .en(or_9_out), .Q(B_State1), .clk(clk), .clr(rst));
  Register #(.width(2)) register_15 (.D(multiplexer_23_out), .en(or_10_out), .Q(B_State2), .clk(clk), .clr(rst));
  Register #(.width(2)) register_16 (.D(multiplexer_24_out), .en(or_11_out), .Q(B_State3), .clk(clk), .clr(rst));
  or or_16 (or_16_out, Set0, Fix_LRU0);
  or or_17 (or_17_out, Set1, Fix_LRU1);
  or or_18 (or_18_out, Set2, Fix_LRU2);
  or or_19 (or_19_out, Set3, Fix_LRU3);
  Multiplexer #(.width(16), .enable("false")) multiplexer_25 (
    .in0(New_LRU0), .in1({16{1'b0}}), .out(multiplexer_25_out), .sel(Set0));
  Multiplexer #(.width(16), .enable("false")) multiplexer_26 (
    .in0(New_LRU1), .in1({16{1'b0}}), .out(multiplexer_26_out), .sel(Set1));
  Multiplexer #(.width(16), .enable("false")) multiplexer_27 (
    .in0(New_LRU2), .in1({16{1'b0}}), .out(multiplexer_27_out), .sel(Set2));
  Multiplexer #(.width(16), .enable("false")) multiplexer_28 (
    .in0(New_LRU3), .in1({16{1'b0}}), .out(multiplexer_28_out), .sel(Set3));
  not not_6 (not_6_out, V0);
  not not_7 (not_7_out, V1);
  not not_8 (not_8_out, V2);
  not not_9 (not_9_out, V3);
  MAX2 max2_1 (.Y(LRU0), .X(LRU1), .Y_num(2'b00), .X_num(2'b01), .MAX(max2_1_max), .Max_num(max2_1_max_num));
  MAX2 max2_2 (.Y(LRU2), .X(LRU3), .Y_num(2'b10), .X_num(2'b11), .MAX(max2_2_max), .Max_num(max2_2_max_num));
  Register #(.width(16)) register_17 (.D(multiplexer_25_out), .en(or_16_out), .Q(LRU0), .clk(clk), .clr(or_20_out));
  or or_20 (or_20_out, rst, clr_LRU0);
  Register #(.width(16)) register_18 (.D(multiplexer_26_out), .en(or_17_out), .Q(LRU1), .clk(clk), .clr(or_21_out));
  or or_21 (or_21_out, rst, clr_LRU1);
  Register #(.width(16)) register_19 (.D(multiplexer_27_out), .en(or_18_out), .Q(LRU2), .clk(clk), .clr(or_22_out));
  or or_22 (or_22_out, rst, clr_LRU2);
  Register #(.width(16)) register_20 (.D(multiplexer_28_out), .en(or_19_out), .Q(LRU3), .clk(clk), .clr(or_23_out));
  or or_23 (or_23_out, rst, clr_LRU3);
  MAX2 max2_3 (
    .Y(max2_1_max), .X(max2_2_max), .Y_num(max2_1_max_num), .X_num(max2_2_max_num), .Max_num(max2_3_max_num));  // open: MAX
  and and_30 (and_30_out, V0, V1, V2, V3);
  Priority_Encoder #(.select(2)) priority_encoder_1 (
    .in0(not_6_out), .in1(not_7_out), .in2(not_8_out), .in3(not_9_out), .out(priority_encoder_1_out));  // open: gs, en_out, en_in
  Multiplexer #(.width(2), .enable("false")) multiplexer_29 (
    .in0(priority_encoder_1_out), .in1(max2_3_max_num), .out(multiplexer_29_out), .sel(and_30_out));
  Decoder #(.select(2), .enable("false")) decoder_1 (
    .out0(decoder_1_out0), .out1(decoder_1_out1), .out2(decoder_1_out2), .out3(decoder_1_out3),
    .sel(multiplexer_29_out));
  Adder #(.width(2)) adder_5 (.a(B_State0), .b(2'b01), .out(adder_5_out), .cout(adder_5_cout));  // open: cin
  Adder #(.width(2)) adder_6 (.a(B_State1), .b(2'b01), .out(adder_6_out), .cout(adder_6_cout));  // open: cin
  Adder #(.width(2)) adder_7 (.a(B_State2), .b(2'b01), .out(adder_7_out), .cout(adder_7_cout));  // open: cin
  Adder #(.width(2)) adder_8 (.a(B_State3), .b(2'b01), .out(adder_8_out), .cout(adder_8_cout));  // open: cin
  and and_31 (Set0, decoder_1_out0, Set);
  and and_32 (Set1, decoder_1_out1, Set);
  and and_33 (Set2, decoder_1_out2, Set);
  and and_34 (Set3, decoder_1_out3, Set);
  Multiplexer #(.width(2), .enable("false")) multiplexer_30 (
    .in0(B_State0), .in1(adder_5_out), .out(multiplexer_30_out), .sel(and_35_out));
  and and_35 (and_35_out, ~adder_5_cout, HIT);  // AND_Gate
  Multiplexer #(.width(2), .enable("false")) multiplexer_31 (
    .in0(B_State1), .in1(adder_6_out), .out(multiplexer_31_out), .sel(and_36_out));
  and and_36 (and_36_out, ~adder_6_cout, HIT);  // AND_Gate
  Multiplexer #(.width(2), .enable("false")) multiplexer_32 (
    .in0(B_State2), .in1(adder_7_out), .out(multiplexer_32_out), .sel(and_37_out));
  and and_37 (and_37_out, ~adder_7_cout, HIT);  // AND_Gate
  Multiplexer #(.width(2), .enable("false")) multiplexer_33 (
    .in0(B_State3), .in1(adder_8_out), .out(multiplexer_33_out), .sel(and_38_out));
  and and_38 (and_38_out, ~adder_8_cout, HIT);  // AND_Gate
  Subtractor #(.width(2)) subtractor_1 (
    .a(multiplexer_30_out), .b(2'b01), .out(subtractor_1_out), .bout(subtractor_1_bout));  // open: bin
  Subtractor #(.width(2)) subtractor_2 (
    .a(multiplexer_31_out), .b(2'b01), .out(subtractor_2_out), .bout(subtractor_2_bout));  // open: bin
  Subtractor #(.width(2)) subtractor_3 (
    .a(multiplexer_32_out), .b(2'b01), .out(subtractor_3_out), .bout(subtractor_3_bout));  // open: bin
  Subtractor #(.width(2)) subtractor_4 (
    .a(multiplexer_33_out), .b(2'b01), .out(subtractor_4_out), .bout(subtractor_4_bout));  // open: bin
  Multiplexer #(.width(2), .enable("false")) multiplexer_34 (
    .in0(multiplexer_30_out), .in1(subtractor_1_out), .out(New_B_State0), .sel(and_39_out));
  and and_39 (and_39_out, ~subtractor_1_bout, MISS);  // AND_Gate
  Multiplexer #(.width(2), .enable("false")) multiplexer_35 (
    .in0(multiplexer_31_out), .in1(subtractor_2_out), .out(New_B_State1), .sel(and_40_out));
  and and_40 (and_40_out, ~subtractor_2_bout, MISS);  // AND_Gate
  Multiplexer #(.width(2), .enable("false")) multiplexer_36 (
    .in0(multiplexer_32_out), .in1(subtractor_3_out), .out(New_B_State2), .sel(and_41_out));
  and and_41 (and_41_out, ~subtractor_3_bout, MISS);  // AND_Gate
  Multiplexer #(.width(2), .enable("false")) multiplexer_37 (
    .in0(multiplexer_33_out), .in1(subtractor_4_out), .out(New_B_State3), .sel(and_42_out));
  and and_42 (and_42_out, ~subtractor_4_bout, MISS);  // AND_Gate

  // Other names for the same wires on the sheet: Branch_Addr[31:0] = PRE_BRANCH_ADDR; Funct[5:0] = PC[5:0];
  //   OP_Code[5:0] = PC[31:26]; PRE_Funct[5:0] = PRE_PC[5:0]; PRE_OP_Code[5:0] = PRE_PC[31:26]

  // Notes on the sheet:
  //   OP
  //   指令字
  //   指令字
  //   Func
  //   OP
  //   Func
  //   VALID
  //   VALID
  //   VALID
  //   VALID
  //   淘汰标志位
  //   淘汰标志位
  //   淘汰标志位
  //   淘汰标志位
endmodule

module MAX2 (
  input  [15:0] Y,
  input  [15:0] X,
  input  [1:0] Y_num,
  input  [1:0] X_num,
  output [15:0] MAX,
  output [1:0] Max_num
);

  wire comparator_1_eq, comparator_1_gt, or_1_out;

  Multiplexer #(.width(16), .enable("false")) multiplexer_1 (.in0(Y), .in1(X), .out(MAX), .sel(or_1_out));
  Comparator #(.width(16), .mode("unsigned")) comparator_1 (
    .a(X), .b(Y), .gt(comparator_1_gt), .eq(comparator_1_eq));  // open: lt
  or or_1 (or_1_out, comparator_1_gt, comparator_1_eq);
  Multiplexer #(.width(2), .enable("false")) multiplexer_2 (.in0(Y_num), .in1(X_num), .out(Max_num), .sel(or_1_out));

  // Notes on the sheet:
  //   输出两个输入中的较大值，并输出较大值的3位编号
endmodule

module \中断识别与响应  (
  input  clk,
  input  [31:0] IE_in,
  input  IR1,
  input  mtc0,
  input  IR2,
  input  [31:0] oldPC,
  input  [4:0] Rd,
  input  IR3,
  input  [31:0] muxPC,
  input  eret,
  output W1,
  output [31:0] IE_out,
  output W2,
  output [31:0] EPC,
  output W3,
  output [31:0] nowPC
);

  wire _1, _2, _3, and_2_out, and_3_out, and_4_out, and_5_out, and_6_out, and_7_out, and_11_out, and_12_out,
       and_13_out, and_14_out, comparator_1_eq, comparator_2_eq, comparator_3_eq, comparator_5_eq, d_ff_1_q,
       d_ff_2_q, d_ff_3_q, IE, interrupt, multiplexer_1_out, nand_1_out, not_1_out, not_2_out, or_4_out,
       or_5_out, or_6_out, or_7_out, or_8_out, or_9_out, or_10_out, or_11_out, or_12_out, register_1_q,
       register_2_q, register_3_q, RST1, RST2, RST3, wait_interr;
  wire [1:0] and_15_out, bit_extender_1_out, interr_num, priority_encoder_1_out, priority_encoder_2_out;
  wire [31:0] multiplexer_2_out, multiplexer_3_out;

  LED u__1 (.in(_1));
  or or_1 (_1, W1, d_ff_1_q);
  or or_2 (_2, W2, d_ff_2_q);
  LED u__2 (.in(_2));
  or or_3 (_3, W3, d_ff_3_q);
  LED u__3 (.in(_3));
  or or_4 (or_4_out, W1, W2, W3);
  Comparator #(.width(2)) comparator_1 (.a(interr_num), .b(2'b11), .eq(comparator_1_eq));  // open: gt, lt
  Comparator #(.width(2)) comparator_2 (.a(interr_num), .b(2'b10), .eq(comparator_2_eq));  // open: gt, lt
  Comparator #(.width(2)) comparator_3 (.a(interr_num), .b(2'b01), .eq(comparator_3_eq));  // open: gt, lt
  D_Flip_Flop d_ff_1 (.clk(IR1), .D(1'b1), .Q(d_ff_1_q), .reset(W1));  // open: Qn, preset, en
  D_Flip_Flop d_ff_2 (.clk(IR2), .D(1'b1), .Q(d_ff_2_q), .reset(W2));  // open: Qn, preset, en
  D_Flip_Flop d_ff_3 (.clk(IR3), .D(1'b1), .Q(d_ff_3_q), .reset(W3));  // open: Qn, preset, en
  and and_1 (wait_interr, IE, or_4_out);
  not not_1 (not_1_out, comparator_1_eq);
  not not_2 (not_2_out, comparator_2_eq);
  and and_2 (and_2_out, eret, comparator_3_eq);
  and and_3 (and_3_out, eret, comparator_2_eq);
  and and_4 (and_4_out, eret, comparator_1_eq);
  or or_5 (or_5_out, d_ff_1_q, W1);
  or or_6 (or_6_out, d_ff_2_q, W2);
  or or_7 (or_7_out, d_ff_3_q, W3);
  or or_8 (or_8_out, W1, and_2_out);
  or or_9 (or_9_out, W2, and_3_out);
  or or_10 (or_10_out, W3, and_4_out);
  and and_5 (and_5_out, or_5_out, ~RST1);  // AND_Gate
  and and_6 (and_6_out, or_6_out, ~RST2);  // AND_Gate
  and and_7 (and_7_out, or_7_out, ~RST3);  // AND_Gate
  nand nand_1 (nand_1_out, wait_interr, eret);
  Multiplexer #(.enable("false")) multiplexer_1 (.in0(1'b1), .in1(1'b0), .out(multiplexer_1_out), .sel(eret));
  D_Flip_Flop u_IR1 (.clk(clk), .D(and_5_out), .Q(W1));  // open: Qn, preset, en, reset
  D_Flip_Flop u_IR2 (.clk(clk), .D(and_6_out), .Q(W2));  // open: Qn, preset, en, reset
  D_Flip_Flop u_IR3 (.clk(clk), .D(and_7_out), .Q(W3));  // open: Qn, preset, en, reset
  Register #(.width(1), .trigger("falling")) register_1 (
    .D(multiplexer_1_out), .en(or_8_out), .Q(register_1_q), .clk(clk));  // open: clr
  Register #(.width(1), .trigger("falling")) register_2 (
    .D(multiplexer_1_out), .en(or_9_out), .Q(register_2_q), .clk(clk));  // open: clr
  Register #(.width(1), .trigger("falling")) register_3 (
    .D(multiplexer_1_out), .en(or_10_out), .Q(register_3_q), .clk(clk));  // open: clr
  and and_8 (RST3, wait_interr, nand_1_out, comparator_1_eq);
  and and_9 (RST2, wait_interr, nand_1_out, comparator_2_eq, not_1_out);
  and and_10 (RST1, wait_interr, nand_1_out, comparator_3_eq, not_1_out, not_2_out);
  Priority_Encoder #(.select(2)) priority_encoder_1 (
    .in0(1'b1), .in1(register_1_q), .in2(register_2_q), .in3(register_3_q), .out(priority_encoder_1_out));  // open: gs, en_out, en_in
  and and_11 (and_11_out, IE, or_11_out);
  or or_11 (or_11_out, register_3_q, register_2_q, register_1_q);
  and and_12 (and_12_out, and_11_out, interrupt);
  Register #(.width(2)) register_4 (
    .D(priority_encoder_1_out), .en(or_12_out), .Q(interr_num), .clk(clk));  // open: clr
  or or_12 (or_12_out, eret, and_12_out);
  Comparator #(.width(2), .mode("unsigned")) comparator_4 (
    .a(priority_encoder_1_out), .b(interr_num), .gt(interrupt));  // open: eq, lt
  Comparator #(.width(5)) comparator_5 (.a(Rd), .b(5'b00001), .eq(comparator_5_eq));  // open: gt, lt
  Priority_Encoder #(.select(2)) priority_encoder_2 (
    .in0(1'b1), .in1(W1), .in2(W2), .in3(W3), .out(priority_encoder_2_out));  // open: gs, en_out, en_in
  and and_13 (and_13_out, wait_interr, interrupt);
  Multiplexer #(.width(32), .enable("false")) multiplexer_2 (
    .in0(IE_in), .in1({32{1'b0}}), .out(multiplexer_2_out), .sel(eret));
  Register #(.width(32), .trigger("falling")) register_5 (
    .D(multiplexer_2_out), .en(mtc0), .Q(IE_out), .clk(clk));  // open: clr
  Multiplexer #(.width(32), .enable("false")) multiplexer_3 (
    .in0(muxPC), .in1(oldPC), .out(multiplexer_3_out), .sel(and_14_out));
  and and_14 (and_14_out, comparator_5_eq, mtc0);
  assign bit_extender_1_out = {{1{and_13_out}}, and_13_out};  // Bit_Extender bit_extender_1
  Register #(.width(32)) register_6 (.D(multiplexer_3_out), .Q(EPC), .clk(clk));  // open: en, clr
  assign and_15_out = priority_encoder_2_out & bit_extender_1_out;  // AND_Gate and_15, 2 bits wide
  not not_3 (IE, IE_out[0]);
  Multiplexer #(.select(2), .width(32), .enable("false")) multiplexer_4 (
    .in0(muxPC), .in1(32'h3474), .in2(32'h3578), .in3(32'h367c), .out(nowPC), .sel(and_15_out));

  // Notes on the sheet:
  //   Reset 
  //   Reset 
  //   Reset 
endmodule

module \多级中断  (
);

  wire and_1_out, and_2_out, and_3_out, and_4_out, and_5_out, CLK, comparator_1_eq, comparator_2_eq, Eret,
       Go, IR1, IR2, IR3, Mfc0, mips_alu_1_equal, Mtc0, not_1_out, not_2_out, or_1_out, or_2_out, or_3_out,
       or_4_out, or_5_out, or_6_out, RST, SignedExt, W1, W2, W3, \硬布线控制器_1_alu_src , \硬布线控制器_1_beq ,
       \硬布线控制器_1_bltz , \硬布线控制器_1_bne , \硬布线控制器_1_jal , \硬布线控制器_1_jmp , \硬布线控制器_1_jr , \硬布线控制器_1_lb ,
       \硬布线控制器_1_memtoreg , \硬布线控制器_1_memwrite , \硬布线控制器_1_regdst , \硬布线控制器_1_regwrite , \硬布线控制器_1_sllv ,
       \硬布线控制器_1_syscall ;
  wire [3:0] \硬布线控制器_1_alu_op ;
  wire [4:0] multiplexer_6_out, multiplexer_9_out, multiplexer_11_out, multiplexer_16_out, R1_1, R1_in, rd,
       rs, rt;
  wire [5:0] FUNC, OP;
  wire [7:0] multiplexer_19_out;
  wire [12:8] rom_1_data;
  wire [15:0] \总周期数 , \无条件分支数 , \条件分支成功数 ;
  wire [31:0] adder_1_out, adder_2_out, bit_extender_1_out, bit_extender_2_out, bit_extender_3_out, CP0,
       LedData, mips_alu_1_result, mips_regifile_1_r1, mips_regifile_1_r2, multiplexer_1_out,
       multiplexer_2_out, multiplexer_3_out, multiplexer_5_out, multiplexer_7_out, multiplexer_10_out,
       multiplexer_12_out, multiplexer_13_out, multiplexer_14_out, multiplexer_15_out, multiplexer_18_out,
       PC, ram_1_data, shifter_1_out, \中断识别与响应_1_epc , \中断识别与响应_1_ie_out , \中断识别与响应_1_nowpc ;

  Button \u_总复位  (.out(RST));
  Button u_Go (.out(Go));
  Clock clock_1 (.out(CLK));
  Multiplexer #(.width(32), .enable("false")) multiplexer_1 (
    .in0(adder_1_out), .in1(adder_2_out), .out(multiplexer_1_out), .sel(or_6_out));
  or or_1 (or_1_out, \硬布线控制器_1_jmp , \硬布线控制器_1_jal );
  Multiplexer #(.width(32), .enable("false")) multiplexer_2 (
    .in0(multiplexer_1_out), .in1(mips_regifile_1_r1), .out(multiplexer_2_out), .sel(\硬布线控制器_1_jr ));
  Multiplexer #(.width(32), .enable("false")) multiplexer_3 (
    .in0(multiplexer_2_out), .in1({PC[31:28], rs, rt, rd, rom_1_data, FUNC, 2'b00}), .out(multiplexer_3_out),
    .sel(or_1_out));
  Hex_Digit_Display hex_digit_display_1 (.value(LedData[27:24]));  // open: dp
  Hex_Digit_Display hex_digit_display_2 (.value(LedData[31:28]));  // open: dp
  \中断识别与响应  \u_中断识别与响应_1  (
    .W1(W1), .clk(CLK), .IE_in(mips_regifile_1_r2), .IE_out(\中断识别与响应_1_ie_out ), .IR1(IR1), .mtc0(Mtc0),
    .W2(W2), .IR2(IR2), .EPC(\中断识别与响应_1_epc ), .oldPC(mips_regifile_1_r2), .Rd(rd), .W3(W3), .IR3(IR3),
    .muxPC(multiplexer_3_out), .nowPC(\中断识别与响应_1_nowpc ), .eret(Eret));
  Hex_Digit_Display hex_digit_display_3 (.value(LedData[23:20]));  // open: dp
  Hex_Digit_Display hex_digit_display_4 (.value(LedData[19:16]));  // open: dp
  Multiplexer #(.width(32), .enable("false")) multiplexer_4 (
    .in0(\中断识别与响应_1_ie_out ), .in1(\中断识别与响应_1_epc ), .out(CP0), .sel(rd[0]));
  Hex_Digit_Display hex_digit_display_5 (.value(LedData[15:12]));  // open: dp
  Hex_Digit_Display hex_digit_display_6 (.value(LedData[11:8]));  // open: dp
  Hex_Digit_Display hex_digit_display_7 (.value(LedData[3:0]));  // open: dp
  Hex_Digit_Display hex_digit_display_8 (.value(LedData[7:4]));  // open: dp
  or or_2 (or_2_out, or_3_out, not_1_out);
  Multiplexer #(.width(32), .enable("false")) multiplexer_5 (
    .in0(\中断识别与响应_1_nowpc ), .in1(\中断识别与响应_1_epc ), .out(multiplexer_5_out), .sel(Eret));
  not not_1 (not_1_out, \硬布线控制器_1_syscall );
  or or_3 (or_3_out, and_1_out, Go);
  Counter #(.width(16), .max('hffff)) counter_1 (
    .count(or_2_out), .Q(\总周期数 ), .clk(CLK), .clr(RST));  // open: load, D, carry
  Register #(.width(32)) u_PC (.D(multiplexer_5_out), .en(or_2_out), .Q(PC), .clk(CLK), .clr(RST));
  Adder #(.width(32)) adder_1 (.a(PC), .b(32'h4), .out(adder_1_out));  // open: cin, cout
  Button _1 (.out(IR1));
  Button _2 (.out(IR2));
  Button _3 (.out(IR3));
  and and_1 (and_1_out, \硬布线控制器_1_syscall , comparator_1_eq);
  Comparator #(.width(32)) comparator_1 (.a(32'h22), .b(mips_regifile_1_r1), .eq(comparator_1_eq));  // open: gt, lt
  LED led_1 (.in(W1));
  LED led_2 (.in(W2));
  LED led_3 (.in(W3));
  ROM #(.addrWidth(10), .dataWidth(32)) rom_1 (
    .addr(PC[11:2]), .data({OP, rs, rt, rd, rom_1_data, FUNC}));  // open: sel
  \硬布线控制器  \u_硬布线控制器_1  (
    .OP(OP), .Func(FUNC), .ALU_OP(\硬布线控制器_1_alu_op ), .MemToReg(\硬布线控制器_1_memtoreg ),
    .MemWrite(\硬布线控制器_1_memwrite ), .ALU_SRC(\硬布线控制器_1_alu_src ), .RegWrite(\硬布线控制器_1_regwrite ),
    .SysCALL(\硬布线控制器_1_syscall ), .SignedExt(SignedExt), .RegDst(\硬布线控制器_1_regdst ), .Beq(\硬布线控制器_1_beq ),
    .Bne(\硬布线控制器_1_bne ), .JR(\硬布线控制器_1_jr ), .JMP(\硬布线控制器_1_jmp ), .JAL(\硬布线控制器_1_jal ),
    .SLLV(\硬布线控制器_1_sllv ), .LB(\硬布线控制器_1_lb ), .BLTZ(\硬布线控制器_1_bltz ), .MFC0(Mfc0), .MTC0(Mtc0),
    .ERET(Eret), .RS(rs));
  Multiplexer #(.width(5), .enable("false")) multiplexer_6 (
    .in0(rt), .in1(rd), .out(multiplexer_6_out), .sel(\硬布线控制器_1_regdst ));
  Multiplexer #(.width(32), .enable("false")) multiplexer_7 (
    .in0(multiplexer_18_out), .in1(adder_1_out), .out(multiplexer_7_out), .sel(\硬布线控制器_1_jal ));
  Multiplexer #(.width(5), .enable("false")) multiplexer_8 (
    .in0(rs), .in1(5'b00010), .out(R1_1), .sel(\硬布线控制器_1_syscall ));
  Multiplexer #(.width(5), .enable("false")) multiplexer_9 (
    .in0(multiplexer_6_out), .in1({5{1'b1}}), .out(multiplexer_9_out), .sel(\硬布线控制器_1_jal ));
  Multiplexer #(.width(32), .enable("false")) multiplexer_10 (
    .in0(multiplexer_7_out), .in1(bit_extender_3_out), .out(multiplexer_10_out), .sel(\硬布线控制器_1_lb ));
  assign bit_extender_1_out = {{16{1'b0}}, {rd, rom_1_data, FUNC}};  // Bit_Extender bit_extender_1
  assign bit_extender_2_out = {{16{rd[4]}}, {rd, rom_1_data, FUNC}};  // Bit_Extender bit_extender_2
  // Probe on \总周期数 
  // Probe on \无条件分支数 
  // Probe on \条件分支成功数 
  Counter #(.width(16), .max('hffff)) counter_2 (
    .count(or_4_out), .Q(\无条件分支数 ), .clk(CLK), .clr(RST));  // open: load, D, carry
  or or_4 (or_4_out, \硬布线控制器_1_jmp , \硬布线控制器_1_jr , \硬布线控制器_1_jal );
  or or_5 (or_5_out, \硬布线控制器_1_regwrite , Mfc0);
  and and_2 (and_2_out, \硬布线控制器_1_syscall , comparator_1_eq);
  Multiplexer #(.width(5), .enable("false")) multiplexer_11 (
    .in0(rt), .in1(5'b00100), .out(multiplexer_11_out), .sel(\硬布线控制器_1_syscall ));
  Multiplexer #(.width(32), .enable("false")) multiplexer_12 (
    .in0(multiplexer_10_out), .in1(CP0), .out(multiplexer_12_out), .sel(Mfc0));
  Multiplexer #(.width(32), .enable("false")) multiplexer_13 (
    .in0(bit_extender_1_out), .in1(bit_extender_2_out), .out(multiplexer_13_out), .sel(SignedExt));
  MIPS_Regifile mips_regifile_1 (
    .Din(multiplexer_12_out), .Clk(CLK), .R1(mips_regifile_1_r1), .R2(mips_regifile_1_r2), .WE(or_5_out),
    .W_num(multiplexer_9_out), .R1_num(R1_in), .R2_num(multiplexer_11_out));
  Multiplexer #(.width(32), .enable("false")) multiplexer_14 (
    .in0(mips_regifile_1_r2), .in1(multiplexer_13_out), .out(multiplexer_14_out), .sel(\硬布线控制器_1_alu_src ));
  Shifter #(.width(32)) shifter_1 (.in(bit_extender_2_out), .\dist (5'b00010), .out(shifter_1_out));
  Multiplexer #(.width(32), .enable("false")) multiplexer_15 (
    .in0(multiplexer_14_out), .in1({32{1'b0}}), .out(multiplexer_15_out), .sel(\硬布线控制器_1_bltz ));
  Multiplexer #(.width(5), .enable("false")) multiplexer_16 (
    .in0(rom_1_data), .in1(mips_regifile_1_r1[4:0]), .out(multiplexer_16_out), .sel(\硬布线控制器_1_sllv ));
  Multiplexer #(.width(5), .enable("false")) multiplexer_17 (.in0(R1_1), .in1(rt), .out(R1_in), .sel(Mtc0));
  Adder #(.width(32)) adder_2 (.a(shifter_1_out), .b(adder_1_out), .out(adder_2_out));  // open: cin, cout
  MIPS_ALU mips_alu_1 (
    .X(mips_regifile_1_r1), .Y(multiplexer_15_out), .AluOP(\硬布线控制器_1_alu_op ), .Equal(mips_alu_1_equal),
    .Result(mips_alu_1_result), .shamt(multiplexer_16_out));  // open: Result_2
  // Probe on mips_regifile_1_r2
  and and_3 (and_3_out, \硬布线控制器_1_beq , mips_alu_1_equal);
  and and_4 (and_4_out, \硬布线控制器_1_bne , not_2_out);
  not not_2 (not_2_out, mips_alu_1_equal);
  Comparator #(.width(32)) comparator_2 (.a(mips_alu_1_result), .b(32'h1), .eq(comparator_2_eq));  // open: gt, lt
  and and_5 (and_5_out, comparator_2_eq, \硬布线控制器_1_bltz );
  RAM #(.addrWidth(10), .dataWidth(32), .bus("separate")) ram_1 (
    .addr(mips_alu_1_result[11:2]), .din(mips_regifile_1_r2), .data(ram_1_data), .str(\硬布线控制器_1_memwrite ),
    .clk(CLK), .clr(RST));  // open: sel, ld
  or or_6 (or_6_out, and_3_out, and_5_out, and_4_out);
  Counter #(.width(16), .max('hffff)) counter_3 (
    .count(or_6_out), .Q(\条件分支成功数 ), .clk(CLK), .clr(RST));  // open: load, D, carry
  Multiplexer #(.width(32)) multiplexer_18 (
    .in0(mips_alu_1_result), .in1(ram_1_data), .out(multiplexer_18_out), .sel(\硬布线控制器_1_memtoreg ));  // open: en
  // Probe on mips_regifile_1_r2
  Register #(.width(32), .trigger("high")) register_1 (
    .D(mips_regifile_1_r2), .en(and_2_out), .Q(LedData), .clk(CLK), .clr(RST));
  Multiplexer #(.select(2), .width(8), .enable("false")) multiplexer_19 (
    .in0(multiplexer_18_out[7:0]), .in1(multiplexer_18_out[15:8]), .in2(multiplexer_18_out[23:16]),
    .in3(multiplexer_18_out[31:24]), .out(multiplexer_19_out), .sel(mips_alu_1_result[1:0]));
  assign bit_extender_3_out = {{24{multiplexer_19_out[7]}}, multiplexer_19_out};  // Bit_Extender bit_extender_3

  // Notes on the sheet:
  //   数码管输出应该用寄存器锁存，否则显示数据只能一闪而过
  //   可以通过项目增加Logisim库的方式将前几次实验完成的电路作为子电路引入到本电路中使用
  //   数码管输出
  //   中断源
  //   指令存储器
  //   中断等待指示
  //   总复位信号应将除ROM以外所有存储组件全部清零
  //   contents of rom_1 (hex, n*v repeats v):
  //   241c0320 241d0190 20110001 8000c07 20110001 20120002 20130003 8000c0b 20110001 20120002 20130003
  //   8000c0f 20110001 20120002 20130003 8000c13 20110001 20120002 20130003 c000cfa 20100001 20110001
  //   118fc0 112020 20020022 c 118882 12200001 8000c17 112020 20020022 c 20110001 118880 112020 20020022 c
  //   12200001 8000c21 20110001 118fc0 112020 20020022 c 1188c3 112020 20020022 c 118903 112020 20020022 c
  //   118903 112020 20020022 c 118903 112020 20020022 c 118903 112020 20020022 c 118903 112020 20020022 c
  //   118903 112020 20020022 c 118903 112020 20020022 c 20100001 109fc0 139fc3 8021 2012000c 24160003
  //   26100001 3210000f 20080008 20090001 139900 2709825 132020 20020022 c 1094022 1500fff9 22100001
  //   2018000f 2188024 108700 20080008 20090001 139902 2709825 132021 20020022 c 1094022 1500fff9 108702
  //   2c9b022 12c00001 8000c52 4020 1084027 84400 3508ffff 82021 20020022 c 2010ffff 20110000 ae300000
  //   22100001 22310004 ae300000 22100001 22310004 ae300000 22100001 22310004 ae300000 22100001 22310004
  //   ae300000 22100001 22310004 ae300000 22100001 22310004 ae300000 22100001 22310004 ae300000 22100001
  //   22310004 ae300000 22100001 22310004 ae300000 22100001 22310004 ae300000 22100001 22310004 ae300000
  //   22100001 22310004 ae300000 22100001 22310004 ae300000 22100001 22310004 ae300000 22100001 22310004
  //   ae300000 22100001 22310004 22100001 8020 2011003c 8e130000 8e340000 274402a 11000002 ae330000
  //   ae140000 2231fffc 1611fff8 102020 20020022 c 22100004 2011003c 1611fff2 20020032 c 20080001 20090003
  //   20110876 112020 20020022 c 200b0008 1118804 131880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
  //   Op
  //   Func
  //   Beq
  //   Bne
  //   MemToReg
  //   MemWrite
  //   AluOP
  //   AluSrcB
  //   RegWrite
  //   RegDst
endmodule
